// Logisim project NC16.circ as structural Verilog: 13 circuits, main circuit main
module main (
);

  wire and_1_out, clock_1_out, CONTINUE_out, d_ff_1_q, dipswitch_1_sw1, in_switcher_1_strobe_out,
       int_controller_1_int, keyboard_1_avail, multiplexer_1_out, nc16_main_1_buffer_full_int,
       nc16_main_1_hlt, nc16_main_1_intret, nc16_main_1_out_st, or_1_out, or_2_out, OS_RESTART_out,
       out_switcher_1_out_38, out_switcher_1_out_39, out_switcher_1_out_40, out_switcher_1_out_41,
       out_switcher_1_strobe_out_0, RESET_out, rom_controller_1_write_probe, rom_controller_2_write_probe,
       rom_controller_3_write_probe, rom_controller_4_write_probe;
  wire [4:0] int_controller_1_out_intnum;
  wire [6:0] bit_extender_1_out, keyboard_1_data;
  wire [15:0] bit_extender_2_out, bit_extender_3_out, in_switcher_1_data_out, nc16_main_1_cpu_status,
       nc16_main_1_in_addr, nc16_main_1_out_addr, nc16_main_1_out_ext, OS_ROM_data,
       out_switcher_1_data_out_0, out_switcher_1_out_5, out_switcher_1_out_6, out_switcher_1_out_7,
       out_switcher_1_out_8, out_switcher_1_out_9, random_1_out, ROM_1_data, ROM_2_data, ROM_3_data,
       rom_controller_1_output_memaddr, rom_controller_2_output_memaddr, rom_controller_3_output_memaddr,
       rom_controller_4_output_memaddr, undriven;

  Clock clock_1 (.out(clock_1_out));
  or or_1 (or_1_out, CONTINUE_out, dipswitch_1_sw1);
  DipSwitch #(.number(1)) dipswitch_1 (.sw1(dipswitch_1_sw1));
  Multiplexer multiplexer_1 (.in0(nc16_main_1_hlt), .in1(1'b1), .out(multiplexer_1_out), .sel(or_1_out));
  and and_1 (and_1_out, clock_1_out, multiplexer_1_out);
  D_Flip_Flop d_ff_1 (.D(out_switcher_1_strobe_out_0), .clk(and_1_out), .Q(d_ff_1_q));  // open: Qn, preset, reset
  Button RESET (.out(RESET_out));
  Button OS_RESTART (.out(OS_RESTART_out));
  Button CONTINUE (.out(CONTINUE_out));
  Random #(.width(16)) random_1 (.next(1'b1), .clk(and_1_out), .out(random_1_out));  // open: clr
  TTY #(.cols(120), .rows(48)) tty_1 (.data(bit_extender_1_out), .clk(and_1_out), .we(d_ff_1_q), .clr(RESET_out));
  Keyboard keyboard_1 (.clr(or_2_out), .avail(keyboard_1_avail), .data(keyboard_1_data));  // open: clk, re
  or or_2 (or_2_out, nc16_main_1_intret, RESET_out);
  Bit_Extender #(.in_width(16), .out_width(7), .\type ("zero")) bit_extender_1 (
    .in(out_switcher_1_data_out_0), .out(bit_extender_1_out));
  assign bit_extender_2_out = {{9{1'b0}}, keyboard_1_data};  // Bit_Extender bit_extender_2
  in_switcher in_switcher_1 (
    .in_0(bit_extender_2_out), .in_2(undriven), .in_3(OS_ROM_data), .in_4(ROM_1_data), .in_5(ROM_2_data),
    .in_6(ROM_3_data), .in_7(random_1_out), .in_strobe_0(keyboard_1_avail),
    .in_35(rom_controller_1_write_probe), .in_36(rom_controller_2_write_probe),
    .in_37(rom_controller_3_write_probe), .in_38(rom_controller_4_write_probe), .in_39(1'b1),
    .addr_in(nc16_main_1_in_addr), .data_out(in_switcher_1_data_out), .strobe_out(in_switcher_1_strobe_out));  // open: in_8, in_9, in_10, in_11, in_12, in_13, in_14, in_15, in_16, in_17, in_18, in_19, in_20, in_21, in_22, in_23, in_24, in_25, in_26, in_27, in_28, in_29, in_30, in_31, in_31_2, in_34, in_40, in_41, in_42, in_43, in_44, in_45, in_46, in_47, in_48, in_49, in_50, in_51, in_52, in_53, in_54, in_55, in_56, in_57, in_58, in_59, in_60, in_61, in_62, in_63, in_strobe_31
  rom_controller rom_controller_1 (
    .data_in(out_switcher_1_out_6), .input_strobe(out_switcher_1_out_38), .RESET(RESET_out), .CLK(and_1_out),
    .output_memaddr(rom_controller_1_output_memaddr), .write_probe(rom_controller_1_write_probe));
  ROM #(.addrWidth(16), .dataWidth(16)) OS_ROM (.addr(rom_controller_1_output_memaddr), .data(OS_ROM_data));
  assign bit_extender_3_out = {{11{1'b0}}, int_controller_1_out_intnum};  // Bit_Extender bit_extender_3
  int_controller int_controller_1 (
    .in_2(keyboard_1_avail), .in_3(nc16_main_1_buffer_full_int), .CLOCK(and_1_out), .RESET(RESET_out),
    .out_intnum(int_controller_1_out_intnum), .INT(int_controller_1_int));  // open: int_0, in_4, in_5, in_6, in_7, in_8, in_9, in_10, in_11, in_12, in_13, in_14, in_15, in_16, in_17, in_18, in_19, in_20, in_21, in_22, in_23, in_24, in_25, in_26, in_27, in_28, in_29, in_30, in_31, int_31
  NC16_main nc16_main_1 (
    .INT_NUM(bit_extender_3_out), .INT(int_controller_1_int), .in_ext(in_switcher_1_data_out),
    .CLK(and_1_out), .RESET(RESET_out), .input_st(in_switcher_1_strobe_out), .OS_RESTART(OS_RESTART_out),
    .out_ext(nc16_main_1_out_ext), .intret(nc16_main_1_intret), .out_st(nc16_main_1_out_st),
    .out_addr(nc16_main_1_out_addr), .in_addr(nc16_main_1_in_addr),
    .buffer_full_int(nc16_main_1_buffer_full_int), .cpu_status(nc16_main_1_cpu_status), .HLT(nc16_main_1_hlt));
  LedBar #(.matrixcols(16)) ledbar_1 (
    .led0(nc16_main_1_cpu_status[15]), .led1(nc16_main_1_cpu_status[14]), .led2(nc16_main_1_cpu_status[13]),
    .led3(nc16_main_1_cpu_status[12]), .led4(nc16_main_1_cpu_status[11]), .led5(nc16_main_1_cpu_status[10]),
    .led6(nc16_main_1_cpu_status[9]), .led7(nc16_main_1_cpu_status[8]), .led8(nc16_main_1_cpu_status[7]),
    .led9(nc16_main_1_cpu_status[6]), .led10(nc16_main_1_cpu_status[5]), .led11(nc16_main_1_cpu_status[4]),
    .led12(nc16_main_1_cpu_status[3]), .led13(nc16_main_1_cpu_status[2]), .led14(nc16_main_1_cpu_status[1]),
    .led15(nc16_main_1_cpu_status[0]));
  Clock clock_2 ();  // open: out
  rom_controller rom_controller_2 (
    .data_in(out_switcher_1_out_7), .input_strobe(out_switcher_1_out_39), .RESET(RESET_out), .CLK(and_1_out),
    .output_memaddr(rom_controller_2_output_memaddr), .write_probe(rom_controller_2_write_probe));
  out_switcher out_switcher_1 (
    .data_in(nc16_main_1_out_ext), .strobe_in(nc16_main_1_out_st), .addr_in(nc16_main_1_out_addr),
    .data_out_0(out_switcher_1_data_out_0), .out_5(out_switcher_1_out_5), .out_6(out_switcher_1_out_6),
    .out_7(out_switcher_1_out_7), .out_8(out_switcher_1_out_8), .out_9(out_switcher_1_out_9),
    .strobe_out_0(out_switcher_1_strobe_out_0), .out_38(out_switcher_1_out_38),
    .out_39(out_switcher_1_out_39), .out_40(out_switcher_1_out_40), .out_41(out_switcher_1_out_41));  // open: out_10, out_11, out_12, out_13, out_14, out_15, out_16, out_17, out_18, out_19, out_20, out_21, out_22, out_23, out_24, out_25, out_26, out_27, out_28, out_29, out_30, out_31, out_32, out_33, out_34, data_out_31, out_37, out_42, out_43, out_44, out_45, out_46, out_47, out_48, out_49, out_50, out_51, out_52, out_53, out_54, out_55, out_56, out_57, out_58, out_59, out_60, out_61, out_62, out_63, out_64, out_65, out_66, strobe_out_31
  ROM #(.addrWidth(16), .dataWidth(16)) ROM_1 (.addr(rom_controller_2_output_memaddr), .data(ROM_1_data));
  LedBar #(.matrixcols(16)) ledbar_2 (
    .led0(out_switcher_1_out_5[15]), .led1(out_switcher_1_out_5[14]), .led2(out_switcher_1_out_5[13]),
    .led3(out_switcher_1_out_5[12]), .led4(out_switcher_1_out_5[11]), .led5(out_switcher_1_out_5[10]),
    .led6(out_switcher_1_out_5[9]), .led7(out_switcher_1_out_5[8]), .led8(out_switcher_1_out_5[7]),
    .led9(out_switcher_1_out_5[6]), .led10(out_switcher_1_out_5[5]), .led11(out_switcher_1_out_5[4]),
    .led12(out_switcher_1_out_5[3]), .led13(out_switcher_1_out_5[2]), .led14(out_switcher_1_out_5[1]),
    .led15(out_switcher_1_out_5[0]));
  rom_controller rom_controller_3 (
    .data_in(out_switcher_1_out_8), .input_strobe(out_switcher_1_out_40), .RESET(RESET_out), .CLK(and_1_out),
    .output_memaddr(rom_controller_3_output_memaddr), .write_probe(rom_controller_3_write_probe));
  ROM #(.addrWidth(16), .dataWidth(16)) ROM_2 (.addr(rom_controller_3_output_memaddr), .data(ROM_2_data));
  rom_controller rom_controller_4 (
    .data_in(out_switcher_1_out_9), .input_strobe(out_switcher_1_out_41), .RESET(RESET_out), .CLK(and_1_out),
    .output_memaddr(rom_controller_4_output_memaddr), .write_probe(rom_controller_4_write_probe));
  ROM #(.addrWidth(16), .dataWidth(16)) ROM_3 (.addr(rom_controller_4_output_memaddr), .data(ROM_3_data));

  // Notes on the sheet:
  //   KEYBOARD(To use,click this!)
  //   contents of OS_ROM (hex, n*v repeats v):
  //   ff21 8f2a 6cc 11ff 6a7 a48 656c 6c6f 2c20 4d6f 6d6f 4f53 2057 6f72 6c64 2021 a52 6561 6479 2066 6f72
  //   2063 6f6d 6d61 6e64 2e0a 0 6571 7561 6c6c 2100 6e6f 7420 6571 7561 6c6c 2100 5468 6520 6669 6c65
  //   2079 6f75 2061 7265 2074 7279 696e 6720 746f 206c 6f61 6420 6973 206e 6f74 2061 2070 726f 6772 616d
  //   2e0a 0 4c6f 6164 2063 6f6d 706c 6574 652e a00 4d6f 6d6f 4f53 3e00 5468 6520 6669 6c65 2073 697a 6520
  //   6973 2074 6f6f 206c 6172 6765 2e0a 265*0 6865 6c70 0 6c6f 6164 2072 6f6d 3100 6c6f 6164 2072 6f6d
  //   3200 6c6f 6164 2072 6f6d 3300 7275 6e00 636f 6d6d 616e 6420 6e6f 7420 666f 756e 642e a00 8*0 85f 1
  //   124f 7 18ff 6a3 26ff 0 4f 67d 8a4 0 849 0 15ff 0 bf a 16f 1 8a6 0 8aa 0 114f 0 85f 0 2aff 0 85f 1
  //   2aff 0 80f 0 81f 502 15ff 0 bf a 16f 1 8a6 0 8aa 0 11ff 905 8af 0 8bf 8fb 8aa 5002 8bf 95f 8aa 5001
  //   8bf 685 8aa 51ff 80f 67d 8a0 0 8bf 83b 8aa 0 8bf 861 8aa 1 8bf 8b5 8aa 2 8bf 8ff 8aa 3 8bf a31 8aa 4
  //   8bf ac0 8aa 5 8bf b78 8aa 6 8bf bbe 8aa 7 8af 5121 8bf 685 8aa 0 8af 65e 8bf 0 8aa 0 80f 0 81f 544
  //   15ff 0 bf a 16f 1 8a6 0 8aa 0 11ff 905 80f 55b 15ff 0 bf a 16f 1 8a6 0 8aa 0 11ff 83f 80f 55b 81f
  //   65f 15ff 0 bf a 16f 1 8a6 0 8aa 0 11ff 869 122f 1 16ff 779 80f 55b 81f 662 15ff 0 bf a 16f 1 8a6 0
  //   8aa 0 11ff 869 122f 1 16ff 78b 80f 55b 81f 667 15ff 0 bf a 16f 1 8a6 0 8aa 0 11ff 869 122f 1 16ff
  //   793 80f 55b 81f 66c 15ff 0 bf a 16f 1 8a6 0 8aa 0 11ff 869 122f 1 16ff 79b 80f 55b 81f 671 15ff 0 bf
  //   a 16f 1 8a6 0 8aa 0 11ff 869 122f 1 16ff 7a3 11ff 7a7 80f 0 81f 65f 15ff 0 bf a 16f 1 8a6 0 8aa 0
  //   11ff 905 11ff 6f5 8af 55a 8bf 3 8aa 0 11ff 7b9 8af 55a 8bf 4 8aa 0 11ff 7b9 8af 55a 8bf 5 8aa 0 11ff
  //   7b9 28ff 5600 11ff 6f5 80f 0 81f 673 15ff 0 bf a 16f 1 8a6 0 8aa 0 11ff 905 11ff 6f5 8af 55a 809 0
  //   81f 0 82f 3 83f 65b 15ff 0 bf a 16f 1 8a6 0 8aa 0 11ff 8b9 81f 65b 8a1 0 809 0 120f ff02 17ff 827
  //   8a1 0 809 1 120f 2019 17ff 827 8a1 0 829 2 842 0 4f 5600 cff 815 124f fc00 19ff 815 8af 55a 809 0
  //   81f 3 83f 5600 15ff 0 bf a 16f 1 8a6 0 8aa 0 11ff 8b9 80f 0 81f 53c 15ff 0 bf a 16f 1 8a6 0 8aa 0
  //   11ff 905 11ff 6f5 80f 0 81f 548 15ff 0 bf a 16f 1 8a6 0 8aa 0 11ff 905 11ff 6f5 80f 0 81f 522 15ff 0
  //   bf a 16f 1 8a6 0 8aa 0 11ff 905 11ff 6f5 13ff 0 120f 5600 1aff 85d 8af 557 8b0 0 8aa 0 8af 65e 8bf 1
  //   8aa 0 8af 65e 859 0 125f 0 17ff 84b 81f 0 8a6 0 8b9 0 6f 1 11bf 0 81f 1 11ff 855 120f 5600 1aff 8ab
  //   121f 5600 1aff 8ab 8a0 0 839 0 8a1 0 849 0 853 0 35f ff00 125f 0 16ff 87f 1234 0 16ff 889 17ff 897
  //   854 0 35f ff00 125f 0 16ff 8a1 17ff 897 853 0 35f ff 125f 0 16ff 8a1 f 1 1f 1 11ff 869 82f 0 8a6 0
  //   8b9 0 6f 1 11bf 0 82f 1 8a6 0 8b9 0 6f 1 11bf 0 82f 2 8a6 0 8b9 0 6f 1 11bf 0 123f 5600 1aff 8f1
  //   21ff 0 232f 0 25ff 0 1d0f 0 1e0f 0 84f 0 1fff 0 a1f 0 a2f 0 26ff 0 124f 1 1aff 8cd 20ff 0 21ff 0 80f
  //   0 24ff 0 8a3 0 8aa 0 3f 1 f 1 22ff 0 1202 0 1aff 8d7 84f 0 8a6 0 8b9 0 6f 1 11bf 0 84f 1 8a6 0 8b9 0
  //   6f 1 11bf 0 84f 1 1cff 0 121f 5600 1aff 95b 80f 0 16f 1 8b2 0 8a6 0 8aa 0 16f 1 8b3 0 8a6 0 8aa 0
  //   16f 1 8b4 0 8a6 0 8aa 0 821 0 8a2 0 839 0 843 0 33f ff00 73f 8 123f 0 16ff 93f 1e0f 0 a3f 0 34f ff
  //   124f 0 16ff 93f 1e0f 0 a4f 0 2f 1 11ff 91f 82f 0 8a6 0 849 0 6f 1 8a6 0 839 0 6f 1 8a6 0 829 0 6f 1
  //   8a6 0 8b9 0 6f 1 11bf 0 82f 1 11ff 953 8af 65e 859 0 125f 1 17ff 9d5 16f 1 8b0 0 8a6 0 8aa 0 16f 1
  //   8b1 0 8a6 0 8aa 0 16f 1 8b2 0 8a6 0 8aa 0 16f 1 8b3 0 8a6 0 8aa 0 16f 1 8b4 0 8a6 0 8aa 0 1dff 0 91f
  //   0 121f a 16ff 9e9 121f 8 16ff 9d7 1eff 0 a1f 0 8af 557 829 0 8af 558 29 0 8a2 0 8b1 0 8aa 0 8af 558
  //   829 0 2f 1 8b2 0 8aa 0 8a6 0 849 0 6f 1 8a6 0 839 0 6f 1 8a6 0 829 0 6f 1 8a6 0 819 0 6f 1 8a6 0 809
  //   0 6f 1 1cff 0 8af 558 829 0 122f 0 16ff 9b7 a1f 0 12f 1 8b2 0 8aa 0 11ff 9b7 1eff 0 a1f 0 8af 557
  //   829 0 842 0 8af 558 29 0 8a2 0 8bf 0 8aa 0 14f 1 834 0 14f 1 804 0 842 0 f 2 3f 1 1204 0 18ff a23
  //   8a0 0 819 0 829 1 21f 100 32f ff 412 0 8b1 0 8a3 0 8aa 0 11ff a07 8af 558 8bf 0 8aa 0 8af 65e 8bf 0
  //   8aa 0 11ff 9b7 120f 5600 1aff ab5 16f 1 8b3 0 8a6 0 8aa 0 16f 1 8b4 0 8a6 0 8aa 0 16f 1 8b5 0 8a6 0
  //   8aa 0 81f 0 830 0 85f 0 8a3 0 849 0 824 0 32f ff00 72f 8 122f 0 16ff a8d 122f 30 1aff a95 122f 39
  //   18ff a95 12f 30 21f a 12 0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
  //   contents of ROM_1 (hex, n*v repeats v):
  //   ff02 2019 6e9 15ff 0 bf a 16f 1 8a6 0 8aa 0 11ff 5a64 29ff 0 16f 1 8b5 0 8a6 0 8aa 0 856 0 16f 3 80f
  //   0 8b0 0 805 0 10f 1 8a0 0 8aa 0 80f 0 8b0 0 805 0 10f 2 8a0 0 8aa 0 80f 0 8b0 0 805 0 10f 3 8a0 0
  //   8aa 0 805 0 10f 1 16f 1 8b0 0 8a6 0 8aa 0 80f 0 8b0 0 8a6 0 809 0 6f 1 8a0 0 8aa 0 80b 0 805 0 10f 1
  //   8a0 0 809 0 16f 1 8b0 0 8a6 0 8aa 0 805 0 f 3 8a0 0 809 0 16f 1 8b0 0 8a6 0 8aa 0 80f 1 810 0 8a6 0
  //   809 0 6f 1 101 0 810 0 8a6 0 809 0 6f 1 60f 8000 61f 8000 1201 0 1aff 569a 80f 0 11ff 569c 80f 1
  //   120f 0 16ff 58fa 805 0 10f 2 16f 1 8b0 0 8a6 0 8aa 0 80f 0 8b0 0 8a6 0 809 0 6f 1 8a0 0 8aa 0 80b 0
  //   805 0 10f 2 8a0 0 809 0 16f 1 8b0 0 8a6 0 8aa 0 805 0 f 3 8a0 0 809 0 16f 1 8b0 0 8a6 0 8aa 0 80f 1
  //   810 0 8a6 0 809 0 6f 1 101 0 810 0 8a6 0 809 0 6f 1 60f 8000 61f 8000 1201 0 1aff 56fc 80f 0 11ff
  //   56fe 80f 1 120f 0 16ff 58c2 805 0 f 2 8a0 0 809 0 16f 1 8b0 0 8a6 0 8aa 0 805 0 10f 2 8a0 0 809 0
  //   16f 1 8b0 0 8a6 0 8aa 0 80f 1 810 0 8a6 0 809 0 6f 1 1 0 810 0 8a6 0 809 0 6f 1 1 0 8a0 0 809 0 16f
  //   1 8b0 0 8a6 0 8aa 0 805 0 f 2 8a0 0 809 0 16f 1 8b0 0 8a6 0 8aa 0 805 0 10f 2 8a0 0 809 0 810 0 8a6
  //   0 809 0 6f 1 1 0 8a0 0 809 0 810 0 8a6 0 809 0 6f 1 60f 8000 61f 8000 1201 0 1aff 577e 80f 0 11ff
  //   5780 80f 1 120f 0 16ff 588a 805 0 10f 3 16f 1 8b0 0 8a6 0 8aa 0 805 0 f 2 8a0 0 809 0 16f 1 8b0 0
  //   8a6 0 8aa 0 805 0 10f 2 8a0 0 809 0 810 0 8a6 0 809 0 6f 1 1 0 8a0 0 809 0 8b0 0 8a6 0 809 0 6f 1
  //   8a0 0 8aa 0 80b 0 805 0 f 2 8a0 0 809 0 16f 1 8b0 0 8a6 0 8aa 0 805 0 10f 2 8a0 0 809 0 810 0 8a6 0
  //   809 0 6f 1 1 0 16f 1 8b0 0 8a6 0 8aa 0 805 0 f 2 8a0 0 809 0 16f 1 8b0 0 8a6 0 8aa 0 805 0 10f 2 8a0
  //   0 809 0 16f 1 8b0 0 8a6 0 8aa 0 80f 1 810 0 8a6 0 809 0 6f 1 1 0 810 0 8a6 0 809 0 6f 1 1 0 8a0 0
  //   809 0 8b0 0 8a6 0 809 0 6f 1 8a0 0 8aa 0 80b 0 805 0 f 2 8a0 0 809 0 16f 1 8b0 0 8a6 0 8aa 0 805 0
  //   10f 2 8a0 0 809 0 16f 1 8b0 0 8a6 0 8aa 0 80f 1 810 0 8a6 0 809 0 6f 1 1 0 810 0 8a6 0 809 0 6f 1 1
  //   0 16f 1 8b0 0 8a6 0 8aa 0 805 0 10f 3 8a0 0 809 0 8b0 0 8a6 0 809 0 6f 1 8a0 0 8aa 0 80b 0 805 0 10f
  //   2 16f 1 8b0 0 8a6 0 8aa 0 805 0 10f 2 8a0 0 809 0 16f 1 8b0 0 8a6 0 8aa 0 80f 1 810 0 8a6 0 809 0 6f
  //   1 1 0 8b0 0 8a6 0 809 0 6f 1 8a0 0 8aa 0 80b 0 11ff 56bc 805 0 10f 1 16f 1 8b0 0 8a6 0 8aa 0 805 0
  //   10f 1 8a0 0 809 0 16f 1 8b0 0 8a6 0 8aa 0 80f 1 810 0 8a6 0 809 0 6f 1 1 0 8b0 0 8a6 0 809 0 6f 1
  //   8a0 0 8aa 0 80b 0 11ff 565a 865 0 8a6 0 859 0 6f 1 8a6 0 8b9 0 6f 1 11bf 0 16f 1 8b5 0 8a6 0 8aa 0
  //   856 0 16f 11 80f 0 8b0 0 805 0 10f 11 8a0 0 8aa 0 805 0 10f 11 8a0 0 809 0 16f 1 8b0 0 8a6 0 8aa 0
  //   805 0 f 3 8a0 0 809 0 810 0 8a6 0 809 0 6f 1 60f 8000 61f 8000 1201 0 1aff 594e 80f 0 11ff 5950 80f
  //   1 120f 0 16ff 5a30 805 0 f 2 8a0 0 809 0 16f 1 8b0 0 8a6 0 8aa 0 805 0 10f 11 8a0 0 809 0 810 0 8a6
  //   0 809 0 6f 1 1 0 8a0 0 809 0 16f 1 8b0 0 8a6 0 8aa 0 805 0 10f 10 16f 1 8b0 0 8a6 0 8aa 0 8a6 0 819
  //   0 6f 1 8a6 0 809 0 6f 1 16f 1 8b5 0 8a6 0 8aa 0 84f 5 27ff 0 8a6 0 859 0 6f 1 802 0 805 0 10f 10 16f
  //   1 8b0 0 8a6 0 8aa 0 8a6 0 819 0 6f 1 16f 1 8b5 0 8a6 0 8aa 0 84f 3 27ff 0 8a6 0 859 0 6f 1 802 0 80f
  //   5cb2 16f 1 8b0 0 8a6 0 8aa 0 8a6 0 819 0 6f 1 16f 1 8b5 0 8a6 0 8aa 0 84f 3 27ff 0 8a6 0 859 0 6f 1
  //   802 0 805 0 10f 11 16f 1 8b0 0 8a6 0 8aa 0 805 0 10f 11 8a0 0 809 0 16f 1 8b0 0 8a6 0 8aa 0 80f 1
  //   810 0 8a6 0 809 0 6f 1 1 0 8b0 0 8a6 0 809 0 6f 1 8a0 0 8aa 0 80b 0 11ff 5922 80f 5cb3 16f 1 8b0 0
  //   8a6 0 8aa 0 8a6 0 819 0 6f 1 16f 1 8b5 0 8a6 0 8aa 0 84f 3 27ff 0 8a6 0 859 0 6f 1 802 0 865 0 8a6 0
  //   859 0 6f 1 8a6 0 8b9 0 6f 1 11bf 0 16f 1 8b5 0 8a6 0 8aa 0 856 0 16f 1a 80f 0 8b0 0 805 0 10f 19 8a0
  //   0 8aa 0 80f 5cb4 16f 1 8b0 0 8a6 0 8aa 0 8a6 0 819 0 6f 1 16f 1 8b5 0 8a6 0 8aa 0 84f 3 27ff 0 8a6 0
  //   859 0 6f 1 802 0 80f 5cbb 16f 1 8b0 0 8a6 0 8aa 0 8a6 0 819 0 6f 1 16f 1 8b5 0 8a6 0 8aa 0 84f 3
  //   27ff 0 8a6 0 859 0 6f 1 802 0 80f 0 8b0 0 805 0 10f 1a 8a0 0 8aa 0 805 0 10f 1a 8a0 0 809 0 16f 1
  //   8b0 0 8a6 0 8aa 0 80f 8 810 0 8a6 0 809 0 6f 1 60f 8000 61f 8000 1201 0 1aff 5af6 80f 0 11ff 5af8
  //   80f 1 120f 0 16ff 5bea 80f 5cd1 16f 1 8b0 0 8a6 0 8aa 0 8a6 0 819 0 6f 1 16f 1 8b5 0 8a6 0 8aa 0 84f
  //   3 27ff 0 8a6 0 859 0 6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
  //   contents of ROM_2 (hex, n*v repeats v):
  //   ff02 2019 a5ff 81f 560c 84f 3 27ff 0 86f fb00 13ff 0 29ff 0 5072 6f67 7261 6d20 5374 6172 7465 6421
  //   a00
endmodule

module NC16_main (
  input  [15:0] INT_NUM,
  input  INT,
  input  [15:0] in_ext,
  input  CLK,
  input  RESET,
  input  input_st,
  input  OS_RESTART,
  output [15:0] out_ext,
  output intret,
  output out_st,
  output [15:0] out_addr,
  output [15:0] in_addr,
  output buffer_full_int,
  output [15:0] cpu_status,
  output HLT
);

  wire alu_1_carry_flag, alu_1_sign_flag, alu_1_zero_flag, instruction_control_1_hlt, not_2_out, not_3_out,
       registers_1_exec_mode, registers_1_out_st;
  wire [15:0] alu_1_alu_out, demultiplexer_1_out0, demultiplexer_1_out1, instruction_control_1_mem_data_out,
       instruction_control_1_operand, instruction_control_1_output_status, instruction_control_1_pc_data_out,
       multiplexer_1_out, multiplexer_2_out, multiplexer_3_out, registers_1_a_out, registers_1_b_out,
       registers_1_bp_out, registers_1_buffer_out, registers_1_buffer_point_out, registers_1_buffer_size_out,
       registers_1_c_out, registers_1_d_out, registers_1_e_out, registers_1_flag_output,
       registers_1_input_out, registers_1_intnum_out, registers_1_memaddr_out, registers_1_memval_out,
       registers_1_sp_out;
  wire [20:0] instruction_control_1_cpu_control_bus;
  wire [31:0] decoder_1_out0;

  Decoder #(.select(5)) decoder_1 (
    .out0(decoder_1_out0[0]), .out1(decoder_1_out0[1]), .out2(decoder_1_out0[2]), .out3(decoder_1_out0[3]),
    .out4(decoder_1_out0[4]), .out5(decoder_1_out0[5]), .out6(decoder_1_out0[6]), .out7(decoder_1_out0[7]),
    .out8(decoder_1_out0[8]), .out9(decoder_1_out0[9]), .out10(decoder_1_out0[10]),
    .out11(decoder_1_out0[11]), .out12(decoder_1_out0[12]), .out13(decoder_1_out0[13]),
    .out14(decoder_1_out0[14]), .out15(decoder_1_out0[15]), .out16(decoder_1_out0[16]),
    .out17(decoder_1_out0[17]), .out18(decoder_1_out0[18]), .out19(decoder_1_out0[19]),
    .out20(decoder_1_out0[20]), .out21(decoder_1_out0[21]), .out22(decoder_1_out0[22]),
    .out23(decoder_1_out0[23]), .out24(decoder_1_out0[24]), .out25(decoder_1_out0[25]),
    .out26(decoder_1_out0[26]), .out27(decoder_1_out0[27]), .out28(decoder_1_out0[28]),
    .out29(decoder_1_out0[29]), .out30(decoder_1_out0[30]), .out31(decoder_1_out0[31]),
    .sel(instruction_control_1_cpu_control_bus[6:2]));  // open: en
  not not_1 (cpu_status[0], HLT);
  registers registers_1 (
    .reg_data_in(multiplexer_1_out), .CLK(CLK), .RESET(RESET), .write_reg_select(decoder_1_out0),
    .carry_flag(alu_1_carry_flag), .zero_flag(alu_1_zero_flag), .sign_flag(alu_1_sign_flag),
    .flag_write_sw(instruction_control_1_cpu_control_bus[20]), .INTNUM_input(INT_NUM), .INT(INT),
    .Input_data(in_ext), .Input_st(input_st), .OS_RESTART(OS_RESTART), .memval_out(registers_1_memval_out),
    .memaddr_out(registers_1_memaddr_out), .a_out(registers_1_a_out), .b_out(registers_1_b_out),
    .c_out(registers_1_c_out), .d_out(registers_1_d_out), .e_out(registers_1_e_out),
    .bp_out(registers_1_bp_out), .sp_out(registers_1_sp_out), .output_out(out_ext),
    .flag_output(registers_1_flag_output), .INTNUM_out(registers_1_intnum_out), .out_st(registers_1_out_st),
    .inaddr_out(in_addr), .outaddr_out(out_addr), .Input_out(registers_1_input_out),
    .buffer_out(registers_1_buffer_out), .buffer_point_out(registers_1_buffer_point_out),
    .buffer_size_out(registers_1_buffer_size_out), .buffer_full_int(buffer_full_int),
    .exec_mode(registers_1_exec_mode));  // open: out_35
  Instruction_Control instruction_control_1 (
    .mem_data_in(registers_1_memval_out), .mem_addr_in(registers_1_memaddr_out), .CLK(CLK),
    .pc_data_in(multiplexer_1_out), .pc_write_enable(decoder_1_out0[7]),
    .carry_flag(registers_1_flag_output[0]), .zero_flag(registers_1_flag_output[1]),
    .sign_flag(registers_1_flag_output[2]), .RESET(RESET), .INT(registers_1_flag_output[3]),
    .exec_mode(registers_1_exec_mode), .OS_RESTART(OS_RESTART), .sp_in(registers_1_sp_out),
    .mem_data_out(instruction_control_1_mem_data_out), .operand(instruction_control_1_operand),
    .pc_data_out(instruction_control_1_pc_data_out), .CPU_Control_BUS(instruction_control_1_cpu_control_bus),
    .intret(intret), .HLT(instruction_control_1_hlt),
    .output_status({instruction_control_1_output_status[15:5], cpu_status[4:1], instruction_control_1_output_status[0]}));
  not not_2 (not_2_out, instruction_control_1_hlt);
  and and_1 (HLT, not_2_out, not_3_out);
  not not_3 (not_3_out, instruction_control_1_cpu_control_bus[19]);
  Multiplexer #(.width(16)) multiplexer_1 (
    .in0(demultiplexer_1_out0), .in1(alu_1_alu_out), .out(multiplexer_1_out),
    .sel(instruction_control_1_cpu_control_bus[13]));
  Multiplexer #(.select(3), .width(16)) multiplexer_2 (
    .in0(registers_1_a_out), .in1(registers_1_b_out), .in2(registers_1_c_out), .in3(registers_1_d_out),
    .in4(registers_1_e_out), .in5(registers_1_bp_out), .in6(registers_1_sp_out),
    .in7(instruction_control_1_operand), .out(multiplexer_2_out),
    .sel(instruction_control_1_cpu_control_bus[12:10]));
  Multiplexer #(.select(5), .width(16)) multiplexer_3 (
    .in0(registers_1_a_out), .in1(registers_1_b_out), .in2(registers_1_c_out), .in3(registers_1_d_out),
    .in4(registers_1_e_out), .in5(registers_1_bp_out), .in6(registers_1_sp_out),
    .in7(instruction_control_1_operand), .in8(registers_1_input_out),
    .in9(instruction_control_1_mem_data_out), .in10(instruction_control_1_pc_data_out),
    .in11(registers_1_memval_out), .in12(registers_1_flag_output), .in13(registers_1_intnum_out),
    .in14(in_addr), .in15(out_addr), .in16(registers_1_buffer_out), .in17(registers_1_buffer_point_out),
    .in18(registers_1_buffer_size_out), .out(multiplexer_3_out),
    .sel(instruction_control_1_cpu_control_bus[18:14]));  // open: in19, in20, in21, in22, in23, in24, in25, in26, in27, in28, in29, in30, in31
  D_Flip_Flop d_ff_1 (.D(registers_1_out_st), .clk(CLK), .Q(out_st), .reset(RESET));  // open: Qn, preset
  Demultiplexer #(.width(16)) demultiplexer_1 (
    .out0(demultiplexer_1_out0), .out1(demultiplexer_1_out1), .in(multiplexer_3_out),
    .sel(instruction_control_1_cpu_control_bus[13]));
  ALU alu_1 (
    .in1_data_in(demultiplexer_1_out1), .in2_data_in(multiplexer_2_out),
    .ALU_function_select(instruction_control_1_cpu_control_bus[9:7]), .ALU_Out(alu_1_alu_out),
    .sign_flag(alu_1_sign_flag), .zero_flag(alu_1_zero_flag), .carry_flag(alu_1_carry_flag));

  assign cpu_status[15:5] = {11{1'b0}};
endmodule

module right_shifter (
  input  [15:0] Input_bus_1,
  input  [15:0] Input_bus_2,
  output carry_out,
  output [15:0] Output_bus_1
);

  wire and_1_out, and_2_out, and_3_out, and_4_out, and_5_out, and_6_out, and_7_out, and_8_out, and_9_out,
       and_10_out, and_11_out, and_12_out, and_13_out, and_14_out, and_15_out, or_1_out, or_2_out;
  wire [14:0] PLA_1_out;
  wire [15:0] multiplexer_1_out, multiplexer_17_out, multiplexer_33_out, multiplexer_49_out,
       multiplexer_65_out, multiplexer_81_out, multiplexer_97_out, multiplexer_113_out, multiplexer_129_out,
       multiplexer_145_out, multiplexer_161_out, multiplexer_177_out, multiplexer_193_out,
       multiplexer_225_out;

  PLA #(.in_width(16), .out_width(15), .\table ("0000000000000001 000000000000001 # 1\n0000000000000010 000000000000011 # 2\n0000000000000011 000000000000111 # 3\n0000000000000100 000000000001111 # 4\n0000000000000101 000000000011111 # 5\n0000000000000110 000000000111111 # 6\n0000000000000111 000000001111111 # 7\n0000000000001000 000000011111111 # 8\n0000000000001001 000000111111111 # 9\n0000000000001010 000001111111111 # 10\n0000000000001011 000011111111111 # 11\n0000000000001100 000111111111111 # 12\n0000000000001101 001111111111111 # 13\n0000000000001110 011111111111111 # 14\n0000000000001111 111111111111111 # 15")) PLA_1 (
    .in(Input_bus_1), .out(PLA_1_out));
  and and_1 (and_1_out, Input_bus_2[0], PLA_1_out[0]);
  Multiplexer multiplexer_1 (
    .in0(Input_bus_2[0]), .in1(Input_bus_2[1]), .out(multiplexer_1_out[0]), .sel(PLA_1_out[0]));
  Multiplexer multiplexer_2 (
    .in0(Input_bus_2[1]), .in1(Input_bus_2[2]), .out(multiplexer_1_out[1]), .sel(PLA_1_out[0]));
  Multiplexer multiplexer_3 (
    .in0(Input_bus_2[2]), .in1(Input_bus_2[3]), .out(multiplexer_1_out[2]), .sel(PLA_1_out[0]));
  Multiplexer multiplexer_4 (
    .in0(Input_bus_2[3]), .in1(Input_bus_2[4]), .out(multiplexer_1_out[3]), .sel(PLA_1_out[0]));
  Multiplexer multiplexer_5 (
    .in0(Input_bus_2[4]), .in1(Input_bus_2[5]), .out(multiplexer_1_out[4]), .sel(PLA_1_out[0]));
  Multiplexer multiplexer_6 (
    .in0(Input_bus_2[5]), .in1(Input_bus_2[6]), .out(multiplexer_1_out[5]), .sel(PLA_1_out[0]));
  Multiplexer multiplexer_7 (
    .in0(Input_bus_2[6]), .in1(Input_bus_2[7]), .out(multiplexer_1_out[6]), .sel(PLA_1_out[0]));
  Multiplexer multiplexer_8 (
    .in0(Input_bus_2[7]), .in1(Input_bus_2[8]), .out(multiplexer_1_out[7]), .sel(PLA_1_out[0]));
  Multiplexer multiplexer_9 (
    .in0(Input_bus_2[8]), .in1(Input_bus_2[9]), .out(multiplexer_1_out[8]), .sel(PLA_1_out[0]));
  Multiplexer multiplexer_10 (
    .in0(Input_bus_2[9]), .in1(Input_bus_2[10]), .out(multiplexer_1_out[9]), .sel(PLA_1_out[0]));
  Multiplexer multiplexer_11 (
    .in0(Input_bus_2[10]), .in1(Input_bus_2[11]), .out(multiplexer_1_out[10]), .sel(PLA_1_out[0]));
  Multiplexer multiplexer_12 (
    .in0(Input_bus_2[11]), .in1(Input_bus_2[12]), .out(multiplexer_1_out[11]), .sel(PLA_1_out[0]));
  Multiplexer multiplexer_13 (
    .in0(Input_bus_2[12]), .in1(Input_bus_2[13]), .out(multiplexer_1_out[12]), .sel(PLA_1_out[0]));
  Multiplexer multiplexer_14 (
    .in0(Input_bus_2[13]), .in1(Input_bus_2[14]), .out(multiplexer_1_out[13]), .sel(PLA_1_out[0]));
  Multiplexer multiplexer_15 (
    .in0(Input_bus_2[14]), .in1(Input_bus_2[15]), .out(multiplexer_1_out[14]), .sel(PLA_1_out[0]));
  Multiplexer multiplexer_16 (.in0(Input_bus_2[15]), .in1(1'b0), .out(multiplexer_1_out[15]), .sel(PLA_1_out[0]));
  and and_2 (and_2_out, multiplexer_225_out[0], PLA_1_out[8]);
  Multiplexer multiplexer_17 (
    .in0(multiplexer_225_out[0]), .in1(multiplexer_225_out[1]), .out(multiplexer_17_out[0]),
    .sel(PLA_1_out[8]));
  Multiplexer multiplexer_18 (
    .in0(multiplexer_225_out[1]), .in1(multiplexer_225_out[2]), .out(multiplexer_17_out[1]),
    .sel(PLA_1_out[8]));
  Multiplexer multiplexer_19 (
    .in0(multiplexer_225_out[2]), .in1(multiplexer_225_out[3]), .out(multiplexer_17_out[2]),
    .sel(PLA_1_out[8]));
  Multiplexer multiplexer_20 (
    .in0(multiplexer_225_out[3]), .in1(multiplexer_225_out[4]), .out(multiplexer_17_out[3]),
    .sel(PLA_1_out[8]));
  Multiplexer multiplexer_21 (
    .in0(multiplexer_225_out[4]), .in1(multiplexer_225_out[5]), .out(multiplexer_17_out[4]),
    .sel(PLA_1_out[8]));
  Multiplexer multiplexer_22 (
    .in0(multiplexer_225_out[5]), .in1(multiplexer_225_out[6]), .out(multiplexer_17_out[5]),
    .sel(PLA_1_out[8]));
  Multiplexer multiplexer_23 (
    .in0(multiplexer_225_out[6]), .in1(multiplexer_225_out[7]), .out(multiplexer_17_out[6]),
    .sel(PLA_1_out[8]));
  Multiplexer multiplexer_24 (
    .in0(multiplexer_225_out[7]), .in1(multiplexer_225_out[8]), .out(multiplexer_17_out[7]),
    .sel(PLA_1_out[8]));
  Multiplexer multiplexer_25 (
    .in0(multiplexer_225_out[8]), .in1(multiplexer_225_out[9]), .out(multiplexer_17_out[8]),
    .sel(PLA_1_out[8]));
  Multiplexer multiplexer_26 (
    .in0(multiplexer_225_out[9]), .in1(multiplexer_225_out[10]), .out(multiplexer_17_out[9]),
    .sel(PLA_1_out[8]));
  Multiplexer multiplexer_27 (
    .in0(multiplexer_225_out[10]), .in1(multiplexer_225_out[11]), .out(multiplexer_17_out[10]),
    .sel(PLA_1_out[8]));
  Multiplexer multiplexer_28 (
    .in0(multiplexer_225_out[11]), .in1(multiplexer_225_out[12]), .out(multiplexer_17_out[11]),
    .sel(PLA_1_out[8]));
  Multiplexer multiplexer_29 (
    .in0(multiplexer_225_out[12]), .in1(multiplexer_225_out[13]), .out(multiplexer_17_out[12]),
    .sel(PLA_1_out[8]));
  Multiplexer multiplexer_30 (
    .in0(multiplexer_225_out[13]), .in1(multiplexer_225_out[14]), .out(multiplexer_17_out[13]),
    .sel(PLA_1_out[8]));
  Multiplexer multiplexer_31 (
    .in0(multiplexer_225_out[14]), .in1(multiplexer_225_out[15]), .out(multiplexer_17_out[14]),
    .sel(PLA_1_out[8]));
  Multiplexer multiplexer_32 (
    .in0(multiplexer_225_out[15]), .in1(1'b0), .out(multiplexer_17_out[15]), .sel(PLA_1_out[8]));
  and and_3 (and_3_out, multiplexer_1_out[0], PLA_1_out[1]);
  and and_4 (and_4_out, multiplexer_17_out[0], PLA_1_out[9]);
  Multiplexer multiplexer_33 (
    .in0(multiplexer_1_out[0]), .in1(multiplexer_1_out[1]), .out(multiplexer_33_out[0]), .sel(PLA_1_out[1]));
  Multiplexer multiplexer_34 (
    .in0(multiplexer_1_out[1]), .in1(multiplexer_1_out[2]), .out(multiplexer_33_out[1]), .sel(PLA_1_out[1]));
  Multiplexer multiplexer_35 (
    .in0(multiplexer_1_out[2]), .in1(multiplexer_1_out[3]), .out(multiplexer_33_out[2]), .sel(PLA_1_out[1]));
  Multiplexer multiplexer_36 (
    .in0(multiplexer_1_out[3]), .in1(multiplexer_1_out[4]), .out(multiplexer_33_out[3]), .sel(PLA_1_out[1]));
  Multiplexer multiplexer_37 (
    .in0(multiplexer_1_out[4]), .in1(multiplexer_1_out[5]), .out(multiplexer_33_out[4]), .sel(PLA_1_out[1]));
  Multiplexer multiplexer_38 (
    .in0(multiplexer_1_out[5]), .in1(multiplexer_1_out[6]), .out(multiplexer_33_out[5]), .sel(PLA_1_out[1]));
  Multiplexer multiplexer_39 (
    .in0(multiplexer_1_out[6]), .in1(multiplexer_1_out[7]), .out(multiplexer_33_out[6]), .sel(PLA_1_out[1]));
  Multiplexer multiplexer_40 (
    .in0(multiplexer_1_out[7]), .in1(multiplexer_1_out[8]), .out(multiplexer_33_out[7]), .sel(PLA_1_out[1]));
  Multiplexer multiplexer_41 (
    .in0(multiplexer_1_out[8]), .in1(multiplexer_1_out[9]), .out(multiplexer_33_out[8]), .sel(PLA_1_out[1]));
  Multiplexer multiplexer_42 (
    .in0(multiplexer_1_out[9]), .in1(multiplexer_1_out[10]), .out(multiplexer_33_out[9]), .sel(PLA_1_out[1]));
  Multiplexer multiplexer_43 (
    .in0(multiplexer_1_out[10]), .in1(multiplexer_1_out[11]), .out(multiplexer_33_out[10]), .sel(PLA_1_out[1]));
  Multiplexer multiplexer_44 (
    .in0(multiplexer_1_out[11]), .in1(multiplexer_1_out[12]), .out(multiplexer_33_out[11]), .sel(PLA_1_out[1]));
  Multiplexer multiplexer_45 (
    .in0(multiplexer_1_out[12]), .in1(multiplexer_1_out[13]), .out(multiplexer_33_out[12]), .sel(PLA_1_out[1]));
  Multiplexer multiplexer_46 (
    .in0(multiplexer_1_out[13]), .in1(multiplexer_1_out[14]), .out(multiplexer_33_out[13]), .sel(PLA_1_out[1]));
  Multiplexer multiplexer_47 (
    .in0(multiplexer_1_out[14]), .in1(multiplexer_1_out[15]), .out(multiplexer_33_out[14]), .sel(PLA_1_out[1]));
  Multiplexer multiplexer_48 (
    .in0(multiplexer_1_out[15]), .in1(1'b0), .out(multiplexer_33_out[15]), .sel(PLA_1_out[1]));
  Multiplexer multiplexer_49 (
    .in0(multiplexer_17_out[0]), .in1(multiplexer_17_out[1]), .out(multiplexer_49_out[0]), .sel(PLA_1_out[9]));
  Multiplexer multiplexer_50 (
    .in0(multiplexer_17_out[1]), .in1(multiplexer_17_out[2]), .out(multiplexer_49_out[1]), .sel(PLA_1_out[9]));
  Multiplexer multiplexer_51 (
    .in0(multiplexer_17_out[2]), .in1(multiplexer_17_out[3]), .out(multiplexer_49_out[2]), .sel(PLA_1_out[9]));
  Multiplexer multiplexer_52 (
    .in0(multiplexer_17_out[3]), .in1(multiplexer_17_out[4]), .out(multiplexer_49_out[3]), .sel(PLA_1_out[9]));
  Multiplexer multiplexer_53 (
    .in0(multiplexer_17_out[4]), .in1(multiplexer_17_out[5]), .out(multiplexer_49_out[4]), .sel(PLA_1_out[9]));
  Multiplexer multiplexer_54 (
    .in0(multiplexer_17_out[5]), .in1(multiplexer_17_out[6]), .out(multiplexer_49_out[5]), .sel(PLA_1_out[9]));
  Multiplexer multiplexer_55 (
    .in0(multiplexer_17_out[6]), .in1(multiplexer_17_out[7]), .out(multiplexer_49_out[6]), .sel(PLA_1_out[9]));
  Multiplexer multiplexer_56 (
    .in0(multiplexer_17_out[7]), .in1(multiplexer_17_out[8]), .out(multiplexer_49_out[7]), .sel(PLA_1_out[9]));
  Multiplexer multiplexer_57 (
    .in0(multiplexer_17_out[8]), .in1(multiplexer_17_out[9]), .out(multiplexer_49_out[8]), .sel(PLA_1_out[9]));
  Multiplexer multiplexer_58 (
    .in0(multiplexer_17_out[9]), .in1(multiplexer_17_out[10]), .out(multiplexer_49_out[9]), .sel(PLA_1_out[9]));
  Multiplexer multiplexer_59 (
    .in0(multiplexer_17_out[10]), .in1(multiplexer_17_out[11]), .out(multiplexer_49_out[10]),
    .sel(PLA_1_out[9]));
  Multiplexer multiplexer_60 (
    .in0(multiplexer_17_out[11]), .in1(multiplexer_17_out[12]), .out(multiplexer_49_out[11]),
    .sel(PLA_1_out[9]));
  Multiplexer multiplexer_61 (
    .in0(multiplexer_17_out[12]), .in1(multiplexer_17_out[13]), .out(multiplexer_49_out[12]),
    .sel(PLA_1_out[9]));
  Multiplexer multiplexer_62 (
    .in0(multiplexer_17_out[13]), .in1(multiplexer_17_out[14]), .out(multiplexer_49_out[13]),
    .sel(PLA_1_out[9]));
  Multiplexer multiplexer_63 (
    .in0(multiplexer_17_out[14]), .in1(multiplexer_17_out[15]), .out(multiplexer_49_out[14]),
    .sel(PLA_1_out[9]));
  Multiplexer multiplexer_64 (
    .in0(multiplexer_17_out[15]), .in1(1'b0), .out(multiplexer_49_out[15]), .sel(PLA_1_out[9]));
  and and_5 (and_5_out, multiplexer_33_out[0], PLA_1_out[2]);
  Multiplexer multiplexer_65 (
    .in0(multiplexer_33_out[0]), .in1(multiplexer_33_out[1]), .out(multiplexer_65_out[0]), .sel(PLA_1_out[2]));
  Multiplexer multiplexer_66 (
    .in0(multiplexer_33_out[1]), .in1(multiplexer_33_out[2]), .out(multiplexer_65_out[1]), .sel(PLA_1_out[2]));
  Multiplexer multiplexer_67 (
    .in0(multiplexer_33_out[2]), .in1(multiplexer_33_out[3]), .out(multiplexer_65_out[2]), .sel(PLA_1_out[2]));
  Multiplexer multiplexer_68 (
    .in0(multiplexer_33_out[3]), .in1(multiplexer_33_out[4]), .out(multiplexer_65_out[3]), .sel(PLA_1_out[2]));
  Multiplexer multiplexer_69 (
    .in0(multiplexer_33_out[4]), .in1(multiplexer_33_out[5]), .out(multiplexer_65_out[4]), .sel(PLA_1_out[2]));
  Multiplexer multiplexer_70 (
    .in0(multiplexer_33_out[5]), .in1(multiplexer_33_out[6]), .out(multiplexer_65_out[5]), .sel(PLA_1_out[2]));
  Multiplexer multiplexer_71 (
    .in0(multiplexer_33_out[6]), .in1(multiplexer_33_out[7]), .out(multiplexer_65_out[6]), .sel(PLA_1_out[2]));
  Multiplexer multiplexer_72 (
    .in0(multiplexer_33_out[7]), .in1(multiplexer_33_out[8]), .out(multiplexer_65_out[7]), .sel(PLA_1_out[2]));
  Multiplexer multiplexer_73 (
    .in0(multiplexer_33_out[8]), .in1(multiplexer_33_out[9]), .out(multiplexer_65_out[8]), .sel(PLA_1_out[2]));
  Multiplexer multiplexer_74 (
    .in0(multiplexer_33_out[9]), .in1(multiplexer_33_out[10]), .out(multiplexer_65_out[9]), .sel(PLA_1_out[2]));
  Multiplexer multiplexer_75 (
    .in0(multiplexer_33_out[10]), .in1(multiplexer_33_out[11]), .out(multiplexer_65_out[10]),
    .sel(PLA_1_out[2]));
  Multiplexer multiplexer_76 (
    .in0(multiplexer_33_out[11]), .in1(multiplexer_33_out[12]), .out(multiplexer_65_out[11]),
    .sel(PLA_1_out[2]));
  Multiplexer multiplexer_77 (
    .in0(multiplexer_33_out[12]), .in1(multiplexer_33_out[13]), .out(multiplexer_65_out[12]),
    .sel(PLA_1_out[2]));
  Multiplexer multiplexer_78 (
    .in0(multiplexer_33_out[13]), .in1(multiplexer_33_out[14]), .out(multiplexer_65_out[13]),
    .sel(PLA_1_out[2]));
  Multiplexer multiplexer_79 (
    .in0(multiplexer_33_out[14]), .in1(multiplexer_33_out[15]), .out(multiplexer_65_out[14]),
    .sel(PLA_1_out[2]));
  Multiplexer multiplexer_80 (
    .in0(multiplexer_33_out[15]), .in1(1'b0), .out(multiplexer_65_out[15]), .sel(PLA_1_out[2]));
  and and_6 (and_6_out, multiplexer_49_out[0], PLA_1_out[10]);
  Multiplexer multiplexer_81 (
    .in0(multiplexer_49_out[0]), .in1(multiplexer_49_out[1]), .out(multiplexer_81_out[0]), .sel(PLA_1_out[10]));
  Multiplexer multiplexer_82 (
    .in0(multiplexer_49_out[1]), .in1(multiplexer_49_out[2]), .out(multiplexer_81_out[1]), .sel(PLA_1_out[10]));
  Multiplexer multiplexer_83 (
    .in0(multiplexer_49_out[2]), .in1(multiplexer_49_out[3]), .out(multiplexer_81_out[2]), .sel(PLA_1_out[10]));
  Multiplexer multiplexer_84 (
    .in0(multiplexer_49_out[3]), .in1(multiplexer_49_out[4]), .out(multiplexer_81_out[3]), .sel(PLA_1_out[10]));
  Multiplexer multiplexer_85 (
    .in0(multiplexer_49_out[4]), .in1(multiplexer_49_out[5]), .out(multiplexer_81_out[4]), .sel(PLA_1_out[10]));
  Multiplexer multiplexer_86 (
    .in0(multiplexer_49_out[5]), .in1(multiplexer_49_out[6]), .out(multiplexer_81_out[5]), .sel(PLA_1_out[10]));
  Multiplexer multiplexer_87 (
    .in0(multiplexer_49_out[6]), .in1(multiplexer_49_out[7]), .out(multiplexer_81_out[6]), .sel(PLA_1_out[10]));
  Multiplexer multiplexer_88 (
    .in0(multiplexer_49_out[7]), .in1(multiplexer_49_out[8]), .out(multiplexer_81_out[7]), .sel(PLA_1_out[10]));
  Multiplexer multiplexer_89 (
    .in0(multiplexer_49_out[8]), .in1(multiplexer_49_out[9]), .out(multiplexer_81_out[8]), .sel(PLA_1_out[10]));
  Multiplexer multiplexer_90 (
    .in0(multiplexer_49_out[9]), .in1(multiplexer_49_out[10]), .out(multiplexer_81_out[9]),
    .sel(PLA_1_out[10]));
  Multiplexer multiplexer_91 (
    .in0(multiplexer_49_out[10]), .in1(multiplexer_49_out[11]), .out(multiplexer_81_out[10]),
    .sel(PLA_1_out[10]));
  Multiplexer multiplexer_92 (
    .in0(multiplexer_49_out[11]), .in1(multiplexer_49_out[12]), .out(multiplexer_81_out[11]),
    .sel(PLA_1_out[10]));
  Multiplexer multiplexer_93 (
    .in0(multiplexer_49_out[12]), .in1(multiplexer_49_out[13]), .out(multiplexer_81_out[12]),
    .sel(PLA_1_out[10]));
  Multiplexer multiplexer_94 (
    .in0(multiplexer_49_out[13]), .in1(multiplexer_49_out[14]), .out(multiplexer_81_out[13]),
    .sel(PLA_1_out[10]));
  Multiplexer multiplexer_95 (
    .in0(multiplexer_49_out[14]), .in1(multiplexer_49_out[15]), .out(multiplexer_81_out[14]),
    .sel(PLA_1_out[10]));
  Multiplexer multiplexer_96 (
    .in0(multiplexer_49_out[15]), .in1(1'b0), .out(multiplexer_81_out[15]), .sel(PLA_1_out[10]));
  and and_7 (and_7_out, multiplexer_65_out[0], PLA_1_out[3]);
  Multiplexer multiplexer_97 (
    .in0(multiplexer_65_out[0]), .in1(multiplexer_65_out[1]), .out(multiplexer_97_out[0]), .sel(PLA_1_out[3]));
  Multiplexer multiplexer_98 (
    .in0(multiplexer_65_out[1]), .in1(multiplexer_65_out[2]), .out(multiplexer_97_out[1]), .sel(PLA_1_out[3]));
  Multiplexer multiplexer_99 (
    .in0(multiplexer_65_out[2]), .in1(multiplexer_65_out[3]), .out(multiplexer_97_out[2]), .sel(PLA_1_out[3]));
  Multiplexer multiplexer_100 (
    .in0(multiplexer_65_out[3]), .in1(multiplexer_65_out[4]), .out(multiplexer_97_out[3]), .sel(PLA_1_out[3]));
  Multiplexer multiplexer_101 (
    .in0(multiplexer_65_out[4]), .in1(multiplexer_65_out[5]), .out(multiplexer_97_out[4]), .sel(PLA_1_out[3]));
  Multiplexer multiplexer_102 (
    .in0(multiplexer_65_out[5]), .in1(multiplexer_65_out[6]), .out(multiplexer_97_out[5]), .sel(PLA_1_out[3]));
  Multiplexer multiplexer_103 (
    .in0(multiplexer_65_out[6]), .in1(multiplexer_65_out[7]), .out(multiplexer_97_out[6]), .sel(PLA_1_out[3]));
  Multiplexer multiplexer_104 (
    .in0(multiplexer_65_out[7]), .in1(multiplexer_65_out[8]), .out(multiplexer_97_out[7]), .sel(PLA_1_out[3]));
  Multiplexer multiplexer_105 (
    .in0(multiplexer_65_out[8]), .in1(multiplexer_65_out[9]), .out(multiplexer_97_out[8]), .sel(PLA_1_out[3]));
  Multiplexer multiplexer_106 (
    .in0(multiplexer_65_out[9]), .in1(multiplexer_65_out[10]), .out(multiplexer_97_out[9]), .sel(PLA_1_out[3]));
  Multiplexer multiplexer_107 (
    .in0(multiplexer_65_out[10]), .in1(multiplexer_65_out[11]), .out(multiplexer_97_out[10]),
    .sel(PLA_1_out[3]));
  Multiplexer multiplexer_108 (
    .in0(multiplexer_65_out[11]), .in1(multiplexer_65_out[12]), .out(multiplexer_97_out[11]),
    .sel(PLA_1_out[3]));
  Multiplexer multiplexer_109 (
    .in0(multiplexer_65_out[12]), .in1(multiplexer_65_out[13]), .out(multiplexer_97_out[12]),
    .sel(PLA_1_out[3]));
  Multiplexer multiplexer_110 (
    .in0(multiplexer_65_out[13]), .in1(multiplexer_65_out[14]), .out(multiplexer_97_out[13]),
    .sel(PLA_1_out[3]));
  Multiplexer multiplexer_111 (
    .in0(multiplexer_65_out[14]), .in1(multiplexer_65_out[15]), .out(multiplexer_97_out[14]),
    .sel(PLA_1_out[3]));
  Multiplexer multiplexer_112 (
    .in0(multiplexer_65_out[15]), .in1(1'b0), .out(multiplexer_97_out[15]), .sel(PLA_1_out[3]));
  and and_8 (and_8_out, multiplexer_81_out[0], PLA_1_out[11]);
  Multiplexer multiplexer_113 (
    .in0(multiplexer_81_out[0]), .in1(multiplexer_81_out[1]), .out(multiplexer_113_out[0]),
    .sel(PLA_1_out[11]));
  Multiplexer multiplexer_114 (
    .in0(multiplexer_81_out[1]), .in1(multiplexer_81_out[2]), .out(multiplexer_113_out[1]),
    .sel(PLA_1_out[11]));
  Multiplexer multiplexer_115 (
    .in0(multiplexer_81_out[2]), .in1(multiplexer_81_out[3]), .out(multiplexer_113_out[2]),
    .sel(PLA_1_out[11]));
  Multiplexer multiplexer_116 (
    .in0(multiplexer_81_out[3]), .in1(multiplexer_81_out[4]), .out(multiplexer_113_out[3]),
    .sel(PLA_1_out[11]));
  Multiplexer multiplexer_117 (
    .in0(multiplexer_81_out[4]), .in1(multiplexer_81_out[5]), .out(multiplexer_113_out[4]),
    .sel(PLA_1_out[11]));
  Multiplexer multiplexer_118 (
    .in0(multiplexer_81_out[5]), .in1(multiplexer_81_out[6]), .out(multiplexer_113_out[5]),
    .sel(PLA_1_out[11]));
  Multiplexer multiplexer_119 (
    .in0(multiplexer_81_out[6]), .in1(multiplexer_81_out[7]), .out(multiplexer_113_out[6]),
    .sel(PLA_1_out[11]));
  Multiplexer multiplexer_120 (
    .in0(multiplexer_81_out[7]), .in1(multiplexer_81_out[8]), .out(multiplexer_113_out[7]),
    .sel(PLA_1_out[11]));
  Multiplexer multiplexer_121 (
    .in0(multiplexer_81_out[8]), .in1(multiplexer_81_out[9]), .out(multiplexer_113_out[8]),
    .sel(PLA_1_out[11]));
  Multiplexer multiplexer_122 (
    .in0(multiplexer_81_out[9]), .in1(multiplexer_81_out[10]), .out(multiplexer_113_out[9]),
    .sel(PLA_1_out[11]));
  Multiplexer multiplexer_123 (
    .in0(multiplexer_81_out[10]), .in1(multiplexer_81_out[11]), .out(multiplexer_113_out[10]),
    .sel(PLA_1_out[11]));
  Multiplexer multiplexer_124 (
    .in0(multiplexer_81_out[11]), .in1(multiplexer_81_out[12]), .out(multiplexer_113_out[11]),
    .sel(PLA_1_out[11]));
  Multiplexer multiplexer_125 (
    .in0(multiplexer_81_out[12]), .in1(multiplexer_81_out[13]), .out(multiplexer_113_out[12]),
    .sel(PLA_1_out[11]));
  Multiplexer multiplexer_126 (
    .in0(multiplexer_81_out[13]), .in1(multiplexer_81_out[14]), .out(multiplexer_113_out[13]),
    .sel(PLA_1_out[11]));
  Multiplexer multiplexer_127 (
    .in0(multiplexer_81_out[14]), .in1(multiplexer_81_out[15]), .out(multiplexer_113_out[14]),
    .sel(PLA_1_out[11]));
  Multiplexer multiplexer_128 (
    .in0(multiplexer_81_out[15]), .in1(1'b0), .out(multiplexer_113_out[15]), .sel(PLA_1_out[11]));
  and and_9 (and_9_out, multiplexer_97_out[0], PLA_1_out[4]);
  Multiplexer multiplexer_129 (
    .in0(multiplexer_97_out[0]), .in1(multiplexer_97_out[1]), .out(multiplexer_129_out[0]), .sel(PLA_1_out[4]));
  Multiplexer multiplexer_130 (
    .in0(multiplexer_97_out[1]), .in1(multiplexer_97_out[2]), .out(multiplexer_129_out[1]), .sel(PLA_1_out[4]));
  Multiplexer multiplexer_131 (
    .in0(multiplexer_97_out[2]), .in1(multiplexer_97_out[3]), .out(multiplexer_129_out[2]), .sel(PLA_1_out[4]));
  Multiplexer multiplexer_132 (
    .in0(multiplexer_97_out[3]), .in1(multiplexer_97_out[4]), .out(multiplexer_129_out[3]), .sel(PLA_1_out[4]));
  Multiplexer multiplexer_133 (
    .in0(multiplexer_97_out[4]), .in1(multiplexer_97_out[5]), .out(multiplexer_129_out[4]), .sel(PLA_1_out[4]));
  Multiplexer multiplexer_134 (
    .in0(multiplexer_97_out[5]), .in1(multiplexer_97_out[6]), .out(multiplexer_129_out[5]), .sel(PLA_1_out[4]));
  Multiplexer multiplexer_135 (
    .in0(multiplexer_97_out[6]), .in1(multiplexer_97_out[7]), .out(multiplexer_129_out[6]), .sel(PLA_1_out[4]));
  Multiplexer multiplexer_136 (
    .in0(multiplexer_97_out[7]), .in1(multiplexer_97_out[8]), .out(multiplexer_129_out[7]), .sel(PLA_1_out[4]));
  Multiplexer multiplexer_137 (
    .in0(multiplexer_97_out[8]), .in1(multiplexer_97_out[9]), .out(multiplexer_129_out[8]), .sel(PLA_1_out[4]));
  Multiplexer multiplexer_138 (
    .in0(multiplexer_97_out[9]), .in1(multiplexer_97_out[10]), .out(multiplexer_129_out[9]),
    .sel(PLA_1_out[4]));
  Multiplexer multiplexer_139 (
    .in0(multiplexer_97_out[10]), .in1(multiplexer_97_out[11]), .out(multiplexer_129_out[10]),
    .sel(PLA_1_out[4]));
  Multiplexer multiplexer_140 (
    .in0(multiplexer_97_out[11]), .in1(multiplexer_97_out[12]), .out(multiplexer_129_out[11]),
    .sel(PLA_1_out[4]));
  Multiplexer multiplexer_141 (
    .in0(multiplexer_97_out[12]), .in1(multiplexer_97_out[13]), .out(multiplexer_129_out[12]),
    .sel(PLA_1_out[4]));
  Multiplexer multiplexer_142 (
    .in0(multiplexer_97_out[13]), .in1(multiplexer_97_out[14]), .out(multiplexer_129_out[13]),
    .sel(PLA_1_out[4]));
  Multiplexer multiplexer_143 (
    .in0(multiplexer_97_out[14]), .in1(multiplexer_97_out[15]), .out(multiplexer_129_out[14]),
    .sel(PLA_1_out[4]));
  Multiplexer multiplexer_144 (
    .in0(multiplexer_97_out[15]), .in1(1'b0), .out(multiplexer_129_out[15]), .sel(PLA_1_out[4]));
  and and_10 (and_10_out, multiplexer_113_out[0], PLA_1_out[12]);
  Multiplexer multiplexer_145 (
    .in0(multiplexer_113_out[0]), .in1(multiplexer_113_out[1]), .out(multiplexer_145_out[0]),
    .sel(PLA_1_out[12]));
  Multiplexer multiplexer_146 (
    .in0(multiplexer_113_out[1]), .in1(multiplexer_113_out[2]), .out(multiplexer_145_out[1]),
    .sel(PLA_1_out[12]));
  Multiplexer multiplexer_147 (
    .in0(multiplexer_113_out[2]), .in1(multiplexer_113_out[3]), .out(multiplexer_145_out[2]),
    .sel(PLA_1_out[12]));
  Multiplexer multiplexer_148 (
    .in0(multiplexer_113_out[3]), .in1(multiplexer_113_out[4]), .out(multiplexer_145_out[3]),
    .sel(PLA_1_out[12]));
  Multiplexer multiplexer_149 (
    .in0(multiplexer_113_out[4]), .in1(multiplexer_113_out[5]), .out(multiplexer_145_out[4]),
    .sel(PLA_1_out[12]));
  Multiplexer multiplexer_150 (
    .in0(multiplexer_113_out[5]), .in1(multiplexer_113_out[6]), .out(multiplexer_145_out[5]),
    .sel(PLA_1_out[12]));
  Multiplexer multiplexer_151 (
    .in0(multiplexer_113_out[6]), .in1(multiplexer_113_out[7]), .out(multiplexer_145_out[6]),
    .sel(PLA_1_out[12]));
  Multiplexer multiplexer_152 (
    .in0(multiplexer_113_out[7]), .in1(multiplexer_113_out[8]), .out(multiplexer_145_out[7]),
    .sel(PLA_1_out[12]));
  Multiplexer multiplexer_153 (
    .in0(multiplexer_113_out[8]), .in1(multiplexer_113_out[9]), .out(multiplexer_145_out[8]),
    .sel(PLA_1_out[12]));
  Multiplexer multiplexer_154 (
    .in0(multiplexer_113_out[9]), .in1(multiplexer_113_out[10]), .out(multiplexer_145_out[9]),
    .sel(PLA_1_out[12]));
  Multiplexer multiplexer_155 (
    .in0(multiplexer_113_out[10]), .in1(multiplexer_113_out[11]), .out(multiplexer_145_out[10]),
    .sel(PLA_1_out[12]));
  Multiplexer multiplexer_156 (
    .in0(multiplexer_113_out[11]), .in1(multiplexer_113_out[12]), .out(multiplexer_145_out[11]),
    .sel(PLA_1_out[12]));
  Multiplexer multiplexer_157 (
    .in0(multiplexer_113_out[12]), .in1(multiplexer_113_out[13]), .out(multiplexer_145_out[12]),
    .sel(PLA_1_out[12]));
  Multiplexer multiplexer_158 (
    .in0(multiplexer_113_out[13]), .in1(multiplexer_113_out[14]), .out(multiplexer_145_out[13]),
    .sel(PLA_1_out[12]));
  Multiplexer multiplexer_159 (
    .in0(multiplexer_113_out[14]), .in1(multiplexer_113_out[15]), .out(multiplexer_145_out[14]),
    .sel(PLA_1_out[12]));
  Multiplexer multiplexer_160 (
    .in0(multiplexer_113_out[15]), .in1(1'b0), .out(multiplexer_145_out[15]), .sel(PLA_1_out[12]));
  and and_11 (and_11_out, multiplexer_129_out[0], PLA_1_out[5]);
  Multiplexer multiplexer_161 (
    .in0(multiplexer_129_out[0]), .in1(multiplexer_129_out[1]), .out(multiplexer_161_out[0]),
    .sel(PLA_1_out[5]));
  Multiplexer multiplexer_162 (
    .in0(multiplexer_129_out[1]), .in1(multiplexer_129_out[2]), .out(multiplexer_161_out[1]),
    .sel(PLA_1_out[5]));
  Multiplexer multiplexer_163 (
    .in0(multiplexer_129_out[2]), .in1(multiplexer_129_out[3]), .out(multiplexer_161_out[2]),
    .sel(PLA_1_out[5]));
  Multiplexer multiplexer_164 (
    .in0(multiplexer_129_out[3]), .in1(multiplexer_129_out[4]), .out(multiplexer_161_out[3]),
    .sel(PLA_1_out[5]));
  Multiplexer multiplexer_165 (
    .in0(multiplexer_129_out[4]), .in1(multiplexer_129_out[5]), .out(multiplexer_161_out[4]),
    .sel(PLA_1_out[5]));
  Multiplexer multiplexer_166 (
    .in0(multiplexer_129_out[5]), .in1(multiplexer_129_out[6]), .out(multiplexer_161_out[5]),
    .sel(PLA_1_out[5]));
  Multiplexer multiplexer_167 (
    .in0(multiplexer_129_out[6]), .in1(multiplexer_129_out[7]), .out(multiplexer_161_out[6]),
    .sel(PLA_1_out[5]));
  Multiplexer multiplexer_168 (
    .in0(multiplexer_129_out[7]), .in1(multiplexer_129_out[8]), .out(multiplexer_161_out[7]),
    .sel(PLA_1_out[5]));
  Multiplexer multiplexer_169 (
    .in0(multiplexer_129_out[8]), .in1(multiplexer_129_out[9]), .out(multiplexer_161_out[8]),
    .sel(PLA_1_out[5]));
  Multiplexer multiplexer_170 (
    .in0(multiplexer_129_out[9]), .in1(multiplexer_129_out[10]), .out(multiplexer_161_out[9]),
    .sel(PLA_1_out[5]));
  Multiplexer multiplexer_171 (
    .in0(multiplexer_129_out[10]), .in1(multiplexer_129_out[11]), .out(multiplexer_161_out[10]),
    .sel(PLA_1_out[5]));
  Multiplexer multiplexer_172 (
    .in0(multiplexer_129_out[11]), .in1(multiplexer_129_out[12]), .out(multiplexer_161_out[11]),
    .sel(PLA_1_out[5]));
  Multiplexer multiplexer_173 (
    .in0(multiplexer_129_out[12]), .in1(multiplexer_129_out[13]), .out(multiplexer_161_out[12]),
    .sel(PLA_1_out[5]));
  Multiplexer multiplexer_174 (
    .in0(multiplexer_129_out[13]), .in1(multiplexer_129_out[14]), .out(multiplexer_161_out[13]),
    .sel(PLA_1_out[5]));
  Multiplexer multiplexer_175 (
    .in0(multiplexer_129_out[14]), .in1(multiplexer_129_out[15]), .out(multiplexer_161_out[14]),
    .sel(PLA_1_out[5]));
  Multiplexer multiplexer_176 (
    .in0(multiplexer_129_out[15]), .in1(1'b0), .out(multiplexer_161_out[15]), .sel(PLA_1_out[5]));
  and and_12 (and_12_out, multiplexer_145_out[0], PLA_1_out[13]);
  Multiplexer multiplexer_177 (
    .in0(multiplexer_145_out[0]), .in1(multiplexer_145_out[1]), .out(multiplexer_177_out[0]),
    .sel(PLA_1_out[13]));
  Multiplexer multiplexer_178 (
    .in0(multiplexer_145_out[1]), .in1(multiplexer_145_out[2]), .out(multiplexer_177_out[1]),
    .sel(PLA_1_out[13]));
  Multiplexer multiplexer_179 (
    .in0(multiplexer_145_out[2]), .in1(multiplexer_145_out[3]), .out(multiplexer_177_out[2]),
    .sel(PLA_1_out[13]));
  Multiplexer multiplexer_180 (
    .in0(multiplexer_145_out[3]), .in1(multiplexer_145_out[4]), .out(multiplexer_177_out[3]),
    .sel(PLA_1_out[13]));
  Multiplexer multiplexer_181 (
    .in0(multiplexer_145_out[4]), .in1(multiplexer_145_out[5]), .out(multiplexer_177_out[4]),
    .sel(PLA_1_out[13]));
  Multiplexer multiplexer_182 (
    .in0(multiplexer_145_out[5]), .in1(multiplexer_145_out[6]), .out(multiplexer_177_out[5]),
    .sel(PLA_1_out[13]));
  Multiplexer multiplexer_183 (
    .in0(multiplexer_145_out[6]), .in1(multiplexer_145_out[7]), .out(multiplexer_177_out[6]),
    .sel(PLA_1_out[13]));
  Multiplexer multiplexer_184 (
    .in0(multiplexer_145_out[7]), .in1(multiplexer_145_out[8]), .out(multiplexer_177_out[7]),
    .sel(PLA_1_out[13]));
  Multiplexer multiplexer_185 (
    .in0(multiplexer_145_out[8]), .in1(multiplexer_145_out[9]), .out(multiplexer_177_out[8]),
    .sel(PLA_1_out[13]));
  Multiplexer multiplexer_186 (
    .in0(multiplexer_145_out[9]), .in1(multiplexer_145_out[10]), .out(multiplexer_177_out[9]),
    .sel(PLA_1_out[13]));
  Multiplexer multiplexer_187 (
    .in0(multiplexer_145_out[10]), .in1(multiplexer_145_out[11]), .out(multiplexer_177_out[10]),
    .sel(PLA_1_out[13]));
  Multiplexer multiplexer_188 (
    .in0(multiplexer_145_out[11]), .in1(multiplexer_145_out[12]), .out(multiplexer_177_out[11]),
    .sel(PLA_1_out[13]));
  Multiplexer multiplexer_189 (
    .in0(multiplexer_145_out[12]), .in1(multiplexer_145_out[13]), .out(multiplexer_177_out[12]),
    .sel(PLA_1_out[13]));
  Multiplexer multiplexer_190 (
    .in0(multiplexer_145_out[13]), .in1(multiplexer_145_out[14]), .out(multiplexer_177_out[13]),
    .sel(PLA_1_out[13]));
  Multiplexer multiplexer_191 (
    .in0(multiplexer_145_out[14]), .in1(multiplexer_145_out[15]), .out(multiplexer_177_out[14]),
    .sel(PLA_1_out[13]));
  Multiplexer multiplexer_192 (
    .in0(multiplexer_145_out[15]), .in1(1'b0), .out(multiplexer_177_out[15]), .sel(PLA_1_out[13]));
  and and_13 (and_13_out, multiplexer_161_out[0], PLA_1_out[6]);
  and and_14 (and_14_out, multiplexer_177_out[0], PLA_1_out[14]);
  Multiplexer multiplexer_193 (
    .in0(multiplexer_161_out[0]), .in1(multiplexer_161_out[1]), .out(multiplexer_193_out[0]),
    .sel(PLA_1_out[6]));
  Multiplexer multiplexer_194 (
    .in0(multiplexer_161_out[1]), .in1(multiplexer_161_out[2]), .out(multiplexer_193_out[1]),
    .sel(PLA_1_out[6]));
  Multiplexer multiplexer_195 (
    .in0(multiplexer_161_out[2]), .in1(multiplexer_161_out[3]), .out(multiplexer_193_out[2]),
    .sel(PLA_1_out[6]));
  Multiplexer multiplexer_196 (
    .in0(multiplexer_161_out[3]), .in1(multiplexer_161_out[4]), .out(multiplexer_193_out[3]),
    .sel(PLA_1_out[6]));
  Multiplexer multiplexer_197 (
    .in0(multiplexer_161_out[4]), .in1(multiplexer_161_out[5]), .out(multiplexer_193_out[4]),
    .sel(PLA_1_out[6]));
  Multiplexer multiplexer_198 (
    .in0(multiplexer_161_out[5]), .in1(multiplexer_161_out[6]), .out(multiplexer_193_out[5]),
    .sel(PLA_1_out[6]));
  Multiplexer multiplexer_199 (
    .in0(multiplexer_161_out[6]), .in1(multiplexer_161_out[7]), .out(multiplexer_193_out[6]),
    .sel(PLA_1_out[6]));
  Multiplexer multiplexer_200 (
    .in0(multiplexer_161_out[7]), .in1(multiplexer_161_out[8]), .out(multiplexer_193_out[7]),
    .sel(PLA_1_out[6]));
  Multiplexer multiplexer_201 (
    .in0(multiplexer_161_out[8]), .in1(multiplexer_161_out[9]), .out(multiplexer_193_out[8]),
    .sel(PLA_1_out[6]));
  Multiplexer multiplexer_202 (
    .in0(multiplexer_161_out[9]), .in1(multiplexer_161_out[10]), .out(multiplexer_193_out[9]),
    .sel(PLA_1_out[6]));
  Multiplexer multiplexer_203 (
    .in0(multiplexer_161_out[10]), .in1(multiplexer_161_out[11]), .out(multiplexer_193_out[10]),
    .sel(PLA_1_out[6]));
  Multiplexer multiplexer_204 (
    .in0(multiplexer_161_out[11]), .in1(multiplexer_161_out[12]), .out(multiplexer_193_out[11]),
    .sel(PLA_1_out[6]));
  Multiplexer multiplexer_205 (
    .in0(multiplexer_161_out[12]), .in1(multiplexer_161_out[13]), .out(multiplexer_193_out[12]),
    .sel(PLA_1_out[6]));
  Multiplexer multiplexer_206 (
    .in0(multiplexer_161_out[13]), .in1(multiplexer_161_out[14]), .out(multiplexer_193_out[13]),
    .sel(PLA_1_out[6]));
  Multiplexer multiplexer_207 (
    .in0(multiplexer_161_out[14]), .in1(multiplexer_161_out[15]), .out(multiplexer_193_out[14]),
    .sel(PLA_1_out[6]));
  Multiplexer multiplexer_208 (
    .in0(multiplexer_161_out[15]), .in1(1'b0), .out(multiplexer_193_out[15]), .sel(PLA_1_out[6]));
  Multiplexer multiplexer_209 (
    .in0(multiplexer_177_out[0]), .in1(multiplexer_177_out[1]), .out(Output_bus_1[0]), .sel(PLA_1_out[14]));
  Multiplexer multiplexer_210 (
    .in0(multiplexer_177_out[1]), .in1(multiplexer_177_out[2]), .out(Output_bus_1[1]), .sel(PLA_1_out[14]));
  Multiplexer multiplexer_211 (
    .in0(multiplexer_177_out[2]), .in1(multiplexer_177_out[3]), .out(Output_bus_1[2]), .sel(PLA_1_out[14]));
  Multiplexer multiplexer_212 (
    .in0(multiplexer_177_out[3]), .in1(multiplexer_177_out[4]), .out(Output_bus_1[3]), .sel(PLA_1_out[14]));
  Multiplexer multiplexer_213 (
    .in0(multiplexer_177_out[4]), .in1(multiplexer_177_out[5]), .out(Output_bus_1[4]), .sel(PLA_1_out[14]));
  Multiplexer multiplexer_214 (
    .in0(multiplexer_177_out[5]), .in1(multiplexer_177_out[6]), .out(Output_bus_1[5]), .sel(PLA_1_out[14]));
  Multiplexer multiplexer_215 (
    .in0(multiplexer_177_out[6]), .in1(multiplexer_177_out[7]), .out(Output_bus_1[6]), .sel(PLA_1_out[14]));
  Multiplexer multiplexer_216 (
    .in0(multiplexer_177_out[7]), .in1(multiplexer_177_out[8]), .out(Output_bus_1[7]), .sel(PLA_1_out[14]));
  Multiplexer multiplexer_217 (
    .in0(multiplexer_177_out[8]), .in1(multiplexer_177_out[9]), .out(Output_bus_1[8]), .sel(PLA_1_out[14]));
  Multiplexer multiplexer_218 (
    .in0(multiplexer_177_out[9]), .in1(multiplexer_177_out[10]), .out(Output_bus_1[9]), .sel(PLA_1_out[14]));
  Multiplexer multiplexer_219 (
    .in0(multiplexer_177_out[10]), .in1(multiplexer_177_out[11]), .out(Output_bus_1[10]), .sel(PLA_1_out[14]));
  Multiplexer multiplexer_220 (
    .in0(multiplexer_177_out[11]), .in1(multiplexer_177_out[12]), .out(Output_bus_1[11]), .sel(PLA_1_out[14]));
  Multiplexer multiplexer_221 (
    .in0(multiplexer_177_out[12]), .in1(multiplexer_177_out[13]), .out(Output_bus_1[12]), .sel(PLA_1_out[14]));
  Multiplexer multiplexer_222 (
    .in0(multiplexer_177_out[13]), .in1(multiplexer_177_out[14]), .out(Output_bus_1[13]), .sel(PLA_1_out[14]));
  Multiplexer multiplexer_223 (
    .in0(multiplexer_177_out[14]), .in1(multiplexer_177_out[15]), .out(Output_bus_1[14]), .sel(PLA_1_out[14]));
  Multiplexer multiplexer_224 (.in0(multiplexer_177_out[15]), .in1(1'b0), .out(Output_bus_1[15]), .sel(PLA_1_out[14]));
  or or_1 (or_1_out, and_4_out, and_6_out, and_8_out, and_2_out, and_12_out, and_14_out, and_10_out);
  and and_15 (and_15_out, multiplexer_193_out[0], PLA_1_out[7]);
  Multiplexer multiplexer_225 (
    .in0(multiplexer_193_out[0]), .in1(multiplexer_193_out[1]), .out(multiplexer_225_out[0]),
    .sel(PLA_1_out[7]));
  Multiplexer multiplexer_226 (
    .in0(multiplexer_193_out[1]), .in1(multiplexer_193_out[2]), .out(multiplexer_225_out[1]),
    .sel(PLA_1_out[7]));
  Multiplexer multiplexer_227 (
    .in0(multiplexer_193_out[2]), .in1(multiplexer_193_out[3]), .out(multiplexer_225_out[2]),
    .sel(PLA_1_out[7]));
  Multiplexer multiplexer_228 (
    .in0(multiplexer_193_out[3]), .in1(multiplexer_193_out[4]), .out(multiplexer_225_out[3]),
    .sel(PLA_1_out[7]));
  Multiplexer multiplexer_229 (
    .in0(multiplexer_193_out[4]), .in1(multiplexer_193_out[5]), .out(multiplexer_225_out[4]),
    .sel(PLA_1_out[7]));
  Multiplexer multiplexer_230 (
    .in0(multiplexer_193_out[5]), .in1(multiplexer_193_out[6]), .out(multiplexer_225_out[5]),
    .sel(PLA_1_out[7]));
  Multiplexer multiplexer_231 (
    .in0(multiplexer_193_out[6]), .in1(multiplexer_193_out[7]), .out(multiplexer_225_out[6]),
    .sel(PLA_1_out[7]));
  Multiplexer multiplexer_232 (
    .in0(multiplexer_193_out[7]), .in1(multiplexer_193_out[8]), .out(multiplexer_225_out[7]),
    .sel(PLA_1_out[7]));
  Multiplexer multiplexer_233 (
    .in0(multiplexer_193_out[8]), .in1(multiplexer_193_out[9]), .out(multiplexer_225_out[8]),
    .sel(PLA_1_out[7]));
  Multiplexer multiplexer_234 (
    .in0(multiplexer_193_out[9]), .in1(multiplexer_193_out[10]), .out(multiplexer_225_out[9]),
    .sel(PLA_1_out[7]));
  Multiplexer multiplexer_235 (
    .in0(multiplexer_193_out[10]), .in1(multiplexer_193_out[11]), .out(multiplexer_225_out[10]),
    .sel(PLA_1_out[7]));
  Multiplexer multiplexer_236 (
    .in0(multiplexer_193_out[11]), .in1(multiplexer_193_out[12]), .out(multiplexer_225_out[11]),
    .sel(PLA_1_out[7]));
  Multiplexer multiplexer_237 (
    .in0(multiplexer_193_out[12]), .in1(multiplexer_193_out[13]), .out(multiplexer_225_out[12]),
    .sel(PLA_1_out[7]));
  Multiplexer multiplexer_238 (
    .in0(multiplexer_193_out[13]), .in1(multiplexer_193_out[14]), .out(multiplexer_225_out[13]),
    .sel(PLA_1_out[7]));
  Multiplexer multiplexer_239 (
    .in0(multiplexer_193_out[14]), .in1(multiplexer_193_out[15]), .out(multiplexer_225_out[14]),
    .sel(PLA_1_out[7]));
  Multiplexer multiplexer_240 (
    .in0(multiplexer_193_out[15]), .in1(1'b0), .out(multiplexer_225_out[15]), .sel(PLA_1_out[7]));
  or or_2 (or_2_out, and_1_out, and_3_out, and_5_out, and_7_out, and_11_out, and_13_out, and_15_out, and_9_out);
  or or_3 (carry_out, or_2_out, or_1_out);
endmodule
module Instruction_Control (
  input  [15:0] mem_data_in,
  input  [15:0] mem_addr_in,
  input  CLK,
  input  [15:0] pc_data_in,
  input  pc_write_enable,
  input  carry_flag,
  input  zero_flag,
  input  sign_flag,
  input  RESET,
  input  INT,
  input  exec_mode,
  input  OS_RESTART,
  input  [15:0] sp_in,
  output [15:0] mem_data_out,
  output [15:0] operand,
  output [15:0] pc_data_out,
  output [20:0] CPU_Control_BUS,
  output intret,
  output HLT,
  output [15:0] output_status
);

  wire and_1_out, comparator_1_eq, comparator_2_eq, comparator_2_gt, comparator_2_lt, comparator_3_lt,
       comparator_5_eq, comparator_6_eq, comparator_7_eq, Instruction_permission_checker_out, not_1_out,
       not_2_out, or_1_out, or_2_out, or_3_out, or_4_out, or_5_out;
  wire [0:0] multiplexer_8_out;
  wire [5:0] State_To_Output_Decoder_out;
  wire [7:0] Next_State_Decoder_out;
  wire [15:0] adder_1_out, adder_2_out, adder_3_out, adder_4_out, adder_5_out, adder_6_out,
       BIOS_LOAD_COUNTER_q, BIOS_ROM_data, IMBD_out, IR_opcode_q, IR_opd_q, MFCR_q, MOR_q, multiplexer_1_out,
       multiplexer_2_out, multiplexer_3_out, multiplexer_4_out, multiplexer_5_out, State_Register_q;
  wire [20:20] and_3_out;
  wire [21:0] multiplexer_7_out;
  wire [23:0] Microcode_ROM_data;

  sixteen_register sixteen_register_1 (
    .OS_RESTART(OS_RESTART), .CLK(CLK), .RESET(RESET), .D(multiplexer_1_out), .WE(or_1_out), .Q(pc_data_out));
  Register #(.width(16)) BIOS_LOAD_COUNTER (
    .D(adder_1_out), .en(comparator_2_gt), .clk(CLK), .Q(BIOS_LOAD_COUNTER_q), .clr(RESET));
  Adder #(.width(16)) adder_1 (.a(BIOS_LOAD_COUNTER_q), .b(16'h1), .out(adder_1_out));  // open: cin, cout
  Comparator #(.mode("unsigned"), .width(16)) comparator_1 (
    .a(pc_data_out), .b(16'h8d3), .eq(comparator_1_eq));  // open: gt, lt
  and and_1 (and_1_out, comparator_1_eq, 1'b0);
  Multiplexer #(.width(16)) multiplexer_1 (
    .in0(adder_3_out), .in1(pc_data_in), .out(multiplexer_1_out), .sel(pc_write_enable));
  or or_1 (or_1_out, pc_write_enable, State_To_Output_Decoder_out[1]);
  Comparator #(.mode("unsigned"), .width(16)) comparator_2 (
    .a(adder_2_out), .b(BIOS_LOAD_COUNTER_q), .gt(comparator_2_gt), .eq(comparator_2_eq), .lt(comparator_2_lt));
  Adder #(.width(16)) adder_2 (.a(16'h255), .b(16'h1), .out(adder_2_out));  // open: cin, cout
  Adder #(.width(16)) adder_3 (.a(pc_data_out), .b(16'h1), .out(adder_3_out));  // open: cin, cout
  or or_2 (or_2_out, comparator_2_eq, comparator_2_lt);
  ROM #(.addrWidth(16), .dataWidth(16)) BIOS_ROM (.addr(BIOS_LOAD_COUNTER_q), .data(BIOS_ROM_data));
  LedBar #(.matrixcols(16)) LedBar_4 (
    .led0(pc_data_out[15]), .led1(pc_data_out[14]), .led2(pc_data_out[13]), .led3(pc_data_out[12]),
    .led4(pc_data_out[11]), .led5(pc_data_out[10]), .led6(pc_data_out[9]), .led7(pc_data_out[8]),
    .led8(pc_data_out[7]), .led9(pc_data_out[6]), .led10(pc_data_out[5]), .led11(pc_data_out[4]),
    .led12(pc_data_out[3]), .led13(pc_data_out[2]), .led14(pc_data_out[1]), .led15(pc_data_out[0]));
  Adder #(.width(16)) adder_4 (.a(mem_addr_in), .b(operand), .out(adder_4_out), .cin(1'b0));  // open: cout
  Multiplexer #(.width(16)) multiplexer_2 (
    .in0(mem_data_in), .in1(BIOS_ROM_data), .out(multiplexer_2_out), .sel(comparator_2_gt));
  Multiplexer #(.select(2), .width(16)) multiplexer_3 (
    .in0(pc_data_out), .in1(adder_4_out), .in2(IR_opd_q), .out(multiplexer_3_out), .sel(CPU_Control_BUS[1:0]));  // open: in3
  or or_3 (or_3_out, comparator_2_gt, multiplexer_8_out[0]);
  Clock clock_1 ();  // open: out
  Multiplexer #(.width(16)) multiplexer_4 (
    .in0(multiplexer_3_out), .in1(BIOS_LOAD_COUNTER_q), .out(multiplexer_4_out), .sel(comparator_2_gt));
  RAM #(.addrWidth(16), .dataWidth(16), .enables("line")) RAM_1 (
    .addr(multiplexer_4_out), .we(or_3_out), .clk(CLK), .din(multiplexer_2_out), .dout(mem_data_out));
  PLA #(.in_width(17), .out_width(8), .\table ("0xxxxxxxx00000000 00000001 # INT_Check -> Instruction_Fetch_1\n1xxxxxxxx00000000 00000111 # INT_Check -> INT_PROC_1\nxxxxxxxxx00000111 00001000 # INT_PROC_1 -> INT_PROC_2\nxxxxxxxxx00001000 00001001 # INT_PROC_2 -> INT_PROC_3\nxxxxxxxxx00001001 00001010 # INT_PROC_3 -> INT_PROC_4\nxxxxxxxxx00001010 00001011 # INT_PROC_4 -> INT_PROC_5\nxxxxxxxxx00001011 00001100 # INT_PROC_5 -> INT_PROC_6\nxxxxxxxxx00001100 00001101 # INT_PROC_6 -> INT_PROC_7\nxxxxxxxxx00001101 00001110 # INT_PROC_7 -> INT_PROC_8\nxxxxxxxxx00001110 00001111 # INT_PROC_8 -> INT_PROC_9\nxxxxxxxxx00001111 00010000 # INT_PROC_9 -> INT_PROC_10\nxxxxxxxxx00010000 00010001 # INT_PROC_10 -> INT_PROC_11\nxxxxxxxxx00010001 00010010 # INT_PROC_11 -> INT_PROC_12\nxxxxxxxxx00010010 00010011 # INT_PROC_12 -> INT_PROC_13\nxxxxxxxxx00010011 00000000 # INT_PROC_13 -> INT_Check\nxxxxxxxxx00000001 00000010 # Instruction_Fetch_1 -> Instruction_Fetch_2\nxxxxxxxxx00000010 00000110 # Instruction_Fetch_2 -> Instruction_Check\nx0000000100000110 00000011 # Instruction_Check -> Microcode_Execute_11\nx0000001000000110 00000100 # Instruction_Check -> Microcode_Execute_21\nx0000011000000110 00011011 # Instruction_Check -> Microcode_Execute_61\nx0000011100000110 00010100 # Instruciton_Check -> Microcode_Execute_71\nx0000101000000110 00100001 # Instruciton_Check -> Microcode_Execute_10_1\nxxxxxxxxx00011011 00011100 # Microcode_Execute_61 -> Microcode_Execute_62\nxxxxxxxxx00011100 00011101 # Microcode_Execute_62 -> Microcode_Execute_63\nxxxxxxxxx00011101 00011110 # Microcode_Execute_63 -> Microcode_Execute_64\nxxxxxxxxx00011110 00011111 # Microcode_Execute_64 -> Microcode_Execute_65\nxxxxxxxxx00011111 00100000 # Microcode_Execute_65 -> Microcode_Execute_66\nxxxxxxxxx00100000 00000000 # Microcode_Execute_66 -> INT_Check\nxxxxxxxxx00010100 00010101 # Microcode_Execute_71 -> Microcode_Execute_72\nxxxxxxxxx00010101 00010110 # Microcode_Execute_72 -> Microcode_Execute_73\nxxxxxxxxx00010110 00010111 # Microcode_Execute_73 -> Microcode_Execute_74\nxxxxxxxxx00010111 00011000 # Microcode_Execute_74 -> Microcode_Execute_75\nxxxxxxxxx00011000 00011001 # Microcode_Execute_75 -> Microcode_Execute_76\nxxxxxxxxx00011001 00011010 # Microcode_Execute_76 -> Microcode_Execute_77\nxxxxxxxxx00011010 00000000 # Microcode_Execute_77 -> INT_Check\nxxxxxxxxx00100001 00100010 # Microcode_Execute_10_1 -> Microcode_Execute_10_2\nxxxxxxxxx00100010 00100011 # Microcode_Execute_10_2  -> Microcode_Execute_10_3\nxxxxxxxxx00100011 00100100 # Microcode_Execute_10_3  -> Microcode_Execute_10_4\nxxxxxxxxx00100100 00100101 # Microcode_Execute_10_4  -> Microcode_Execute_10_5\nxxxxxxxxx00100101 00100110 # Microcode_Execute_10_5  -> Microcode_Execute_10_6\nxxxxxxxxx00100110 00100111 # Microcode_Execute_10_6  -> Microcode_Execute_10_7\nxxxxxxxxx00100111 00101000 # Microcode_Execute_10_7  -> Microcode_Execute_10_8\nxxxxxxxxx00101000 00101001 # Microcode_Execute_10_8  -> Microcode_Execute_10_9\nxxxxxxxxx00101001 00101010 # Microcode_Execute_10_9  -> Microcode_Execute_10_10\nxxxxxxxxx00101010 00000000 # Microcode_Execute_10_10 -> INT_Check\nxxxxxxxxx00000011 00000000 # Microcode_Execute_11 -> INT_Check\nxxxxxxxxx00000100 00000101 # Microcode_Execute_21 -> Microcode_Execute_22\nxxxxxxxxx00000101 00000000 # Microcode_Execute_22 -> INT_Check")) Next_State_Decoder (
    .in({INT, State_Register_q}), .out(Next_State_Decoder_out));
  Comparator #(.mode("unsigned"), .width(16)) comparator_3 (
    .a(multiplexer_4_out), .b(16'h5600), .lt(comparator_3_lt));  // open: gt, eq
  Comparator #(.mode("unsigned"), .width(16)) comparator_4 (
    .a(sp_in), .b(16'hfc00), .lt(output_status[4]));  // open: gt, eq
  and and_2 (output_status[2], exec_mode, or_5_out, comparator_3_lt);
  Register #(.width(16)) IR_opd (
    .D(mem_data_out), .en(State_To_Output_Decoder_out[5]), .clk(CLK), .Q(IR_opd_q), .clr(RESET));
  Register State_Register (
    .D(Next_State_Decoder_out), .en(or_2_out), .clk(CLK), .Q(State_Register_q[7:0]), .clr(RESET));
  Register #(.width(16)) IR_opcode (
    .D(IR_opd_q), .en(State_To_Output_Decoder_out[5]), .clk(CLK), .Q(IR_opcode_q), .clr(RESET));
  Register #(.width(16)) MFCR (.D(multiplexer_5_out), .en(or_4_out), .clk(CLK), .Q(MFCR_q), .clr(RESET));
  Multiplexer #(.width(16)) multiplexer_5 (
    .in0(adder_5_out), .in1({16{1'b0}}), .out(multiplexer_5_out), .sel(State_To_Output_Decoder_out[3]));
  or or_4 (or_4_out, State_To_Output_Decoder_out[3], State_To_Output_Decoder_out[4]);
  PLA #(.in_width(8), .out_width(7), .\table ("00000000 0000001 # INT_Check\n00000001 0100010 # Instruction_Fetch_1\n00000010 0100010 # Instruction_Fetch_2\n00000011 0001100 # Microcode_Execute_11\n00000100 0010100 # Microcode_Execute_21\n00000101 0001100 # Microcode_Execute_22\n00000110 0000000 # Instruction_Check\n00000111 0010101 # INT_PROC_1\n00001000 0010101 # INT_PROC_2\n00001001 0010101 # INT_PROC_3\n00001010 0010101 # INT_PROC_4\n00001011 0010101 # INT_PROC_5\n00001100 0010101 # INT_PROC_6\n00001101 0010101 # INT_PROC_7\n00001110 0010101 # INT_PROC_8\n00001111 0010101 # INT_PROC_9\n00010000 0010101 # INT_PROC_10\n00010001 0010101 # INT_PROC_11\n00010010 0010101 # INT_PROC_12\n00010011 0001101 # INT_PROC_13\n00010100 0010101 # Microcode_Execute_71\n00010101 0010101 # Microcode_Execute_72\n00010110 0010101 # Microcode_Execute_73\n00010111 0010101 # Microcode_Execute_74\n00011000 0010101 # Microcode_Execute_75\n00011001 0010101 # Microcode_Execute_76\n00011010 1001101 # Microcode_Execute_77\n00011011 0010100 # Microcode_Execute_61\n00011100 0010100 # Microcode_Execute_62\n00011101 0010100 # Microcode_Execute_63\n00011110 0010100 # Microcode_Execute_64\n00011111 0010100 # Microcode_Execute_65\n00100000 0001100 # Microcode_Execute_66\n00100001 0010100 # Microcode_Execute_10_1\n00100010 0010100 # Microcode_Execute_10_2\n00100011 0010100 # Microcode_Execute_10_3\n00100100 0010100 # Microcode_Execute_10_4\n00100101 0010100 # Microcode_Execute_10_5\n00100110 0010100 # Microcode_Execute_10_6\n00100111 0010100 # Microcode_Execute_10_7\n00101000 0010100 # Microcode_Execute_10_8\n00101001 0010100 # Microcode_Execute_10_9\n00101010 0001100 # Microcode_Execute_10_10")) State_To_Output_Decoder (
    .in(State_Register_q[7:0]), .out({intret, State_To_Output_Decoder_out}));
  Adder #(.width(16)) adder_5 (.a(MFCR_q), .b(16'h1), .out(adder_5_out), .cin(1'b0));  // open: cout
  Comparator #(.mode("unsigned")) comparator_5 (
    .a(State_Register_q[7:0]), .b(8'h3), .eq(comparator_5_eq));  // open: gt, lt
  Comparator #(.mode("unsigned")) comparator_6 (
    .a(State_Register_q[7:0]), .b(8'h6), .eq(comparator_6_eq));  // open: gt, lt
  PLA #(.in_width(21), .out_width(8), .\table ("0xxx0xxxxxxxxxxxxxxxx 00000001 # IE=0 (during fetch)\n00xx10000101111111111 00000001 # jnc opd (Taken)\n01xx10000101111111111 00000001 # jnc opd (Skip)\n01xx10000110011111111 00000001 # jc opd (Taken)\n00xx10000110011111111 00000001 # jc opd (Skip)\n0x0x10000110111111111 00000001 # jnz opd (Taken)\n0x1x10000110111111111 00000001 # jnz opd (Skip)\n0x1x10000111011111111 00000001 # jz opd (Taken)\n0x0x10000111011111111 00000001 # jz opd (Skip)\n0xx010000111111111111 00000001 # jns opd (Taken)\n0xx110000111111111111 00000001 # jns opd (Skip)\n0xx110001000011111111 00000001 # js opd (Taken)\n0xx010001000011111111 00000001 # js opd (Skip)\n0xxx10001000111111111 00000001 # jmp opd\n0x1x10001011011111111 00000001 # je opd (Taken)\n0x0x10001011011111111 00000001 # je opd (Skip)\n0x0x10001011111111111 00000001 # jne opd(Taken)\n0x1x10001011111111111 00000001 # jne opd(Skip)\n0x0010001100011111111 00000001 # ja opd (Taken)\n0xxx10001100011111111 00000001 # ja opd (Skip)\n0x0010001100111111111 00000001 # jae opd (Taken)\n0x1010001100111111111 00000001 # jae opd (Taken)\n0xxx10001100111111111 00000001 # jae opd (Skip)\n0x0110001101011111111 00000001 # jl opd (Taken)\n0xxx10001101011111111 00000001 # jl opd (Skip)\n0x0110001101111111111 00000001 # jle opd (Taken)\n0x1010001101111111111 00000001 # jle opd (Taken)\n0xxx10001101111111111 00000001 # jle opd (Skip)\n0xxx10001001111111111 00000001 # hlt\n0xxx10001010011111111 00000001 # nop\n0xxxx1111111111111111 00000001 # invaild\n0xxx10001010111111111 00000001 # lpc\n0xxx10000000000000000 00000001 # add a, a\n0xxx10000000000000001 00000001 # add a, b\n0xxx10000000000000010 00000001 # add a, c\n0xxx10000000000000011 00000001 # add a, d\n0xxx10000000000000100 00000001 # add a, e\n0xxx10000000000000101 00000001 # add a, bp\n0xxx10000000000000110 00000001 # add a, sp\n0xxx10000000000010000 00000001 # add b, a\n0xxx10000000000010001 00000001 # add b, b\n0xxx10000000000010010 00000001 # add b, c\n0xxx10000000000010011 00000001 # add b, d\n0xxx10000000000010100 00000001 # add b, e\n0xxx10000000000010101 00000001 # add b, bp\n0xxx10000000000010110 00000001 # add b, sp\n0xxx10000000000100000 00000001 # add c, a\n0xxx10000000000100001 00000001 # add c, b\n0xxx10000000000100010 00000001 # add c, c\n0xxx10000000000100011 00000001 # add c, d\n0xxx10000000000100100 00000001 # add c, e\n0xxx10000000000100101 00000001 # add c, bp\n0xxx10000000000100110 00000001 # add c, sp\n0xxx10000000000110000 00000001 # add d, a\n0xxx10000000000110001 00000001 # add d, b\n0xxx10000000000110010 00000001 # add d, c\n0xxx10000000000110011 00000001 # add d, d\n0xxx10000000000110100 00000001 # add d, e\n0xxx10000000000110101 00000001 # add d, bp\n0xxx10000000000110110 00000001 # add d, sp\n0xxx10000000001000000 00000001 # add e, a\n0xxx10000000001000001 00000001 # add e, b\n0xxx10000000001000010 00000001 # add e, c\n0xxx10000000001000011 00000001 # add e, d\n0xxx10000000001000100 00000001 # add e, e\n0xxx10000000001000101 00000001 # add e, bp\n0xxx10000000001000110 00000001 # add e, sp\n0xxx10000000001010000 00000001 # add bp, a\n0xxx10000000001010001 00000001 # add bp, b\n0xxx10000000001010010 00000001 # add bp, c\n0xxx10000000001010011 00000001 # add bp, d\n0xxx10000000001010100 00000001 # add bp, e\n0xxx10000000001010101 00000001 # add bp, bp\n0xxx10000000001010110 00000001 # add bp, sp\n0xxx10000000001100000 00000001 # add sp, a\n0xxx10000000001100001 00000001 # add sp, b\n0xxx10000000001100010 00000001 # add sp, c\n0xxx10000000001100011 00000001 # add sp, d\n0xxx10000000001100100 00000001 # add sp, e\n0xxx10000000001100101 00000001 # add sp, bp\n0xxx10000000001100110 00000001 # add sp, sp\n0xxx10000000100000000 00000001 # sub a, a\n0xxx10000000100000001 00000001 # sub a, b\n0xxx10000000100000010 00000001 # sub a, c\n0xxx10000000100000011 00000001 # sub a, d\n0xxx10000000100000100 00000001 # sub a, e\n0xxx10000000100000101 00000001 # sub a, bp\n0xxx10000000100000110 00000001 # sub a, sp\n0xxx10000000100010000 00000001 # sub b, a\n0xxx10000000100010001 00000001 # sub b, b\n0xxx10000000100010010 00000001 # sub b, c\n0xxx10000000100010011 00000001 # sub b, d\n0xxx10000000100010100 00000001 # sub b, e\n0xxx10000000100010101 00000001 # sub b, bp\n0xxx10000000100010110 00000001 # sub b, sp\n0xxx10000000100100000 00000001 # sub c, a\n0xxx10000000100100001 00000001 # sub c, b\n0xxx10000000100100010 00000001 # sub c, c\n0xxx10000000100100011 00000001 # sub c, d\n0xxx10000000100100100 00000001 # sub c, e\n0xxx10000000100100101 00000001 # sub c, bp\n0xxx10000000100100110 00000001 # sub c, sp\n0xxx10000000100110000 00000001 # sub d, a\n0xxx10000000100110001 00000001 # sub d, b\n0xxx10000000100110010 00000001 # sub d, c\n0xxx10000000100110011 00000001 # sub d, d\n0xxx10000000100110100 00000001 # sub d, e\n0xxx10000000100110101 00000001 # sub d, bp\n0xxx10000000100110110 00000001 # sub d, sp\n0xxx10000000101000000 00000001 # sub e, a\n0xxx10000000101000001 00000001 # sub e, b\n0xxx10000000101000010 00000001 # sub e, c\n0xxx10000000101000011 00000001 # sub e, d\n0xxx10000000101000100 00000001 # sub e, e\n0xxx10000000101000101 00000001 # sub e, bp\n0xxx10000000101000110 00000001 # sub e, sp\n0xxx10000000101010000 00000001 # sub bp, a\n0xxx10000000101010001 00000001 # sub bp, b\n0xxx10000000101010010 00000001 # sub bp, c\n0xxx10000000101010011 00000001 # sub bp, d\n0xxx10000000101010100 00000001 # sub bp, e\n0xxx10000000101010101 00000001 # sub bp, bp\n0xxx10000000101010110 00000001 # sub bp, sp\n0xxx10000000101100000 00000001 # sub sp, a\n0xxx10000000101100001 00000001 # sub sp, b\n0xxx10000000101100010 00000001 # sub sp, c\n0xxx10000000101100011 00000001 # sub sp, d\n0xxx10000000101100100 00000001 # sub sp, e\n0xxx10000000101100101 00000001 # sub sp, bp\n0xxx10000000101100110 00000001 # sub sp, sp\n0xxx10000001000000000 00000001 # mul a, a\n0xxx10000001000000001 00000001 # mul a, b\n0xxx10000001000000010 00000001 # mul a, c\n0xxx10000001000000011 00000001 # mul a, d\n0xxx10000001000000100 00000001 # mul a, e\n0xxx10000001000000101 00000001 # mul a, bp\n0xxx10000001000000110 00000001 # mul a, sp\n0xxx10000001000010000 00000001 # mul b, a\n0xxx10000001000010001 00000001 # mul b, b\n0xxx10000001000010010 00000001 # mul b, c\n0xxx10000001000010011 00000001 # mul b, d\n0xxx10000001000010100 00000001 # mul b, e\n0xxx10000001000010101 00000001 # mul b, bp\n0xxx10000001000010110 00000001 # mul b, sp\n0xxx10000001000100000 00000001 # mul c, a\n0xxx10000001000100001 00000001 # mul c, b\n0xxx10000001000100010 00000001 # mul c, c\n0xxx10000001000100011 00000001 # mul c, d\n0xxx10000001000100100 00000001 # mul c, e\n0xxx10000001000100101 00000001 # mul c, bp\n0xxx10000001000100110 00000001 # mul c, sp\n0xxx10000001000110000 00000001 # mul d, a\n0xxx10000001000110001 00000001 # mul d, b\n0xxx10000001000110010 00000001 # mul d, c\n0xxx10000001000110011 00000001 # mul d, d\n0xxx10000001000110100 00000001 # mul d, e\n0xxx10000001000110101 00000001 # mul d, bp\n0xxx10000001000110110 00000001 # mul d, sp\n0xxx10000001001000000 00000001 # mul e, a\n0xxx10000001001000001 00000001 # mul e, b\n0xxx10000001001000010 00000001 # mul e, c\n0xxx10000001001000011 00000001 # mul e, d\n0xxx10000001001000100 00000001 # mul e, e\n0xxx10000001001000101 00000001 # mul e, bp\n0xxx10000001001000110 00000001 # mul e, sp\n0xxx10000001001010000 00000001 # mul bp, a\n0xxx10000001001010001 00000001 # mul bp, b\n0xxx10000001001010010 00000001 # mul bp, c\n0xxx10000001001010011 00000001 # mul bp, d\n0xxx10000001001010100 00000001 # mul bp, e\n0xxx10000001001010101 00000001 # mul bp, bp\n0xxx10000001001010110 00000001 # mul bp, sp\n0xxx10000001001100000 00000001 # mul sp, a\n0xxx10000001001100001 00000001 # mul sp, b\n0xxx10000001001100010 00000001 # mul sp, c\n0xxx10000001001100011 00000001 # mul sp, d\n0xxx10000001001100100 00000001 # mul sp, e\n0xxx10000001001100101 00000001 # mul sp, bp\n0xxx10000001001100110 00000001 # mul sp, sp\n0xxx10000001100000000 00000001 # and a, a\n0xxx10000001100000001 00000001 # and a, b\n0xxx10000001100000010 00000001 # and a, c\n0xxx10000001100000011 00000001 # and a, d\n0xxx10000001100000100 00000001 # and a, e\n0xxx10000001100000101 00000001 # and a, bp\n0xxx10000001100000110 00000001 # and a, sp\n0xxx10000001100010000 00000001 # and b, a\n0xxx10000001100010001 00000001 # and b, b\n0xxx10000001100010010 00000001 # and b, c\n0xxx10000001100010011 00000001 # and b, d\n0xxx10000001100010100 00000001 # and b, e\n0xxx10000001100010101 00000001 # and b, bp\n0xxx10000001100010110 00000001 # and b, sp\n0xxx10000001100100000 00000001 # and c, a\n0xxx10000001100100001 00000001 # and c, b\n0xxx10000001100100010 00000001 # and c, c\n0xxx10000001100100011 00000001 # and c, d\n0xxx10000001100100100 00000001 # and c, e\n0xxx10000001100100101 00000001 # and c, bp\n0xxx10000001100100110 00000001 # and c, sp\n0xxx10000001100110000 00000001 # and d, a\n0xxx10000001100110001 00000001 # and d, b\n0xxx10000001100110010 00000001 # and d, c\n0xxx10000001100110011 00000001 # and d, d\n0xxx10000001100110100 00000001 # and d, e\n0xxx10000001100110101 00000001 # and d, bp\n0xxx10000001100110110 00000001 # and d, sp\n0xxx10000001101000000 00000001 # and e, a\n0xxx10000001101000001 00000001 # and e, b\n0xxx10000001101000010 00000001 # and e, c\n0xxx10000001101000011 00000001 # and e, d\n0xxx10000001101000100 00000001 # and e, e\n0xxx10000001101000101 00000001 # and e, bp\n0xxx10000001101000110 00000001 # and e, sp\n0xxx10000001101010000 00000001 # and bp, a\n0xxx10000001101010001 00000001 # and bp, b\n0xxx10000001101010010 00000001 # and bp, c\n0xxx10000001101010011 00000001 # and bp, d\n0xxx10000001101010100 00000001 # and bp, e\n0xxx10000001101010101 00000001 # and bp, bp\n0xxx10000001101010110 00000001 # and bp, sp\n0xxx10000001101100000 00000001 # and sp, a\n0xxx10000001101100001 00000001 # and sp, b\n0xxx10000001101100010 00000001 # and sp, c\n0xxx10000001101100011 00000001 # and sp, d\n0xxx10000001101100100 00000001 # and sp, e\n0xxx10000001101100101 00000001 # and sp, bp\n0xxx10000001101100110 00000001 # and sp, sp\n0xxx10000010000000000 00000001 # or a, a\n0xxx10000010000000001 00000001 # or a, b\n0xxx10000010000000010 00000001 # or a, c\n0xxx10000010000000011 00000001 # or a, d\n0xxx10000010000000100 00000001 # or a, e\n0xxx10000010000000101 00000001 # or a, bp\n0xxx10000010000000110 00000001 # or a, sp\n0xxx10000010000010000 00000001 # or b, a\n0xxx10000010000010001 00000001 # or b, b\n0xxx10000010000010010 00000001 # or b, c\n0xxx10000010000010011 00000001 # or b, d\n0xxx10000010000010100 00000001 # or b, e\n0xxx10000010000010101 00000001 # or b, bp\n0xxx10000010000010110 00000001 # or b, sp\n0xxx10000010000100000 00000001 # or c, a\n0xxx10000010000100001 00000001 # or c, b\n0xxx10000010000100010 00000001 # or c, c\n0xxx10000010000100011 00000001 # or c, d\n0xxx10000010000100100 00000001 # or c, e\n0xxx10000010000100101 00000001 # or c, bp\n0xxx10000010000100110 00000001 # or c, sp\n0xxx10000010000110000 00000001 # or d, a\n0xxx10000010000110001 00000001 # or d, b\n0xxx10000010000110010 00000001 # or d, c\n0xxx10000010000110011 00000001 # or d, d\n0xxx10000010000110100 00000001 # or d, e\n0xxx10000010000110101 00000001 # or d, bp\n0xxx10000010000110110 00000001 # or d, sp\n0xxx10000010001000000 00000001 # or e, a\n0xxx10000010001000001 00000001 # or e, b\n0xxx10000010001000010 00000001 # or e, c\n0xxx10000010001000011 00000001 # or e, d\n0xxx10000010001000100 00000001 # or e, e\n0xxx10000010001000101 00000001 # or e, bp\n0xxx10000010001000110 00000001 # or e, sp\n0xxx10000010001010000 00000001 # or bp, a\n0xxx10000010001010001 00000001 # or bp, b\n0xxx10000010001010010 00000001 # or bp, c\n0xxx10000010001010011 00000001 # or bp, d\n0xxx10000010001010100 00000001 # or bp, e\n0xxx10000010001010101 00000001 # or bp, bp\n0xxx10000010001010110 00000001 # or bp, sp\n0xxx10000010001100000 00000001 # or sp, a\n0xxx10000010001100001 00000001 # or sp, b\n0xxx10000010001100010 00000001 # or sp, c\n0xxx10000010001100011 00000001 # or sp, d\n0xxx10000010001100100 00000001 # or sp, e\n0xxx10000010001100101 00000001 # or sp, bp\n0xxx10000010001100110 00000001 # or sp, sp\n0xxx10000011000000000 00000001 # xor a, a\n0xxx10000011000000001 00000001 # xor a, b\n0xxx10000011000000010 00000001 # xor a, c\n0xxx10000011000000011 00000001 # xor a, d\n0xxx10000011000000100 00000001 # xor a, e\n0xxx10000011000000101 00000001 # xor a, bp\n0xxx10000011000000110 00000001 # xor a, sp\n0xxx10000011000010000 00000001 # xor b, a\n0xxx10000011000010001 00000001 # xor b, b\n0xxx10000011000010010 00000001 # xor b, c\n0xxx10000011000010011 00000001 # xor b, d\n0xxx10000011000010100 00000001 # xor b, e\n0xxx10000011000010101 00000001 # xor b, bp\n0xxx10000011000010110 00000001 # xor b, sp\n0xxx10000011000100000 00000001 # xor c, a\n0xxx10000011000100001 00000001 # xor c, b\n0xxx10000011000100010 00000001 # xor c, c\n0xxx10000011000100011 00000001 # xor c, d\n0xxx10000011000100100 00000001 # xor c, e\n0xxx10000011000100101 00000001 # xor c, bp\n0xxx10000011000100110 00000001 # xor c, sp\n0xxx10000011000110000 00000001 # xor d, a\n0xxx10000011000110001 00000001 # xor d, b\n0xxx10000011000110010 00000001 # xor d, c\n0xxx10000011000110011 00000001 # xor d, d\n0xxx10000011000110100 00000001 # xor d, e\n0xxx10000011000110101 00000001 # xor d, bp\n0xxx10000011000110110 00000001 # xor d, sp\n0xxx10000011001000000 00000001 # xor e, a\n0xxx10000011001000001 00000001 # xor e, b\n0xxx10000011001000010 00000001 # xor e, c\n0xxx10000011001000011 00000001 # xor e, d\n0xxx10000011001000100 00000001 # xor e, e\n0xxx10000011001000101 00000001 # xor e, bp\n0xxx10000011001000110 00000001 # xor e, sp\n0xxx10000011001010000 00000001 # xor bp, a\n0xxx10000011001010001 00000001 # xor bp, b\n0xxx10000011001010010 00000001 # xor bp, c\n0xxx10000011001010011 00000001 # xor bp, d\n0xxx10000011001010100 00000001 # xor bp, e\n0xxx10000011001010101 00000001 # xor bp, bp\n0xxx10000011001010110 00000001 # xor bp, sp\n0xxx10000011001100000 00000001 # xor sp, a\n0xxx10000011001100001 00000001 # xor sp, b\n0xxx10000011001100010 00000001 # xor sp, c\n0xxx10000011001100011 00000001 # xor sp, d\n0xxx10000011001100100 00000001 # xor sp, e\n0xxx10000011001100101 00000001 # xor sp, bp\n0xxx10000011001100110 00000001 # xor sp, sp\n0xxx10000011100000000 00000001 # shr a, a\n0xxx10000011100000001 00000001 # shr a, b\n0xxx10000011100000010 00000001 # shr a, c\n0xxx10000011100000011 00000001 # shr a, d\n0xxx10000011100000100 00000001 # shr a, e\n0xxx10000011100000101 00000001 # shr a, bp\n0xxx10000011100000110 00000001 # shr a, sp\n0xxx10000011100010000 00000001 # shr b, a\n0xxx10000011100010001 00000001 # shr b, b\n0xxx10000011100010010 00000001 # shr b, c\n0xxx10000011100010011 00000001 # shr b, d\n0xxx10000011100010100 00000001 # shr b, e\n0xxx10000011100010101 00000001 # shr b, bp\n0xxx10000011100010110 00000001 # shr b, sp\n0xxx10000011100100000 00000001 # shr c, a\n0xxx10000011100100001 00000001 # shr c, b\n0xxx10000011100100010 00000001 # shr c, c\n0xxx10000011100100011 00000001 # shr c, d\n0xxx10000011100100100 00000001 # shr c, e\n0xxx10000011100100101 00000001 # shr c, bp\n0xxx10000011100100110 00000001 # shr c, sp\n0xxx10000011100110000 00000001 # shr d, a\n0xxx10000011100110001 00000001 # shr d, b\n0xxx10000011100110010 00000001 # shr d, c\n0xxx10000011100110011 00000001 # shr d, d\n0xxx10000011100110100 00000001 # shr d, e\n0xxx10000011100110101 00000001 # shr d, bp\n0xxx10000011100110110 00000001 # shr d, sp\n0xxx10000011101000000 00000001 # shr e, a\n0xxx10000011101000001 00000001 # shr e, b\n0xxx10000011101000010 00000001 # shr e, c\n0xxx10000011101000011 00000001 # shr e, d\n0xxx10000011101000100 00000001 # shr e, e\n0xxx10000011101000101 00000001 # shr e, bp\n0xxx10000011101000110 00000001 # shr e, sp\n0xxx10000011101010000 00000001 # shr bp, a\n0xxx10000011101010001 00000001 # shr bp, b\n0xxx10000011101010010 00000001 # shr bp, c\n0xxx10000011101010011 00000001 # shr bp, d\n0xxx10000011101010100 00000001 # shr bp, e\n0xxx10000011101010101 00000001 # shr bp, bp\n0xxx10000011101010110 00000001 # shr bp, sp\n0xxx10000011101100000 00000001 # shr sp, a\n0xxx10000011101100001 00000001 # shr sp, b\n0xxx10000011101100010 00000001 # shr sp, c\n0xxx10000011101100011 00000001 # shr sp, d\n0xxx10000011101100100 00000001 # shr sp, e\n0xxx10000011101100101 00000001 # shr sp, bp\n0xxx10000011101100110 00000001 # shr sp, sp\n0xxx10000000000001111 00000001 # add a, opd\n0xxx10000000000011111 00000001 # add b, opd\n0xxx10000000000101111 00000001 # add c, opd\n0xxx10000000000111111 00000001 # add d, opd\n0xxx10000000001001111 00000001 # add e, opd\n0xxx10000000001011111 00000001 # add bp, opd\n0xxx10000000001101111 00000001 # add sp, opd\n0xxx10000000100001111 00000001 # sub a, opd\n0xxx10000000100011111 00000001 # sub b, opd\n0xxx10000000100101111 00000001 # sub c, opd\n0xxx10000000100111111 00000001 # sub d, opd\n0xxx10000000101001111 00000001 # sub e, opd\n0xxx10000000101011111 00000001 # sub bp, opd\n0xxx10000000101101111 00000001 # sub sp, opd\n0xxx10000001000001111 00000001 # mul a, opd\n0xxx10000001000011111 00000001 # mul b, opd\n0xxx10000001000101111 00000001 # mul c, opd\n0xxx10000001000111111 00000001 # mul d, opd\n0xxx10000001001001111 00000001 # mul e, opd\n0xxx10000001001011111 00000001 # mul bp, opd\n0xxx10000001001101111 00000001 # mul sp, opd\n0xxx10000001100001111 00000001 # and a, opd\n0xxx10000001100011111 00000001 # and b, opd\n0xxx10000001100101111 00000001 # and c, opd\n0xxx10000001100111111 00000001 # and d, opd\n0xxx10000001101001111 00000001 # and e, opd\n0xxx10000001101011111 00000001 # and bp, opd\n0xxx10000001101101111 00000001 # and sp, opd\n0xxx10000010000001111 00000001 # or a, opd\n0xxx10000010000011111 00000001 # or b, opd\n0xxx10000010000101111 00000001 # or c, opd\n0xxx10000010000111111 00000001 # or d, opd\n0xxx10000010001001111 00000001 # or e, opd\n0xxx10000010001011111 00000001 # or bp, opd\n0xxx10000010001101111 00000001 # or sp, opd\n0xxx10000011000001111 00000001 # xor a, opd\n0xxx10000011000011111 00000001 # xor b, opd\n0xxx10000011000101111 00000001 # xor c, opd\n0xxx10000011000111111 00000001 # xor d, opd\n0xxx10000011001001111 00000001 # xor e, opd\n0xxx10000011001011111 00000001 # xor bp, opd\n0xxx10000011001101111 00000001 # xor sp, opd\n0xxx10000011100001111 00000001 # shr a, opd\n0xxx10000011100011111 00000001 # shr b, opd\n0xxx10000011100101111 00000001 # shr c, opd\n0xxx10000011100111111 00000001 # shr d, opd\n0xxx10000011101001111 00000001 # shr e, opd\n0xxx10000011101011111 00000001 # shr bp, opd\n0xxx10000011101101111 00000001 # shr sp, opd\n0xxx10000000000001001 00000001 # add a, [memaddr+opd]\n0xxx10000000000011001 00000001 # add b, [memaddr+opd]\n0xxx10000000000101001 00000001 # add c, [memaddr+opd]\n0xxx10000000000111001 00000001 # add d, [memaddr+opd]\n0xxx10000000001001001 00000001 # add e, [memaddr+opd]\n0xxx10000000001011001 00000001 # add bp, [memaddr+opd]\n0xxx10000000001101001 00000001 # add sp, [memaddr+opd]\n0xxx10000000100001001 00000001 # sub a, [memaddr+opd]\n0xxx10000000100011001 00000001 # sub b, [memaddr+opd]\n0xxx10000000100101001 00000001 # sub c, [memaddr+opd]\n0xxx10000000100111001 00000001 # sub d, [memaddr+opd]\n0xxx10000000101001001 00000001 # sub e, [memaddr+opd]\n0xxx10000000101011001 00000001 # sub bp, [memaddr+opd]\n0xxx10000000101101001 00000001 # sub sp, [memaddr+opd]\n0xxx10000001000001001 00000001 # mul a, [memaddr+opd]\n0xxx10000001000011001 00000001 # mul b, [memaddr+opd]\n0xxx10000001000101001 00000001 # mul c, [memaddr+opd]\n0xxx10000001000111001 00000001 # mul d, [memaddr+opd]\n0xxx10000001001001001 00000001 # mul e, [memaddr+opd]\n0xxx10000001001011001 00000001 # mul bp, [memaddr+opd]\n0xxx10000001001101001 00000001 # mul sp, [memaddr+opd]\n0xxx10000001100001001 00000001 # and a, [memaddr+opd]\n0xxx10000001100011001 00000001 # and b, [memaddr+opd]\n0xxx10000001100101001 00000001 # and c, [memaddr+opd]\n0xxx10000001100111001 00000001 # and d, [memaddr+opd]\n0xxx10000001101001001 00000001 # and e, [memaddr+opd]\n0xxx10000001101011001 00000001 # and bp, [memaddr+opd]\n0xxx10000001101101001 00000001 # and sp, [memaddr+opd]\n0xxx10000010000001001 00000001 # or a, [memaddr+opd]\n0xxx10000010000011001 00000001 # or b, [memaddr+opd]\n0xxx10000010000101001 00000001 # or c, [memaddr+opd]\n0xxx10000010000111001 00000001 # or d, [memaddr+opd]\n0xxx10000010001001001 00000001 # or e, [memaddr+opd]\n0xxx10000010001011001 00000001 # or bp, [memaddr+opd]\n0xxx10000010001101001 00000001 # or sp, [memaddr+opd]\n0xxx10000011000001001 00000001 # xor a, [memaddr+opd]\n0xxx10000011000011001 00000001 # xor b, [memaddr+opd]\n0xxx10000011000101001 00000001 # xor c, [memaddr+opd]\n0xxx10000011000111001 00000001 # xor d, [memaddr+opd]\n0xxx10000011001001001 00000001 # xor e, [memaddr+opd]\n0xxx10000011001011001 00000001 # xor bp, [memaddr+opd]\n0xxx10000011001101001 00000001 # xor sp, [memaddr+opd]\n0xxx10000011100001001 00000001 # shr a, [memaddr+opd]\n0xxx10000011100011001 00000001 # shr b, [memaddr+opd]\n0xxx10000011100101001 00000001 # shr c, [memaddr+opd]\n0xxx10000011100111001 00000001 # shr d, [memaddr+opd]\n0xxx10000011101001001 00000001 # shr e, [memaddr+opd]\n0xxx10000011101011001 00000001 # shr bp, [memaddr+opd]\n0xxx10000011101101001 00000001 # shr sp, [memaddr+opd]\n0xxx10000000010111111 00000001 # add memval,opd\n0xxx10000010100001111 00000001 # not a\n0xxx10000010100011111 00000001 # not b\n0xxx10000010100101111 00000001 # not c\n0xxx10000010100111111 00000001 # not d\n0xxx10000010101001111 00000001 # not e\n0xxx10000010101011111 00000001 # not bp\n0xxx10000010101101111 00000001 # not sp\n0xxx10000100000000000 00000001 # mov a, a\n0xxx10000100000000001 00000001 # mov a, b\n0xxx10000100000000010 00000001 # mov a, c\n0xxx10000100000000011 00000001 # mov a, d\n0xxx10000100000000100 00000001 # mov a, e\n0xxx10000100000000101 00000001 # mov a, bp\n0xxx10000100000000110 00000001 # mov a, sp\n0xxx10000100000010000 00000001 # mov b, a\n0xxx10000100000010001 00000001 # mov b, b\n0xxx10000100000010010 00000001 # mov b, c\n0xxx10000100000010011 00000001 # mov b, d\n0xxx10000100000010100 00000001 # mov b, e\n0xxx10000100000010101 00000001 # mov b, bp\n0xxx10000100000010110 00000001 # mov b, sp\n0xxx10000100000100000 00000001 # mov c, a\n0xxx10000100000100001 00000001 # mov c, b\n0xxx10000100000100010 00000001 # mov c, c\n0xxx10000100000100011 00000001 # mov c, d\n0xxx10000100000100100 00000001 # mov c, e\n0xxx10000100000100101 00000001 # mov c, bp\n0xxx10000100000100110 00000001 # mov c, sp\n0xxx10000100000110000 00000001 # mov d, a\n0xxx10000100000110001 00000001 # mov d, b\n0xxx10000100000110010 00000001 # mov d, c\n0xxx10000100000110011 00000001 # mov d, d\n0xxx10000100000110100 00000001 # mov d, e\n0xxx10000100000110101 00000001 # mov d, bp\n0xxx10000100000110110 00000001 # mov d, sp\n0xxx10000100001000000 00000001 # mov e, a\n0xxx10000100001000001 00000001 # mov e, b\n0xxx10000100001000010 00000001 # mov e, c\n0xxx10000100001000011 00000001 # mov e, d\n0xxx10000100001000100 00000001 # mov e, e\n0xxx10000100001000101 00000001 # mov e, bp\n0xxx10000100001000110 00000001 # mov e, sp\n0xxx10000100001010000 00000001 # mov bp, a\n0xxx10000100001010001 00000001 # mov bp, b\n0xxx10000100001010010 00000001 # mov bp, c\n0xxx10000100001010011 00000001 # mov bp, d\n0xxx10000100001010100 00000001 # mov bp, e\n0xxx10000100001010101 00000001 # mov bp, bp\n0xxx10000100001010110 00000001 # mov bp, sp\n0xxx10000100001100000 00000001 # mov sp, a\n0xxx10000100001100001 00000001 # mov sp, b\n0xxx10000100001100010 00000001 # mov sp, c\n0xxx10000100001100011 00000001 # mov sp, d\n0xxx10000100001100100 00000001 # mov sp, e\n0xxx10000100001100101 00000001 # mov sp, bp\n0xxx10000100001100110 00000001 # mov sp, sp\n0xxx10000100000001001 00000001 # mov a, [memaddr+opd]\n0xxx10000100000011001 00000001 # mov b, [memaddr+opd]\n0xxx10000100000101001 00000001 # mov c, [memaddr+opd]\n0xxx10000100000111001 00000001 # mov d, [memaddr+opd]\n0xxx10000100001001001 00000001 # mov e, [memaddr+opd]\n0xxx10000100001011001 00000001 # mov bp, [memaddr+opd]\n0xxx10000100001101001 00000001 # mov sp, [memaddr+opd]\n0xxx10000100010111001 00000001 # mov memval, [memaddr+opd]\n0xxx10000100010100000 00000001 # mov memaddr,a\n0xxx10000100010100001 00000001 # mov memaddr,b\n0xxx10000100010100010 00000001 # mov memaddr,c\n0xxx10000100010100011 00000001 # mov memaddr,d\n0xxx10000100010100100 00000001 # mov memaddr,e\n0xxx10000100010100101 00000001 # mov memaddr,bp\n0xxx10000100010100110 00000001 # mov memaddr,sp\n0xxx10000100010110000 00000001 # mov memval,a\n0xxx10000100010110001 00000001 # mov memval,b\n0xxx10000100010110010 00000001 # mov memval,c\n0xxx10000100010110011 00000001 # mov memval,d\n0xxx10000100010110100 00000001 # mov memval,e\n0xxx10000100010110101 00000001 # mov memval,bp\n0xxx10000100010110110 00000001 # mov memval,sp\n0xxx10000100000001011 00000001 # mov a,memval\n0xxx10000100000011011 00000001 # mov b,memval\n0xxx10000100000101011 00000001 # mov c,memval\n0xxx10000100000111011 00000001 # mov d,memval\n0xxx10000100001001011 00000001 # mov e,memval\n0xxx10000100001011011 00000001 # mov bp,memval\n0xxx10000100001101011 00000001 # mov sp,memval\n0xxx10000100010101010 00000001 # mov [memaddr+opd],memval\n0xxx10000100010101111 00000001 # mov memaddr, opd\n0xxx10000100010111111 00000001 # mov memval, opd\n0xxx10000100000001111 00000001 # mov a, opd\n0xxx10000100000011111 00000001 # mov b, opd\n0xxx10000100000101111 00000001 # mov c, opd\n0xxx10000100000111111 00000001 # mov d, opd\n0xxx10000100001001111 00000001 # mov e, opd\n0xxx10000100001011111 00000001 # mov bp, opd\n0xxx10000100001101111 00000001 # mov sp, opd\n0xxx10000100100001111 00000001 # in a\n0xxx10000100100011111 00000001 # in b\n0xxx10000100100101111 00000001 # in c\n0xxx10000100100111111 00000001 # in d\n0xxx10000100101001111 00000001 # in e\n0xxx10000100101011111 00000001 # in bp\n0xxx10000100101101111 00000001 # in sp\n0xxx10000101000001111 00000001 # out a\n0xxx10000101000011111 00000001 # out b\n0xxx10000101000101111 00000001 # out c\n0xxx10000101000111111 00000001 # out d\n0xxx10000101001001111 00000001 # out e\n0xxx10000101001011111 00000001 # out bp\n0xxx10000101001101111 00000001 # out sp\n0xxx10000101011111111 00000001 # out opd\n0xxx10001001000000000 00000001 # cmp a, a\n0xxx10001001000000001 00000001 # cmp a, b\n0xxx10001001000000010 00000001 # cmp a, c\n0xxx10001001000000011 00000001 # cmp a, d\n0xxx10001001000000100 00000001 # cmp a, e\n0xxx10001001000000101 00000001 # cmp a, bp\n0xxx10001001000000110 00000001 # cmp a, sp\n0xxx10001001000010000 00000001 # cmp b, a\n0xxx10001001000010001 00000001 # cmp b, b\n0xxx10001001000010010 00000001 # cmp b, c\n0xxx10001001000010011 00000001 # cmp b, d\n0xxx10001001000010100 00000001 # cmp b, e\n0xxx10001001000010101 00000001 # cmp b, bp\n0xxx10001001000010110 00000001 # cmp b, sp\n0xxx10001001000100000 00000001 # cmp c, a\n0xxx10001001000100001 00000001 # cmp c, b\n0xxx10001001000100010 00000001 # cmp c, c\n0xxx10001001000100011 00000001 # cmp c, d\n0xxx10001001000100100 00000001 # cmp c, e\n0xxx10001001000100101 00000001 # cmp c, bp\n0xxx10001001000100110 00000001 # cmp c, sp\n0xxx10001001000110000 00000001 # cmp d, a\n0xxx10001001000110001 00000001 # cmp d, b\n0xxx10001001000110010 00000001 # cmp d, c\n0xxx10001001000110011 00000001 # cmp d, d\n0xxx10001001000110100 00000001 # cmp d, e\n0xxx10001001000110101 00000001 # cmp d, bp\n0xxx10001001000110110 00000001 # cmp d, sp\n0xxx10001001001000000 00000001 # cmp e, a\n0xxx10001001001000001 00000001 # cmp e, b\n0xxx10001001001000010 00000001 # cmp e, c\n0xxx10001001001000011 00000001 # cmp e, d\n0xxx10001001001000100 00000001 # cmp e, e\n0xxx10001001001000101 00000001 # cmp e, bp\n0xxx10001001001000110 00000001 # cmp e, sp\n0xxx10001001001010000 00000001 # cmp bp, a\n0xxx10001001001010001 00000001 # cmp bp, b\n0xxx10001001001010010 00000001 # cmp bp, c\n0xxx10001001001010011 00000001 # cmp bp, d\n0xxx10001001001010100 00000001 # cmp bp, e\n0xxx10001001001010101 00000001 # cmp bp, bp\n0xxx10001001001010110 00000001 # cmp bp, sp\n0xxx10001001001100000 00000001 # cmp sp, a\n0xxx10001001001100001 00000001 # cmp sp, b\n0xxx10001001001100010 00000001 # cmp sp, c\n0xxx10001001001100011 00000001 # cmp sp, d\n0xxx10001001001100100 00000001 # cmp sp, e\n0xxx10001001001100101 00000001 # cmp sp, bp\n0xxx10001001001100110 00000001 # cmp sp, sp\n0xxx10001001000001111 00000001 # cmp a, opd\n0xxx10001001000011111 00000001 # cmp b, opd\n0xxx10001001000101111 00000001 # cmp c, opd\n0xxx10001001000111111 00000001 # cmp d, opd\n0xxx10001001001001111 00000001 # cmp e, opd\n0xxx10001001001011111 00000001 # cmp bp, opd\n0xxx10001001001101111 00000001 # cmp sp, opd\n0xxx10001000110111111 00000001 # jmp memval\n00xx10000101100001111 00000001 # jnc a (Taken)\n00xx10000101100011111 00000001 # jnc b (Taken)\n00xx10000101100101111 00000001 # jnc c (Taken)\n00xx10000101100111111 00000001 # jnc d (Taken)\n00xx10000101101001111 00000001 # jnc e (Taken)\n00xx10000101101011111 00000001 # jnc bp (Taken)\n00xx10000101101101111 00000001 # jnc sp (Taken)\n01xx10000101100001111 00000001 # jnc a (Skip)\n01xx10000101100011111 00000001 # jnc b (Skip)\n01xx10000101100101111 00000001 # jnc c (Skip)\n01xx10000101100111111 00000001 # jnc d (Skip)\n01xx10000101101001111 00000001 # jnc e (Skip)\n01xx10000101101011111 00000001 # jnc bp (Skip)\n01xx10000101101101111 00000001 # jnc sp (Skip)\n01xx10000110000001111 00000001 # jc a (Taken)\n01xx10000110000011111 00000001 # jc b (Taken)\n01xx10000110000101111 00000001 # jc c (Taken)\n01xx10000110000111111 00000001 # jc d (Taken)\n01xx10000110001001111 00000001 # jc e (Taken)\n01xx10000110001011111 00000001 # jc bp (Taken)\n01xx10000110001101111 00000001 # jc sp (Taken)\n00xx10000110000001111 00000001 # jc a (Skip)\n00xx10000110000011111 00000001 # jc b (Skip)\n00xx10000110000101111 00000001 # jc c (Skip)\n00xx10000110000111111 00000001 # jc d (Skip)\n00xx10000110001001111 00000001 # jc e (Skip)\n00xx10000110001011111 00000001 # jc bp (Skip)\n00xx10000110001101111 00000001 # jc sp (Skip)\n0x0x10000110100001111 00000001 # jnz a (Taken)\n0x0x10000110100011111 00000001 # jnz b (Taken)\n0x0x10000110100101111 00000001 # jnz c (Taken)\n0x0x10000110100111111 00000001 # jnz d (Taken)\n0x0x10000110101001111 00000001 # jnz e (Taken)\n0x0x10000110101011111 00000001 # jnz bp (Taken)\n0x0x10000110101101111 00000001 # jnz sp (Taken)\n0x1x10000110100001111 00000001 # jnz a (Skip)\n0x1x10000110100011111 00000001 # jnz b (Skip)\n0x1x10000110100101111 00000001 # jnz c (Skip)\n0x1x10000110100111111 00000001 # jnz d (Skip)\n0x1x10000110101001111 00000001 # jnz e (Skip)\n0x1x10000110101011111 00000001 # jnz bp (Skip)\n0x1x10000110101101111 00000001 # jnz sp (Skip)\n0x1x10000111000001111 00000001 # jz a (Taken)\n0x1x10000111000011111 00000001 # jz b (Taken)\n0x1x10000111000101111 00000001 # jz c (Taken)\n0x1x10000111000111111 00000001 # jz d (Taken)\n0x1x10000111001001111 00000001 # jz e (Taken)\n0x1x10000111001011111 00000001 # jz bp (Taken)\n0x1x10000111001101111 00000001 # jz sp (Taken)\n0x0x10000111000001111 00000001 # jz a (Skip)\n0x0x10000111000011111 00000001 # jz b (Skip)\n0x0x10000111000101111 00000001 # jz c (Skip)\n0x0x10000111000111111 00000001 # jz d (Skip)\n0x0x10000111001001111 00000001 # jz e (Skip)\n0x0x10000111001011111 00000001 # jz bp (Skip)\n0x0x10000111001101111 00000001 # jz sp (Skip)\n0xx010000111100001111 00000001 # jns a (Taken)\n0xx010000111100011111 00000001 # jns b (Taken)\n0xx010000111100101111 00000001 # jns c (Taken)\n0xx010000111100111111 00000001 # jns d (Taken)\n0xx010000111101001111 00000001 # jns e (Taken)\n0xx010000111101011111 00000001 # jns bp (Taken)\n0xx010000111101101111 00000001 # jns sp (Taken)\n0xx110000111100001111 00000001 # jns a (Skip)\n0xx110000111100011111 00000001 # jns b (Skip)\n0xx110000111100101111 00000001 # jns c (Skip)\n0xx110000111100111111 00000001 # jns d (Skip)\n0xx110000111101001111 00000001 # jns e (Skip)\n0xx110000111101011111 00000001 # jns bp (Skip)\n0xx110000111101101111 00000001 # jns sp (Skip)\n0xx110001000000001111 00000001 # js a (Taken)\n0xx110001000000011111 00000001 # js b (Taken)\n0xx110001000000101111 00000001 # js c (Taken)\n0xx110001000000111111 00000001 # js d (Taken)\n0xx110001000001001111 00000001 # js e (Taken)\n0xx110001000001011111 00000001 # js bp (Taken)\n0xx110001000001101111 00000001 # js sp (Taken)\n0xx010001000000001111 00000001 # js a (Skip)\n0xx010001000000011111 00000001 # js b (Skip)\n0xx010001000000101111 00000001 # js c (Skip)\n0xx010001000000111111 00000001 # js d (Skip)\n0xx010001000001001111 00000001 # js e (Skip)\n0xx010001000001011111 00000001 # js bp (Skip)\n0xx010001000001101111 00000001 # js sp (Skip)\n0xxx10001000100001111 00000001 # jmp a\n0xxx10001000100011111 00000001 # jmp b\n0xxx10001000100101111 00000001 # jmp c\n0xxx10001000100111111 00000001 # jmp d\n0xxx10001000101001111 00000001 # jmp e\n0xxx10001000101011111 00000001 # jmp bp\n0xxx10001000101101111 00000001 # jmp sp\n0x1x10001011000001111 00000001 # je a (Taken)\n0x1x10001011000011111 00000001 # je b (Taken)\n0x1x10001011000101111 00000001 # je c (Taken)\n0x1x10001011000111111 00000001 # je d (Taken)\n0x1x10001011001001111 00000001 # je e (Taken)\n0x1x10001011001011111 00000001 # je bp (Taken)\n0x1x10001011001101111 00000001 # je sp (Taken)\n0x0x10001011000001111 00000001 # je a (Skip)\n0x0x10001011000011111 00000001 # je b (Skip)\n0x0x10001011000101111 00000001 # je c (Skip)\n0x0x10001011000111111 00000001 # je d (Skip)\n0x0x10001011001001111 00000001 # je e (Skip)\n0x0x10001011001011111 00000001 # je bp (Skip)\n0x0x10001011001101111 00000001 # je sp (Skip)\n0x0x10001011100001111 00000001 # jne a(Taken)\n0x0x10001011100011111 00000001 # jne b(Taken)\n0x0x10001011100101111 00000001 # jne c(Taken)\n0x0x10001011100111111 00000001 # jne d(Taken)\n0x0x10001011101001111 00000001 # jne e(Taken)\n0x0x10001011101011111 00000001 # jne bp(Taken)\n0x0x10001011101101111 00000001 # jne sp(Taken)\n0x1x10001011100001111 00000001 # jne a(Skip)\n0x1x10001011100011111 00000001 # jne b(Skip)\n0x1x10001011100101111 00000001 # jne c(Skip)\n0x1x10001011100111111 00000001 # jne d(Skip)\n0x1x10001011101001111 00000001 # jne e(Skip)\n0x1x10001011101011111 00000001 # jne bp(Skip)\n0x1x10001011101101111 00000001 # jne sp(Skip)\n0x0010001100000001111 00000001 # ja a (Taken)\n0x0010001100000011111 00000001 # ja b (Taken)\n0x0010001100000101111 00000001 # ja c (Taken)\n0x0010001100000111111 00000001 # ja d (Taken)\n0x0010001100001001111 00000001 # ja e (Taken)\n0x0010001100001011111 00000001 # ja bp (Taken)\n0x0010001100001101111 00000001 # ja sp (Taken)\n0xxx10001100000001111 00000001 # ja a (Skip)\n0xxx10001100000011111 00000001 # ja b (Skip)\n0xxx10001100000101111 00000001 # ja c (Skip)\n0xxx10001100000111111 00000001 # ja d (Skip)\n0xxx10001100001001111 00000001 # ja e (Skip)\n0xxx10001100001011111 00000001 # ja bp (Skip)\n0xxx10001100001101111 00000001 # ja sp (Skip)\n0x0010001100100001111 00000001 # jae a (Taken)\n0x0010001100100011111 00000001 # jae b (Taken)\n0x0010001100100101111 00000001 # jae c (Taken)\n0x0010001100100111111 00000001 # jae d (Taken)\n0x0010001100101001111 00000001 # jae e (Taken)\n0x0010001100101011111 00000001 # jae bp (Taken)\n0x0010001100101101111 00000001 # jae sp (Taken)\n0x1010001100100001111 00000001 # jae a (Taken)\n0x1010001100100011111 00000001 # jae b (Taken)\n0x1010001100100101111 00000001 # jae c (Taken)\n0x1010001100100111111 00000001 # jae d (Taken)\n0x1010001100101001111 00000001 # jae e (Taken)\n0x1010001100101011111 00000001 # jae bp (Taken)\n0x1010001100101101111 00000001 # jae sp (Taken)\n0xxx10001100100001111 00000001 # jae a (Skip)\n0xxx10001100100011111 00000001 # jae b (Skip)\n0xxx10001100100101111 00000001 # jae c (Skip)\n0xxx10001100100111111 00000001 # jae d (Skip)\n0xxx10001100101001111 00000001 # jae e (Skip)\n0xxx10001100101011111 00000001 # jae bp (Skip)\n0xxx10001100101101111 00000001 # jae sp (Skip)\n0x0110001101000001111 00000001 # jl a (Taken)\n0x0110001101000011111 00000001 # jl b (Taken)\n0x0110001101000101111 00000001 # jl c (Taken)\n0x0110001101000111111 00000001 # jl d (Taken)\n0x0110001101001001111 00000001 # jl e (Taken)\n0x0110001101001011111 00000001 # jl bp (Taken)\n0x0110001101001101111 00000001 # jl sp (Taken)\n0xxx10001101000001111 00000001 # jl a (Skip)\n0xxx10001101000011111 00000001 # jl b (Skip)\n0xxx10001101000101111 00000001 # jl c (Skip)\n0xxx10001101000111111 00000001 # jl d (Skip)\n0xxx10001101001001111 00000001 # jl e (Skip)\n0xxx10001101001011111 00000001 # jl bp (Skip)\n0xxx10001101001101111 00000001 # jl sp (Skip)\n0x0110001101100001111 00000001 # jle a (Taken)\n0x0110001101100011111 00000001 # jle b (Taken)\n0x0110001101100101111 00000001 # jle c (Taken)\n0x0110001101100111111 00000001 # jle d (Taken)\n0x0110001101101001111 00000001 # jle e (Taken)\n0x0110001101101011111 00000001 # jle bp (Taken)\n0x0110001101101101111 00000001 # jle sp (Taken)\n0x1010001101100001111 00000001 # jle a (Taken)\n0x1010001101100011111 00000001 # jle b (Taken)\n0x1010001101100101111 00000001 # jle c (Taken)\n0x1010001101100111111 00000001 # jle d (Taken)\n0x1010001101101001111 00000001 # jle e (Taken)\n0x1010001101101011111 00000001 # jle bp (Taken)\n0x1010001101101101111 00000001 # jle sp (Taken)\n0xxx10001101100001111 00000001 # jle a (Skip)\n0xxx10001101100011111 00000001 # jle b (Skip)\n0xxx10001101100101111 00000001 # jle c (Skip)\n0xxx10001101100111111 00000001 # jle d (Skip)\n0xxx10001101101001111 00000001 # jle e (Skip)\n0xxx10001101101011111 00000001 # jle bp (Skip)\n0xxx10001101101101111 00000001 # jle sp (Skip)\n0xxx10001110111111111 00000001 # setinaddr opd\n0xxx10001110100001111 00000001 # setinaddr a\n0xxx10001110100011111 00000001 # setinaddr b\n0xxx10001110100101111 00000001 # setinaddr c\n0xxx10001110100111111 00000001 # setinaddr d\n0xxx10001110101001111 00000001 # setinaddr e\n0xxx10001110101011111 00000001 # setinaddr bp\n0xxx10001110101101111 00000001 # setinaddr sp\n0xxx10001111011111111 00000001 # setoutaddr opd\n0xxx10001111000001111 00000001 # setoutaddr a\n0xxx10001111000011111 00000001 # setoutaddr b\n0xxx10001111000101111 00000001 # setoutaddr c\n0xxx10001111000111111 00000001 # setoutaddr d\n0xxx10001111001001111 00000001 # setoutaddr e\n0xxx10001111001011111 00000001 # setoutaddr bp\n0xxx10001111001101111 00000001 # setoutaddr sp\n0xxx10001111111111111 00000010 # setreadburstmode\n0xxx10010000011111111 00000010 # clearreadburstmode\n0xxx10010000111111111 00000010 # setzerobufferpointer\n0xxx10010001011111111 00000010 # incbufferpointer\n0xxx10010001111111111 00000001 # setbuffersize opd\n0xxx10010001100001111 00000001 # setbuffersize a\n0xxx10010001100011111 00000001 # setbuffersize b\n0xxx10010001100101111 00000001 # setbuffersize c\n0xxx10010001100111111 00000001 # setbuffersize d\n0xxx10010001101001111 00000001 # setbuffersize e\n0xxx10010001101011111 00000001 # setbuffersize bp\n0xxx10010001101101111 00000001 # setbuffersize sp\n0xxx10010010011111111 00000001 # buffertomemval\n0xxx10010010111111111 00000010 # setintdisableflag\n0xxx10010011011111111 00000010 # clearintdisableflag\n0xxx10001110011111111 00000111 # intret\n0xxx10010011111111111 00001010 # syscall\n0xxx10010101011111111 00000110 # sysret\n0xxx10010100011111111 00001010 # usercall\n0xxx10010100111111111 00000110 # userret\n1xxxxxxxxxxxxxxxxxxxx 00000000 # Interrupt\nxxxxxxxxxxxxxxxxxxxxx 11111111 # Undefined Instruction")) Instruction_Classifier (
    .in({and_3_out[20], carry_flag, zero_flag, sign_flag, 1'b1, IR_opcode_q}), .out(State_Register_q[15:8]));
  PLA #(.in_width(8), .out_width(1), .\table ("00000000 1 # add\n00000001 1 # sub\n00000010 1 # mul\n00000011 1 # and\n00000100 1 # or\n00000101 1 # not\n00000110 1 # xor\n00000111 1 # shr\n00001000 1 # mov\n00001001 0 # in\n00001010 0 # out\n00001011 1 # jnc\n00001100 1 # jc\n00001101 1 # jnz\n00001110 1 # jz\n00001111 1 # jns\n00010000 1 # js\n00010001 1 # jmp\n00010010 1 # cmp\n00010011 1 # hlt\n00010100 1 # nop\n00010101 1 # lpc\n00010110 1 # je\n00010111 1 # jne\n00011000 1 # ja\n00011001 1 # jae\n00011010 1 # jl\n00011011 1 # jle\n00011100 0 # intret\n00011101 0 # setinaddr\n00011110 0 # setoutaddr\n00011111 0 # setreadburstmode\n00100000 0 # clearreadburstmode\n00100001 0 # setzerobufferpointer\n00100010 0 # incbufferpointer\n00100011 0 # setbuffersize\n00100100 0 # buffertomemval\n00100101 0 # setintdisableflag\n00100110 0 # clearintdisableflag\n00100111 1 # syscall\n00101000 0 # usercall\n00101001 1 # userret\n00101010 0 # sysret\nxxxxxxxx 1 # undefined")) Instruction_permission_checker (
    .in(IR_opcode_q[15:8]), .out(Instruction_permission_checker_out));
  or or_5 (or_5_out, comparator_5_eq, comparator_6_eq);
  Multiplexer #(.width(16)) multiplexer_6 (.in0(IR_opd_q), .in1(MOR_q), .out(operand), .sel(Microcode_ROM_data[22]));
  PLA #(.in_width(21), .out_width(16), .\table ("0xxx0xxxxxxxxxxxxxxxx 0000000000000000 # IE=0 (during fetch)\n00xx10000101111111111 0000000000000001 # jnc opd (Taken)\n01xx10000101111111111 0000000000000010 # jnc opd (Skip)\n01xx10000110011111111 0000000000000011 # jc opd (Taken)\n00xx10000110011111111 0000000000000100 # jc opd (Skip)\n0x0x10000110111111111 0000000000000101 # jnz opd (Taken)\n0x1x10000110111111111 0000000000000110 # jnz opd (Skip)\n0x1x10000111011111111 0000000000000111 # jz opd (Taken)\n0x0x10000111011111111 0000000000001000 # jz opd (Skip)\n0xx010000111111111111 0000000000001001 # jns opd (Taken)\n0xx110000111111111111 0000000000001010 # jns opd (Skip)\n0xx110001000011111111 0000000000001011 # js opd (Taken)\n0xx010001000011111111 0000000000001100 # js opd (Skip)\n0xxx10001000111111111 0000000000001101 # jmp opd\n0x1x10001011011111111 0000000000001110 # je opd (Taken)\n0x0x10001011011111111 0000000000001111 # je opd (Skip)\n0x0x10001011111111111 0000000000010000 # jne opd(Taken)\n0x1x10001011111111111 0000000000010001 # jne opd(Skip)\n0x0010001100011111111 0000000000010010 # ja opd (Taken)\n0xxx10001100011111111 0000000000010011 # ja opd (Skip)\n0x0010001100111111111 0000000000010100 # jae opd (Taken)\n0x1010001100111111111 0000000000010101 # jae opd (Taken)\n0xxx10001100111111111 0000000000010110 # jae opd (Skip)\n0x0110001101011111111 0000000000010111 # jl opd (Taken)\n0xxx10001101011111111 0000000000011000 # jl opd (Skip)\n0x0110001101111111111 0000000000011001 # jle opd (Taken)\n0x1010001101111111111 0000000000011010 # jle opd (Taken)\n0xxx10001101111111111 0000000000011011 # jle opd (Skip)\n0xxx10001001111111111 0000000000011100 # hlt\n0xxx10001010011111111 0000000000011101 # nop\n0xxxx1111111111111111 0000000000011110 # invaild\n0xxx10001010111111111 0000000000011111 # lpc\n0xxx10000000000000000 0000000000100000 # add a, a\n0xxx10000000000000001 0000000000100001 # add a, b\n0xxx10000000000000010 0000000000100010 # add a, c\n0xxx10000000000000011 0000000000100011 # add a, d\n0xxx10000000000000100 0000000000100100 # add a, e\n0xxx10000000000000101 0000000000100101 # add a, bp\n0xxx10000000000000110 0000000000100110 # add a, sp\n0xxx10000000000010000 0000000000100111 # add b, a\n0xxx10000000000010001 0000000000101000 # add b, b\n0xxx10000000000010010 0000000000101001 # add b, c\n0xxx10000000000010011 0000000000101010 # add b, d\n0xxx10000000000010100 0000000000101011 # add b, e\n0xxx10000000000010101 0000000000101100 # add b, bp\n0xxx10000000000010110 0000000000101101 # add b, sp\n0xxx10000000000100000 0000000000101110 # add c, a\n0xxx10000000000100001 0000000000101111 # add c, b\n0xxx10000000000100010 0000000000110000 # add c, c\n0xxx10000000000100011 0000000000110001 # add c, d\n0xxx10000000000100100 0000000000110010 # add c, e\n0xxx10000000000100101 0000000000110011 # add c, bp\n0xxx10000000000100110 0000000000110100 # add c, sp\n0xxx10000000000110000 0000000000110101 # add d, a\n0xxx10000000000110001 0000000000110110 # add d, b\n0xxx10000000000110010 0000000000110111 # add d, c\n0xxx10000000000110011 0000000000111000 # add d, d\n0xxx10000000000110100 0000000000111001 # add d, e\n0xxx10000000000110101 0000000000111010 # add d, bp\n0xxx10000000000110110 0000000000111011 # add d, sp\n0xxx10000000001000000 0000000000111100 # add e, a\n0xxx10000000001000001 0000000000111101 # add e, b\n0xxx10000000001000010 0000000000111110 # add e, c\n0xxx10000000001000011 0000000000111111 # add e, d\n0xxx10000000001000100 0000000001000000 # add e, e\n0xxx10000000001000101 0000000001000001 # add e, bp\n0xxx10000000001000110 0000000001000010 # add e, sp\n0xxx10000000001010000 0000000001000011 # add bp, a\n0xxx10000000001010001 0000000001000100 # add bp, b\n0xxx10000000001010010 0000000001000101 # add bp, c\n0xxx10000000001010011 0000000001000110 # add bp, d\n0xxx10000000001010100 0000000001000111 # add bp, e\n0xxx10000000001010101 0000000001001000 # add bp, bp\n0xxx10000000001010110 0000000001001001 # add bp, sp\n0xxx10000000001100000 0000000001001010 # add sp, a\n0xxx10000000001100001 0000000001001011 # add sp, b\n0xxx10000000001100010 0000000001001100 # add sp, c\n0xxx10000000001100011 0000000001001101 # add sp, d\n0xxx10000000001100100 0000000001001110 # add sp, e\n0xxx10000000001100101 0000000001001111 # add sp, bp\n0xxx10000000001100110 0000000001010000 # add sp, sp\n0xxx10000000100000000 0000000001010001 # sub a, a\n0xxx10000000100000001 0000000001010010 # sub a, b\n0xxx10000000100000010 0000000001010011 # sub a, c\n0xxx10000000100000011 0000000001010100 # sub a, d\n0xxx10000000100000100 0000000001010101 # sub a, e\n0xxx10000000100000101 0000000001010110 # sub a, bp\n0xxx10000000100000110 0000000001010111 # sub a, sp\n0xxx10000000100010000 0000000001011000 # sub b, a\n0xxx10000000100010001 0000000001011001 # sub b, b\n0xxx10000000100010010 0000000001011010 # sub b, c\n0xxx10000000100010011 0000000001011011 # sub b, d\n0xxx10000000100010100 0000000001011100 # sub b, e\n0xxx10000000100010101 0000000001011101 # sub b, bp\n0xxx10000000100010110 0000000001011110 # sub b, sp\n0xxx10000000100100000 0000000001011111 # sub c, a\n0xxx10000000100100001 0000000001100000 # sub c, b\n0xxx10000000100100010 0000000001100001 # sub c, c\n0xxx10000000100100011 0000000001100010 # sub c, d\n0xxx10000000100100100 0000000001100011 # sub c, e\n0xxx10000000100100101 0000000001100100 # sub c, bp\n0xxx10000000100100110 0000000001100101 # sub c, sp\n0xxx10000000100110000 0000000001100110 # sub d, a\n0xxx10000000100110001 0000000001100111 # sub d, b\n0xxx10000000100110010 0000000001101000 # sub d, c\n0xxx10000000100110011 0000000001101001 # sub d, d\n0xxx10000000100110100 0000000001101010 # sub d, e\n0xxx10000000100110101 0000000001101011 # sub d, bp\n0xxx10000000100110110 0000000001101100 # sub d, sp\n0xxx10000000101000000 0000000001101101 # sub e, a\n0xxx10000000101000001 0000000001101110 # sub e, b\n0xxx10000000101000010 0000000001101111 # sub e, c\n0xxx10000000101000011 0000000001110000 # sub e, d\n0xxx10000000101000100 0000000001110001 # sub e, e\n0xxx10000000101000101 0000000001110010 # sub e, bp\n0xxx10000000101000110 0000000001110011 # sub e, sp\n0xxx10000000101010000 0000000001110100 # sub bp, a\n0xxx10000000101010001 0000000001110101 # sub bp, b\n0xxx10000000101010010 0000000001110110 # sub bp, c\n0xxx10000000101010011 0000000001110111 # sub bp, d\n0xxx10000000101010100 0000000001111000 # sub bp, e\n0xxx10000000101010101 0000000001111001 # sub bp, bp\n0xxx10000000101010110 0000000001111010 # sub bp, sp\n0xxx10000000101100000 0000000001111011 # sub sp, a\n0xxx10000000101100001 0000000001111100 # sub sp, b\n0xxx10000000101100010 0000000001111101 # sub sp, c\n0xxx10000000101100011 0000000001111110 # sub sp, d\n0xxx10000000101100100 0000000001111111 # sub sp, e\n0xxx10000000101100101 0000000010000000 # sub sp, bp\n0xxx10000000101100110 0000000010000001 # sub sp, sp\n0xxx10000001000000000 0000000010000010 # mul a, a\n0xxx10000001000000001 0000000010000011 # mul a, b\n0xxx10000001000000010 0000000010000100 # mul a, c\n0xxx10000001000000011 0000000010000101 # mul a, d\n0xxx10000001000000100 0000000010000110 # mul a, e\n0xxx10000001000000101 0000000010000111 # mul a, bp\n0xxx10000001000000110 0000000010001000 # mul a, sp\n0xxx10000001000010000 0000000010001001 # mul b, a\n0xxx10000001000010001 0000000010001010 # mul b, b\n0xxx10000001000010010 0000000010001011 # mul b, c\n0xxx10000001000010011 0000000010001100 # mul b, d\n0xxx10000001000010100 0000000010001101 # mul b, e\n0xxx10000001000010101 0000000010001110 # mul b, bp\n0xxx10000001000010110 0000000010001111 # mul b, sp\n0xxx10000001000100000 0000000010010000 # mul c, a\n0xxx10000001000100001 0000000010010001 # mul c, b\n0xxx10000001000100010 0000000010010010 # mul c, c\n0xxx10000001000100011 0000000010010011 # mul c, d\n0xxx10000001000100100 0000000010010100 # mul c, e\n0xxx10000001000100101 0000000010010101 # mul c, bp\n0xxx10000001000100110 0000000010010110 # mul c, sp\n0xxx10000001000110000 0000000010010111 # mul d, a\n0xxx10000001000110001 0000000010011000 # mul d, b\n0xxx10000001000110010 0000000010011001 # mul d, c\n0xxx10000001000110011 0000000010011010 # mul d, d\n0xxx10000001000110100 0000000010011011 # mul d, e\n0xxx10000001000110101 0000000010011100 # mul d, bp\n0xxx10000001000110110 0000000010011101 # mul d, sp\n0xxx10000001001000000 0000000010011110 # mul e, a\n0xxx10000001001000001 0000000010011111 # mul e, b\n0xxx10000001001000010 0000000010100000 # mul e, c\n0xxx10000001001000011 0000000010100001 # mul e, d\n0xxx10000001001000100 0000000010100010 # mul e, e\n0xxx10000001001000101 0000000010100011 # mul e, bp\n0xxx10000001001000110 0000000010100100 # mul e, sp\n0xxx10000001001010000 0000000010100101 # mul bp, a\n0xxx10000001001010001 0000000010100110 # mul bp, b\n0xxx10000001001010010 0000000010100111 # mul bp, c\n0xxx10000001001010011 0000000010101000 # mul bp, d\n0xxx10000001001010100 0000000010101001 # mul bp, e\n0xxx10000001001010101 0000000010101010 # mul bp, bp\n0xxx10000001001010110 0000000010101011 # mul bp, sp\n0xxx10000001001100000 0000000010101100 # mul sp, a\n0xxx10000001001100001 0000000010101101 # mul sp, b\n0xxx10000001001100010 0000000010101110 # mul sp, c\n0xxx10000001001100011 0000000010101111 # mul sp, d\n0xxx10000001001100100 0000000010110000 # mul sp, e\n0xxx10000001001100101 0000000010110001 # mul sp, bp\n0xxx10000001001100110 0000000010110010 # mul sp, sp\n0xxx10000001100000000 0000000010110011 # and a, a\n0xxx10000001100000001 0000000010110100 # and a, b\n0xxx10000001100000010 0000000010110101 # and a, c\n0xxx10000001100000011 0000000010110110 # and a, d\n0xxx10000001100000100 0000000010110111 # and a, e\n0xxx10000001100000101 0000000010111000 # and a, bp\n0xxx10000001100000110 0000000010111001 # and a, sp\n0xxx10000001100010000 0000000010111010 # and b, a\n0xxx10000001100010001 0000000010111011 # and b, b\n0xxx10000001100010010 0000000010111100 # and b, c\n0xxx10000001100010011 0000000010111101 # and b, d\n0xxx10000001100010100 0000000010111110 # and b, e\n0xxx10000001100010101 0000000010111111 # and b, bp\n0xxx10000001100010110 0000000011000000 # and b, sp\n0xxx10000001100100000 0000000011000001 # and c, a\n0xxx10000001100100001 0000000011000010 # and c, b\n0xxx10000001100100010 0000000011000011 # and c, c\n0xxx10000001100100011 0000000011000100 # and c, d\n0xxx10000001100100100 0000000011000101 # and c, e\n0xxx10000001100100101 0000000011000110 # and c, bp\n0xxx10000001100100110 0000000011000111 # and c, sp\n0xxx10000001100110000 0000000011001000 # and d, a\n0xxx10000001100110001 0000000011001001 # and d, b\n0xxx10000001100110010 0000000011001010 # and d, c\n0xxx10000001100110011 0000000011001011 # and d, d\n0xxx10000001100110100 0000000011001100 # and d, e\n0xxx10000001100110101 0000000011001101 # and d, bp\n0xxx10000001100110110 0000000011001110 # and d, sp\n0xxx10000001101000000 0000000011001111 # and e, a\n0xxx10000001101000001 0000000011010000 # and e, b\n0xxx10000001101000010 0000000011010001 # and e, c\n0xxx10000001101000011 0000000011010010 # and e, d\n0xxx10000001101000100 0000000011010011 # and e, e\n0xxx10000001101000101 0000000011010100 # and e, bp\n0xxx10000001101000110 0000000011010101 # and e, sp\n0xxx10000001101010000 0000000011010110 # and bp, a\n0xxx10000001101010001 0000000011010111 # and bp, b\n0xxx10000001101010010 0000000011011000 # and bp, c\n0xxx10000001101010011 0000000011011001 # and bp, d\n0xxx10000001101010100 0000000011011010 # and bp, e\n0xxx10000001101010101 0000000011011011 # and bp, bp\n0xxx10000001101010110 0000000011011100 # and bp, sp\n0xxx10000001101100000 0000000011011101 # and sp, a\n0xxx10000001101100001 0000000011011110 # and sp, b\n0xxx10000001101100010 0000000011011111 # and sp, c\n0xxx10000001101100011 0000000011100000 # and sp, d\n0xxx10000001101100100 0000000011100001 # and sp, e\n0xxx10000001101100101 0000000011100010 # and sp, bp\n0xxx10000001101100110 0000000011100011 # and sp, sp\n0xxx10000010000000000 0000000011100100 # or a, a\n0xxx10000010000000001 0000000011100101 # or a, b\n0xxx10000010000000010 0000000011100110 # or a, c\n0xxx10000010000000011 0000000011100111 # or a, d\n0xxx10000010000000100 0000000011101000 # or a, e\n0xxx10000010000000101 0000000011101001 # or a, bp\n0xxx10000010000000110 0000000011101010 # or a, sp\n0xxx10000010000010000 0000000011101011 # or b, a\n0xxx10000010000010001 0000000011101100 # or b, b\n0xxx10000010000010010 0000000011101101 # or b, c\n0xxx10000010000010011 0000000011101110 # or b, d\n0xxx10000010000010100 0000000011101111 # or b, e\n0xxx10000010000010101 0000000011110000 # or b, bp\n0xxx10000010000010110 0000000011110001 # or b, sp\n0xxx10000010000100000 0000000011110010 # or c, a\n0xxx10000010000100001 0000000011110011 # or c, b\n0xxx10000010000100010 0000000011110100 # or c, c\n0xxx10000010000100011 0000000011110101 # or c, d\n0xxx10000010000100100 0000000011110110 # or c, e\n0xxx10000010000100101 0000000011110111 # or c, bp\n0xxx10000010000100110 0000000011111000 # or c, sp\n0xxx10000010000110000 0000000011111001 # or d, a\n0xxx10000010000110001 0000000011111010 # or d, b\n0xxx10000010000110010 0000000011111011 # or d, c\n0xxx10000010000110011 0000000011111100 # or d, d\n0xxx10000010000110100 0000000011111101 # or d, e\n0xxx10000010000110101 0000000011111110 # or d, bp\n0xxx10000010000110110 0000000011111111 # or d, sp\n0xxx10000010001000000 0000000100000000 # or e, a\n0xxx10000010001000001 0000000100000001 # or e, b\n0xxx10000010001000010 0000000100000010 # or e, c\n0xxx10000010001000011 0000000100000011 # or e, d\n0xxx10000010001000100 0000000100000100 # or e, e\n0xxx10000010001000101 0000000100000101 # or e, bp\n0xxx10000010001000110 0000000100000110 # or e, sp\n0xxx10000010001010000 0000000100000111 # or bp, a\n0xxx10000010001010001 0000000100001000 # or bp, b\n0xxx10000010001010010 0000000100001001 # or bp, c\n0xxx10000010001010011 0000000100001010 # or bp, d\n0xxx10000010001010100 0000000100001011 # or bp, e\n0xxx10000010001010101 0000000100001100 # or bp, bp\n0xxx10000010001010110 0000000100001101 # or bp, sp\n0xxx10000010001100000 0000000100001110 # or sp, a\n0xxx10000010001100001 0000000100001111 # or sp, b\n0xxx10000010001100010 0000000100010000 # or sp, c\n0xxx10000010001100011 0000000100010001 # or sp, d\n0xxx10000010001100100 0000000100010010 # or sp, e\n0xxx10000010001100101 0000000100010011 # or sp, bp\n0xxx10000010001100110 0000000100010100 # or sp, sp\n0xxx10000011000000000 0000000100010101 # xor a, a\n0xxx10000011000000001 0000000100010110 # xor a, b\n0xxx10000011000000010 0000000100010111 # xor a, c\n0xxx10000011000000011 0000000100011000 # xor a, d\n0xxx10000011000000100 0000000100011001 # xor a, e\n0xxx10000011000000101 0000000100011010 # xor a, bp\n0xxx10000011000000110 0000000100011011 # xor a, sp\n0xxx10000011000010000 0000000100011100 # xor b, a\n0xxx10000011000010001 0000000100011101 # xor b, b\n0xxx10000011000010010 0000000100011110 # xor b, c\n0xxx10000011000010011 0000000100011111 # xor b, d\n0xxx10000011000010100 0000000100100000 # xor b, e\n0xxx10000011000010101 0000000100100001 # xor b, bp\n0xxx10000011000010110 0000000100100010 # xor b, sp\n0xxx10000011000100000 0000000100100011 # xor c, a\n0xxx10000011000100001 0000000100100100 # xor c, b\n0xxx10000011000100010 0000000100100101 # xor c, c\n0xxx10000011000100011 0000000100100110 # xor c, d\n0xxx10000011000100100 0000000100100111 # xor c, e\n0xxx10000011000100101 0000000100101000 # xor c, bp\n0xxx10000011000100110 0000000100101001 # xor c, sp\n0xxx10000011000110000 0000000100101010 # xor d, a\n0xxx10000011000110001 0000000100101011 # xor d, b\n0xxx10000011000110010 0000000100101100 # xor d, c\n0xxx10000011000110011 0000000100101101 # xor d, d\n0xxx10000011000110100 0000000100101110 # xor d, e\n0xxx10000011000110101 0000000100101111 # xor d, bp\n0xxx10000011000110110 0000000100110000 # xor d, sp\n0xxx10000011001000000 0000000100110001 # xor e, a\n0xxx10000011001000001 0000000100110010 # xor e, b\n0xxx10000011001000010 0000000100110011 # xor e, c\n0xxx10000011001000011 0000000100110100 # xor e, d\n0xxx10000011001000100 0000000100110101 # xor e, e\n0xxx10000011001000101 0000000100110110 # xor e, bp\n0xxx10000011001000110 0000000100110111 # xor e, sp\n0xxx10000011001010000 0000000100111000 # xor bp, a\n0xxx10000011001010001 0000000100111001 # xor bp, b\n0xxx10000011001010010 0000000100111010 # xor bp, c\n0xxx10000011001010011 0000000100111011 # xor bp, d\n0xxx10000011001010100 0000000100111100 # xor bp, e\n0xxx10000011001010101 0000000100111101 # xor bp, bp\n0xxx10000011001010110 0000000100111110 # xor bp, sp\n0xxx10000011001100000 0000000100111111 # xor sp, a\n0xxx10000011001100001 0000000101000000 # xor sp, b\n0xxx10000011001100010 0000000101000001 # xor sp, c\n0xxx10000011001100011 0000000101000010 # xor sp, d\n0xxx10000011001100100 0000000101000011 # xor sp, e\n0xxx10000011001100101 0000000101000100 # xor sp, bp\n0xxx10000011001100110 0000000101000101 # xor sp, sp\n0xxx10000011100000000 0000000101000110 # shr a, a\n0xxx10000011100000001 0000000101000111 # shr a, b\n0xxx10000011100000010 0000000101001000 # shr a, c\n0xxx10000011100000011 0000000101001001 # shr a, d\n0xxx10000011100000100 0000000101001010 # shr a, e\n0xxx10000011100000101 0000000101001011 # shr a, bp\n0xxx10000011100000110 0000000101001100 # shr a, sp\n0xxx10000011100010000 0000000101001101 # shr b, a\n0xxx10000011100010001 0000000101001110 # shr b, b\n0xxx10000011100010010 0000000101001111 # shr b, c\n0xxx10000011100010011 0000000101010000 # shr b, d\n0xxx10000011100010100 0000000101010001 # shr b, e\n0xxx10000011100010101 0000000101010010 # shr b, bp\n0xxx10000011100010110 0000000101010011 # shr b, sp\n0xxx10000011100100000 0000000101010100 # shr c, a\n0xxx10000011100100001 0000000101010101 # shr c, b\n0xxx10000011100100010 0000000101010110 # shr c, c\n0xxx10000011100100011 0000000101010111 # shr c, d\n0xxx10000011100100100 0000000101011000 # shr c, e\n0xxx10000011100100101 0000000101011001 # shr c, bp\n0xxx10000011100100110 0000000101011010 # shr c, sp\n0xxx10000011100110000 0000000101011011 # shr d, a\n0xxx10000011100110001 0000000101011100 # shr d, b\n0xxx10000011100110010 0000000101011101 # shr d, c\n0xxx10000011100110011 0000000101011110 # shr d, d\n0xxx10000011100110100 0000000101011111 # shr d, e\n0xxx10000011100110101 0000000101100000 # shr d, bp\n0xxx10000011100110110 0000000101100001 # shr d, sp\n0xxx10000011101000000 0000000101100010 # shr e, a\n0xxx10000011101000001 0000000101100011 # shr e, b\n0xxx10000011101000010 0000000101100100 # shr e, c\n0xxx10000011101000011 0000000101100101 # shr e, d\n0xxx10000011101000100 0000000101100110 # shr e, e\n0xxx10000011101000101 0000000101100111 # shr e, bp\n0xxx10000011101000110 0000000101101000 # shr e, sp\n0xxx10000011101010000 0000000101101001 # shr bp, a\n0xxx10000011101010001 0000000101101010 # shr bp, b\n0xxx10000011101010010 0000000101101011 # shr bp, c\n0xxx10000011101010011 0000000101101100 # shr bp, d\n0xxx10000011101010100 0000000101101101 # shr bp, e\n0xxx10000011101010101 0000000101101110 # shr bp, bp\n0xxx10000011101010110 0000000101101111 # shr bp, sp\n0xxx10000011101100000 0000000101110000 # shr sp, a\n0xxx10000011101100001 0000000101110001 # shr sp, b\n0xxx10000011101100010 0000000101110010 # shr sp, c\n0xxx10000011101100011 0000000101110011 # shr sp, d\n0xxx10000011101100100 0000000101110100 # shr sp, e\n0xxx10000011101100101 0000000101110101 # shr sp, bp\n0xxx10000011101100110 0000000101110110 # shr sp, sp\n0xxx10000000000001111 0000000101110111 # add a, opd\n0xxx10000000000011111 0000000101111000 # add b, opd\n0xxx10000000000101111 0000000101111001 # add c, opd\n0xxx10000000000111111 0000000101111010 # add d, opd\n0xxx10000000001001111 0000000101111011 # add e, opd\n0xxx10000000001011111 0000000101111100 # add bp, opd\n0xxx10000000001101111 0000000101111101 # add sp, opd\n0xxx10000000100001111 0000000101111110 # sub a, opd\n0xxx10000000100011111 0000000101111111 # sub b, opd\n0xxx10000000100101111 0000000110000000 # sub c, opd\n0xxx10000000100111111 0000000110000001 # sub d, opd\n0xxx10000000101001111 0000000110000010 # sub e, opd\n0xxx10000000101011111 0000000110000011 # sub bp, opd\n0xxx10000000101101111 0000000110000100 # sub sp, opd\n0xxx10000001000001111 0000000110000101 # mul a, opd\n0xxx10000001000011111 0000000110000110 # mul b, opd\n0xxx10000001000101111 0000000110000111 # mul c, opd\n0xxx10000001000111111 0000000110001000 # mul d, opd\n0xxx10000001001001111 0000000110001001 # mul e, opd\n0xxx10000001001011111 0000000110001010 # mul bp, opd\n0xxx10000001001101111 0000000110001011 # mul sp, opd\n0xxx10000001100001111 0000000110001100 # and a, opd\n0xxx10000001100011111 0000000110001101 # and b, opd\n0xxx10000001100101111 0000000110001110 # and c, opd\n0xxx10000001100111111 0000000110001111 # and d, opd\n0xxx10000001101001111 0000000110010000 # and e, opd\n0xxx10000001101011111 0000000110010001 # and bp, opd\n0xxx10000001101101111 0000000110010010 # and sp, opd\n0xxx10000010000001111 0000000110010011 # or a, opd\n0xxx10000010000011111 0000000110010100 # or b, opd\n0xxx10000010000101111 0000000110010101 # or c, opd\n0xxx10000010000111111 0000000110010110 # or d, opd\n0xxx10000010001001111 0000000110010111 # or e, opd\n0xxx10000010001011111 0000000110011000 # or bp, opd\n0xxx10000010001101111 0000000110011001 # or sp, opd\n0xxx10000011000001111 0000000110011010 # xor a, opd\n0xxx10000011000011111 0000000110011011 # xor b, opd\n0xxx10000011000101111 0000000110011100 # xor c, opd\n0xxx10000011000111111 0000000110011101 # xor d, opd\n0xxx10000011001001111 0000000110011110 # xor e, opd\n0xxx10000011001011111 0000000110011111 # xor bp, opd\n0xxx10000011001101111 0000000110100000 # xor sp, opd\n0xxx10000011100001111 0000000110100001 # shr a, opd\n0xxx10000011100011111 0000000110100010 # shr b, opd\n0xxx10000011100101111 0000000110100011 # shr c, opd\n0xxx10000011100111111 0000000110100100 # shr d, opd\n0xxx10000011101001111 0000000110100101 # shr e, opd\n0xxx10000011101011111 0000000110100110 # shr bp, opd\n0xxx10000011101101111 0000000110100111 # shr sp, opd\n0xxx10000000000001001 0000000110101000 # add a, [memaddr+opd]\n0xxx10000000000011001 0000000110101001 # add b, [memaddr+opd]\n0xxx10000000000101001 0000000110101010 # add c, [memaddr+opd]\n0xxx10000000000111001 0000000110101011 # add d, [memaddr+opd]\n0xxx10000000001001001 0000000110101100 # add e, [memaddr+opd]\n0xxx10000000001011001 0000000110101101 # add bp, [memaddr+opd]\n0xxx10000000001101001 0000000110101110 # add sp, [memaddr+opd]\n0xxx10000000100001001 0000000110101111 # sub a, [memaddr+opd]\n0xxx10000000100011001 0000000110110000 # sub b, [memaddr+opd]\n0xxx10000000100101001 0000000110110001 # sub c, [memaddr+opd]\n0xxx10000000100111001 0000000110110010 # sub d, [memaddr+opd]\n0xxx10000000101001001 0000000110110011 # sub e, [memaddr+opd]\n0xxx10000000101011001 0000000110110100 # sub bp, [memaddr+opd]\n0xxx10000000101101001 0000000110110101 # sub sp, [memaddr+opd]\n0xxx10000001000001001 0000000110110110 # mul a, [memaddr+opd]\n0xxx10000001000011001 0000000110110111 # mul b, [memaddr+opd]\n0xxx10000001000101001 0000000110111000 # mul c, [memaddr+opd]\n0xxx10000001000111001 0000000110111001 # mul d, [memaddr+opd]\n0xxx10000001001001001 0000000110111010 # mul e, [memaddr+opd]\n0xxx10000001001011001 0000000110111011 # mul bp, [memaddr+opd]\n0xxx10000001001101001 0000000110111100 # mul sp, [memaddr+opd]\n0xxx10000001100001001 0000000110111101 # and a, [memaddr+opd]\n0xxx10000001100011001 0000000110111110 # and b, [memaddr+opd]\n0xxx10000001100101001 0000000110111111 # and c, [memaddr+opd]\n0xxx10000001100111001 0000000111000000 # and d, [memaddr+opd]\n0xxx10000001101001001 0000000111000001 # and e, [memaddr+opd]\n0xxx10000001101011001 0000000111000010 # and bp, [memaddr+opd]\n0xxx10000001101101001 0000000111000011 # and sp, [memaddr+opd]\n0xxx10000010000001001 0000000111000100 # or a, [memaddr+opd]\n0xxx10000010000011001 0000000111000101 # or b, [memaddr+opd]\n0xxx10000010000101001 0000000111000110 # or c, [memaddr+opd]\n0xxx10000010000111001 0000000111000111 # or d, [memaddr+opd]\n0xxx10000010001001001 0000000111001000 # or e, [memaddr+opd]\n0xxx10000010001011001 0000000111001001 # or bp, [memaddr+opd]\n0xxx10000010001101001 0000000111001010 # or sp, [memaddr+opd]\n0xxx10000011000001001 0000000111001011 # xor a, [memaddr+opd]\n0xxx10000011000011001 0000000111001100 # xor b, [memaddr+opd]\n0xxx10000011000101001 0000000111001101 # xor c, [memaddr+opd]\n0xxx10000011000111001 0000000111001110 # xor d, [memaddr+opd]\n0xxx10000011001001001 0000000111001111 # xor e, [memaddr+opd]\n0xxx10000011001011001 0000000111010000 # xor bp, [memaddr+opd]\n0xxx10000011001101001 0000000111010001 # xor sp, [memaddr+opd]\n0xxx10000011100001001 0000000111010010 # shr a, [memaddr+opd]\n0xxx10000011100011001 0000000111010011 # shr b, [memaddr+opd]\n0xxx10000011100101001 0000000111010100 # shr c, [memaddr+opd]\n0xxx10000011100111001 0000000111010101 # shr d, [memaddr+opd]\n0xxx10000011101001001 0000000111010110 # shr e, [memaddr+opd]\n0xxx10000011101011001 0000000111010111 # shr bp, [memaddr+opd]\n0xxx10000011101101001 0000000111011000 # shr sp, [memaddr+opd]\n0xxx10000000010111111 0000000111011001 # add memval,opd\n0xxx10000010100001111 0000000111011010 # not a\n0xxx10000010100011111 0000000111011011 # not b\n0xxx10000010100101111 0000000111011100 # not c\n0xxx10000010100111111 0000000111011101 # not d\n0xxx10000010101001111 0000000111011110 # not e\n0xxx10000010101011111 0000000111011111 # not bp\n0xxx10000010101101111 0000000111100000 # not sp\n0xxx10000100000000000 0000000111100001 # mov a, a\n0xxx10000100000000001 0000000111100010 # mov a, b\n0xxx10000100000000010 0000000111100011 # mov a, c\n0xxx10000100000000011 0000000111100100 # mov a, d\n0xxx10000100000000100 0000000111100101 # mov a, e\n0xxx10000100000000101 0000000111100110 # mov a, bp\n0xxx10000100000000110 0000000111100111 # mov a, sp\n0xxx10000100000010000 0000000111101000 # mov b, a\n0xxx10000100000010001 0000000111101001 # mov b, b\n0xxx10000100000010010 0000000111101010 # mov b, c\n0xxx10000100000010011 0000000111101011 # mov b, d\n0xxx10000100000010100 0000000111101100 # mov b, e\n0xxx10000100000010101 0000000111101101 # mov b, bp\n0xxx10000100000010110 0000000111101110 # mov b, sp\n0xxx10000100000100000 0000000111101111 # mov c, a\n0xxx10000100000100001 0000000111110000 # mov c, b\n0xxx10000100000100010 0000000111110001 # mov c, c\n0xxx10000100000100011 0000000111110010 # mov c, d\n0xxx10000100000100100 0000000111110011 # mov c, e\n0xxx10000100000100101 0000000111110100 # mov c, bp\n0xxx10000100000100110 0000000111110101 # mov c, sp\n0xxx10000100000110000 0000000111110110 # mov d, a\n0xxx10000100000110001 0000000111110111 # mov d, b\n0xxx10000100000110010 0000000111111000 # mov d, c\n0xxx10000100000110011 0000000111111001 # mov d, d\n0xxx10000100000110100 0000000111111010 # mov d, e\n0xxx10000100000110101 0000000111111011 # mov d, bp\n0xxx10000100000110110 0000000111111100 # mov d, sp\n0xxx10000100001000000 0000000111111101 # mov e, a\n0xxx10000100001000001 0000000111111110 # mov e, b\n0xxx10000100001000010 0000000111111111 # mov e, c\n0xxx10000100001000011 0000001000000000 # mov e, d\n0xxx10000100001000100 0000001000000001 # mov e, e\n0xxx10000100001000101 0000001000000010 # mov e, bp\n0xxx10000100001000110 0000001000000011 # mov e, sp\n0xxx10000100001010000 0000001000000100 # mov bp, a\n0xxx10000100001010001 0000001000000101 # mov bp, b\n0xxx10000100001010010 0000001000000110 # mov bp, c\n0xxx10000100001010011 0000001000000111 # mov bp, d\n0xxx10000100001010100 0000001000001000 # mov bp, e\n0xxx10000100001010101 0000001000001001 # mov bp, bp\n0xxx10000100001010110 0000001000001010 # mov bp, sp\n0xxx10000100001100000 0000001000001011 # mov sp, a\n0xxx10000100001100001 0000001000001100 # mov sp, b\n0xxx10000100001100010 0000001000001101 # mov sp, c\n0xxx10000100001100011 0000001000001110 # mov sp, d\n0xxx10000100001100100 0000001000001111 # mov sp, e\n0xxx10000100001100101 0000001000010000 # mov sp, bp\n0xxx10000100001100110 0000001000010001 # mov sp, sp\n0xxx10000100000001001 0000001000010010 # mov a, [memaddr+opd]\n0xxx10000100000011001 0000001000010011 # mov b, [memaddr+opd]\n0xxx10000100000101001 0000001000010100 # mov c, [memaddr+opd]\n0xxx10000100000111001 0000001000010101 # mov d, [memaddr+opd]\n0xxx10000100001001001 0000001000010110 # mov e, [memaddr+opd]\n0xxx10000100001011001 0000001000010111 # mov bp, [memaddr+opd]\n0xxx10000100001101001 0000001000011000 # mov sp, [memaddr+opd]\n0xxx10000100010111001 0000001000011001 # mov memval, [memaddr+opd]\n0xxx10000100010100000 0000001000011010 # mov memaddr,a\n0xxx10000100010100001 0000001000011011 # mov memaddr,b\n0xxx10000100010100010 0000001000011100 # mov memaddr,c\n0xxx10000100010100011 0000001000011101 # mov memaddr,d\n0xxx10000100010100100 0000001000011110 # mov memaddr,e\n0xxx10000100010100101 0000001000011111 # mov memaddr,bp\n0xxx10000100010100110 0000001000100000 # mov memaddr,sp\n0xxx10000100010110000 0000001000100001 # mov memval,a\n0xxx10000100010110001 0000001000100010 # mov memval,b\n0xxx10000100010110010 0000001000100011 # mov memval,c\n0xxx10000100010110011 0000001000100100 # mov memval,d\n0xxx10000100010110100 0000001000100101 # mov memval,e\n0xxx10000100010110101 0000001000100110 # mov memval,bp\n0xxx10000100010110110 0000001000100111 # mov memval,sp\n0xxx10000100000001011 0000001000101000 # mov a,memval\n0xxx10000100000011011 0000001000101001 # mov b,memval\n0xxx10000100000101011 0000001000101010 # mov c,memval\n0xxx10000100000111011 0000001000101011 # mov d,memval\n0xxx10000100001001011 0000001000101100 # mov e,memval\n0xxx10000100001011011 0000001000101101 # mov bp,memval\n0xxx10000100001101011 0000001000101110 # mov sp,memval\n0xxx10000100010101010 0000001000101111 # mov [memaddr+opd],memval\n0xxx10000100010101111 0000001000110000 # mov memaddr, opd\n0xxx10000100010111111 0000001000110001 # mov memval, opd\n0xxx10000100000001111 0000001000110010 # mov a, opd\n0xxx10000100000011111 0000001000110011 # mov b, opd\n0xxx10000100000101111 0000001000110100 # mov c, opd\n0xxx10000100000111111 0000001000110101 # mov d, opd\n0xxx10000100001001111 0000001000110110 # mov e, opd\n0xxx10000100001011111 0000001000110111 # mov bp, opd\n0xxx10000100001101111 0000001000111000 # mov sp, opd\n0xxx10000100100001111 0000001000111001 # in a\n0xxx10000100100011111 0000001000111010 # in b\n0xxx10000100100101111 0000001000111011 # in c\n0xxx10000100100111111 0000001000111100 # in d\n0xxx10000100101001111 0000001000111101 # in e\n0xxx10000100101011111 0000001000111110 # in bp\n0xxx10000100101101111 0000001000111111 # in sp\n0xxx10000101000001111 0000001001000000 # out a\n0xxx10000101000011111 0000001001000001 # out b\n0xxx10000101000101111 0000001001000010 # out c\n0xxx10000101000111111 0000001001000011 # out d\n0xxx10000101001001111 0000001001000100 # out e\n0xxx10000101001011111 0000001001000101 # out bp\n0xxx10000101001101111 0000001001000110 # out sp\n0xxx10000101011111111 0000001001000111 # out opd\n0xxx10001001000000000 0000001001001000 # cmp a, a\n0xxx10001001000000001 0000001001001001 # cmp a, b\n0xxx10001001000000010 0000001001001010 # cmp a, c\n0xxx10001001000000011 0000001001001011 # cmp a, d\n0xxx10001001000000100 0000001001001100 # cmp a, e\n0xxx10001001000000101 0000001001001101 # cmp a, bp\n0xxx10001001000000110 0000001001001110 # cmp a, sp\n0xxx10001001000010000 0000001001001111 # cmp b, a\n0xxx10001001000010001 0000001001010000 # cmp b, b\n0xxx10001001000010010 0000001001010001 # cmp b, c\n0xxx10001001000010011 0000001001010010 # cmp b, d\n0xxx10001001000010100 0000001001010011 # cmp b, e\n0xxx10001001000010101 0000001001010100 # cmp b, bp\n0xxx10001001000010110 0000001001010101 # cmp b, sp\n0xxx10001001000100000 0000001001010110 # cmp c, a\n0xxx10001001000100001 0000001001010111 # cmp c, b\n0xxx10001001000100010 0000001001011000 # cmp c, c\n0xxx10001001000100011 0000001001011001 # cmp c, d\n0xxx10001001000100100 0000001001011010 # cmp c, e\n0xxx10001001000100101 0000001001011011 # cmp c, bp\n0xxx10001001000100110 0000001001011100 # cmp c, sp\n0xxx10001001000110000 0000001001011101 # cmp d, a\n0xxx10001001000110001 0000001001011110 # cmp d, b\n0xxx10001001000110010 0000001001011111 # cmp d, c\n0xxx10001001000110011 0000001001100000 # cmp d, d\n0xxx10001001000110100 0000001001100001 # cmp d, e\n0xxx10001001000110101 0000001001100010 # cmp d, bp\n0xxx10001001000110110 0000001001100011 # cmp d, sp\n0xxx10001001001000000 0000001001100100 # cmp e, a\n0xxx10001001001000001 0000001001100101 # cmp e, b\n0xxx10001001001000010 0000001001100110 # cmp e, c\n0xxx10001001001000011 0000001001100111 # cmp e, d\n0xxx10001001001000100 0000001001101000 # cmp e, e\n0xxx10001001001000101 0000001001101001 # cmp e, bp\n0xxx10001001001000110 0000001001101010 # cmp e, sp\n0xxx10001001001010000 0000001001101011 # cmp bp, a\n0xxx10001001001010001 0000001001101100 # cmp bp, b\n0xxx10001001001010010 0000001001101101 # cmp bp, c\n0xxx10001001001010011 0000001001101110 # cmp bp, d\n0xxx10001001001010100 0000001001101111 # cmp bp, e\n0xxx10001001001010101 0000001001110000 # cmp bp, bp\n0xxx10001001001010110 0000001001110001 # cmp bp, sp\n0xxx10001001001100000 0000001001110010 # cmp sp, a\n0xxx10001001001100001 0000001001110011 # cmp sp, b\n0xxx10001001001100010 0000001001110100 # cmp sp, c\n0xxx10001001001100011 0000001001110101 # cmp sp, d\n0xxx10001001001100100 0000001001110110 # cmp sp, e\n0xxx10001001001100101 0000001001110111 # cmp sp, bp\n0xxx10001001001100110 0000001001111000 # cmp sp, sp\n0xxx10001001000001111 0000001001111001 # cmp a, opd\n0xxx10001001000011111 0000001001111010 # cmp b, opd\n0xxx10001001000101111 0000001001111011 # cmp c, opd\n0xxx10001001000111111 0000001001111100 # cmp d, opd\n0xxx10001001001001111 0000001001111101 # cmp e, opd\n0xxx10001001001011111 0000001001111110 # cmp bp, opd\n0xxx10001001001101111 0000001001111111 # cmp sp, opd\n0xxx10001000110111111 0000001010000000 # jmp memval\n00xx10000101100001111 0000001010000001 # jnc a (Taken)\n00xx10000101100011111 0000001010000010 # jnc b (Taken)\n00xx10000101100101111 0000001010000011 # jnc c (Taken)\n00xx10000101100111111 0000001010000100 # jnc d (Taken)\n00xx10000101101001111 0000001010000101 # jnc e (Taken)\n00xx10000101101011111 0000001010000110 # jnc bp (Taken)\n00xx10000101101101111 0000001010000111 # jnc sp (Taken)\n01xx10000101100001111 0000001010001000 # jnc a (Skip)\n01xx10000101100011111 0000001010001001 # jnc b (Skip)\n01xx10000101100101111 0000001010001010 # jnc c (Skip)\n01xx10000101100111111 0000001010001011 # jnc d (Skip)\n01xx10000101101001111 0000001010001100 # jnc e (Skip)\n01xx10000101101011111 0000001010001101 # jnc bp (Skip)\n01xx10000101101101111 0000001010001110 # jnc sp (Skip)\n01xx10000110000001111 0000001010001111 # jc a (Taken)\n01xx10000110000011111 0000001010010000 # jc b (Taken)\n01xx10000110000101111 0000001010010001 # jc c (Taken)\n01xx10000110000111111 0000001010010010 # jc d (Taken)\n01xx10000110001001111 0000001010010011 # jc e (Taken)\n01xx10000110001011111 0000001010010100 # jc bp (Taken)\n01xx10000110001101111 0000001010010101 # jc sp (Taken)\n00xx10000110000001111 0000001010010110 # jc a (Skip)\n00xx10000110000011111 0000001010010111 # jc b (Skip)\n00xx10000110000101111 0000001010011000 # jc c (Skip)\n00xx10000110000111111 0000001010011001 # jc d (Skip)\n00xx10000110001001111 0000001010011010 # jc e (Skip)\n00xx10000110001011111 0000001010011011 # jc bp (Skip)\n00xx10000110001101111 0000001010011100 # jc sp (Skip)\n0x0x10000110100001111 0000001010011101 # jnz a (Taken)\n0x0x10000110100011111 0000001010011110 # jnz b (Taken)\n0x0x10000110100101111 0000001010011111 # jnz c (Taken)\n0x0x10000110100111111 0000001010100000 # jnz d (Taken)\n0x0x10000110101001111 0000001010100001 # jnz e (Taken)\n0x0x10000110101011111 0000001010100010 # jnz bp (Taken)\n0x0x10000110101101111 0000001010100011 # jnz sp (Taken)\n0x1x10000110100001111 0000001010100100 # jnz a (Skip)\n0x1x10000110100011111 0000001010100101 # jnz b (Skip)\n0x1x10000110100101111 0000001010100110 # jnz c (Skip)\n0x1x10000110100111111 0000001010100111 # jnz d (Skip)\n0x1x10000110101001111 0000001010101000 # jnz e (Skip)\n0x1x10000110101011111 0000001010101001 # jnz bp (Skip)\n0x1x10000110101101111 0000001010101010 # jnz sp (Skip)\n0x1x10000111000001111 0000001010101011 # jz a (Taken)\n0x1x10000111000011111 0000001010101100 # jz b (Taken)\n0x1x10000111000101111 0000001010101101 # jz c (Taken)\n0x1x10000111000111111 0000001010101110 # jz d (Taken)\n0x1x10000111001001111 0000001010101111 # jz e (Taken)\n0x1x10000111001011111 0000001010110000 # jz bp (Taken)\n0x1x10000111001101111 0000001010110001 # jz sp (Taken)\n0x0x10000111000001111 0000001010110010 # jz a (Skip)\n0x0x10000111000011111 0000001010110011 # jz b (Skip)\n0x0x10000111000101111 0000001010110100 # jz c (Skip)\n0x0x10000111000111111 0000001010110101 # jz d (Skip)\n0x0x10000111001001111 0000001010110110 # jz e (Skip)\n0x0x10000111001011111 0000001010110111 # jz bp (Skip)\n0x0x10000111001101111 0000001010111000 # jz sp (Skip)\n0xx010000111100001111 0000001010111001 # jns a (Taken)\n0xx010000111100011111 0000001010111010 # jns b (Taken)\n0xx010000111100101111 0000001010111011 # jns c (Taken)\n0xx010000111100111111 0000001010111100 # jns d (Taken)\n0xx010000111101001111 0000001010111101 # jns e (Taken)\n0xx010000111101011111 0000001010111110 # jns bp (Taken)\n0xx010000111101101111 0000001010111111 # jns sp (Taken)\n0xx110000111100001111 0000001011000000 # jns a (Skip)\n0xx110000111100011111 0000001011000001 # jns b (Skip)\n0xx110000111100101111 0000001011000010 # jns c (Skip)\n0xx110000111100111111 0000001011000011 # jns d (Skip)\n0xx110000111101001111 0000001011000100 # jns e (Skip)\n0xx110000111101011111 0000001011000101 # jns bp (Skip)\n0xx110000111101101111 0000001011000110 # jns sp (Skip)\n0xx110001000000001111 0000001011000111 # js a (Taken)\n0xx110001000000011111 0000001011001000 # js b (Taken)\n0xx110001000000101111 0000001011001001 # js c (Taken)\n0xx110001000000111111 0000001011001010 # js d (Taken)\n0xx110001000001001111 0000001011001011 # js e (Taken)\n0xx110001000001011111 0000001011001100 # js bp (Taken)\n0xx110001000001101111 0000001011001101 # js sp (Taken)\n0xx010001000000001111 0000001011001110 # js a (Skip)\n0xx010001000000011111 0000001011001111 # js b (Skip)\n0xx010001000000101111 0000001011010000 # js c (Skip)\n0xx010001000000111111 0000001011010001 # js d (Skip)\n0xx010001000001001111 0000001011010010 # js e (Skip)\n0xx010001000001011111 0000001011010011 # js bp (Skip)\n0xx010001000001101111 0000001011010100 # js sp (Skip)\n0xxx10001000100001111 0000001011010101 # jmp a\n0xxx10001000100011111 0000001011010110 # jmp b\n0xxx10001000100101111 0000001011010111 # jmp c\n0xxx10001000100111111 0000001011011000 # jmp d\n0xxx10001000101001111 0000001011011001 # jmp e\n0xxx10001000101011111 0000001011011010 # jmp bp\n0xxx10001000101101111 0000001011011011 # jmp sp\n0x1x10001011000001111 0000001011011100 # je a (Taken)\n0x1x10001011000011111 0000001011011101 # je b (Taken)\n0x1x10001011000101111 0000001011011110 # je c (Taken)\n0x1x10001011000111111 0000001011011111 # je d (Taken)\n0x1x10001011001001111 0000001011100000 # je e (Taken)\n0x1x10001011001011111 0000001011100001 # je bp (Taken)\n0x1x10001011001101111 0000001011100010 # je sp (Taken)\n0x0x10001011000001111 0000001011100011 # je a (Skip)\n0x0x10001011000011111 0000001011100100 # je b (Skip)\n0x0x10001011000101111 0000001011100101 # je c (Skip)\n0x0x10001011000111111 0000001011100110 # je d (Skip)\n0x0x10001011001001111 0000001011100111 # je e (Skip)\n0x0x10001011001011111 0000001011101000 # je bp (Skip)\n0x0x10001011001101111 0000001011101001 # je sp (Skip)\n0x0x10001011100001111 0000001011101010 # jne a(Taken)\n0x0x10001011100011111 0000001011101011 # jne b(Taken)\n0x0x10001011100101111 0000001011101100 # jne c(Taken)\n0x0x10001011100111111 0000001011101101 # jne d(Taken)\n0x0x10001011101001111 0000001011101110 # jne e(Taken)\n0x0x10001011101011111 0000001011101111 # jne bp(Taken)\n0x0x10001011101101111 0000001011110000 # jne sp(Taken)\n0x1x10001011100001111 0000001011110001 # jne a(Skip)\n0x1x10001011100011111 0000001011110010 # jne b(Skip)\n0x1x10001011100101111 0000001011110011 # jne c(Skip)\n0x1x10001011100111111 0000001011110100 # jne d(Skip)\n0x1x10001011101001111 0000001011110101 # jne e(Skip)\n0x1x10001011101011111 0000001011110110 # jne bp(Skip)\n0x1x10001011101101111 0000001011110111 # jne sp(Skip)\n0x0010001100000001111 0000001011111000 # ja a (Taken)\n0x0010001100000011111 0000001011111001 # ja b (Taken)\n0x0010001100000101111 0000001011111010 # ja c (Taken)\n0x0010001100000111111 0000001011111011 # ja d (Taken)\n0x0010001100001001111 0000001011111100 # ja e (Taken)\n0x0010001100001011111 0000001011111101 # ja bp (Taken)\n0x0010001100001101111 0000001011111110 # ja sp (Taken)\n0xxx10001100000001111 0000001011111111 # ja a (Skip)\n0xxx10001100000011111 0000001100000000 # ja b (Skip)\n0xxx10001100000101111 0000001100000001 # ja c (Skip)\n0xxx10001100000111111 0000001100000010 # ja d (Skip)\n0xxx10001100001001111 0000001100000011 # ja e (Skip)\n0xxx10001100001011111 0000001100000100 # ja bp (Skip)\n0xxx10001100001101111 0000001100000101 # ja sp (Skip)\n0x0010001100100001111 0000001100000110 # jae a (Taken)\n0x0010001100100011111 0000001100000111 # jae b (Taken)\n0x0010001100100101111 0000001100001000 # jae c (Taken)\n0x0010001100100111111 0000001100001001 # jae d (Taken)\n0x0010001100101001111 0000001100001010 # jae e (Taken)\n0x0010001100101011111 0000001100001011 # jae bp (Taken)\n0x0010001100101101111 0000001100001100 # jae sp (Taken)\n0x1010001100100001111 0000001100001101 # jae a (Taken)\n0x1010001100100011111 0000001100001110 # jae b (Taken)\n0x1010001100100101111 0000001100001111 # jae c (Taken)\n0x1010001100100111111 0000001100010000 # jae d (Taken)\n0x1010001100101001111 0000001100010001 # jae e (Taken)\n0x1010001100101011111 0000001100010010 # jae bp (Taken)\n0x1010001100101101111 0000001100010011 # jae sp (Taken)\n0xxx10001100100001111 0000001100010100 # jae a (Skip)\n0xxx10001100100011111 0000001100010101 # jae b (Skip)\n0xxx10001100100101111 0000001100010110 # jae c (Skip)\n0xxx10001100100111111 0000001100010111 # jae d (Skip)\n0xxx10001100101001111 0000001100011000 # jae e (Skip)\n0xxx10001100101011111 0000001100011001 # jae bp (Skip)\n0xxx10001100101101111 0000001100011010 # jae sp (Skip)\n0x0110001101000001111 0000001100011011 # jl a (Taken)\n0x0110001101000011111 0000001100011100 # jl b (Taken)\n0x0110001101000101111 0000001100011101 # jl c (Taken)\n0x0110001101000111111 0000001100011110 # jl d (Taken)\n0x0110001101001001111 0000001100011111 # jl e (Taken)\n0x0110001101001011111 0000001100100000 # jl bp (Taken)\n0x0110001101001101111 0000001100100001 # jl sp (Taken)\n0xxx10001101000001111 0000001100100010 # jl a (Skip)\n0xxx10001101000011111 0000001100100011 # jl b (Skip)\n0xxx10001101000101111 0000001100100100 # jl c (Skip)\n0xxx10001101000111111 0000001100100101 # jl d (Skip)\n0xxx10001101001001111 0000001100100110 # jl e (Skip)\n0xxx10001101001011111 0000001100100111 # jl bp (Skip)\n0xxx10001101001101111 0000001100101000 # jl sp (Skip)\n0x0110001101100001111 0000001100101001 # jle a (Taken)\n0x0110001101100011111 0000001100101010 # jle b (Taken)\n0x0110001101100101111 0000001100101011 # jle c (Taken)\n0x0110001101100111111 0000001100101100 # jle d (Taken)\n0x0110001101101001111 0000001100101101 # jle e (Taken)\n0x0110001101101011111 0000001100101110 # jle bp (Taken)\n0x0110001101101101111 0000001100101111 # jle sp (Taken)\n0x1010001101100001111 0000001100110000 # jle a (Taken)\n0x1010001101100011111 0000001100110001 # jle b (Taken)\n0x1010001101100101111 0000001100110010 # jle c (Taken)\n0x1010001101100111111 0000001100110011 # jle d (Taken)\n0x1010001101101001111 0000001100110100 # jle e (Taken)\n0x1010001101101011111 0000001100110101 # jle bp (Taken)\n0x1010001101101101111 0000001100110110 # jle sp (Taken)\n0xxx10001101100001111 0000001100110111 # jle a (Skip)\n0xxx10001101100011111 0000001100111000 # jle b (Skip)\n0xxx10001101100101111 0000001100111001 # jle c (Skip)\n0xxx10001101100111111 0000001100111010 # jle d (Skip)\n0xxx10001101101001111 0000001100111011 # jle e (Skip)\n0xxx10001101101011111 0000001100111100 # jle bp (Skip)\n0xxx10001101101101111 0000001100111101 # jle sp (Skip)\n0xxx10001110111111111 0000001100111110 # setinaddr opd\n0xxx10001110100001111 0000001100111111 # setinaddr a\n0xxx10001110100011111 0000001101000000 # setinaddr b\n0xxx10001110100101111 0000001101000001 # setinaddr c\n0xxx10001110100111111 0000001101000010 # setinaddr d\n0xxx10001110101001111 0000001101000011 # setinaddr e\n0xxx10001110101011111 0000001101000100 # setinaddr bp\n0xxx10001110101101111 0000001101000101 # setinaddr sp\n0xxx10001111011111111 0000001101000110 # setoutaddr opd\n0xxx10001111000001111 0000001101000111 # setoutaddr a\n0xxx10001111000011111 0000001101001000 # setoutaddr b\n0xxx10001111000101111 0000001101001001 # setoutaddr c\n0xxx10001111000111111 0000001101001010 # setoutaddr d\n0xxx10001111001001111 0000001101001011 # setoutaddr e\n0xxx10001111001011111 0000001101001100 # setoutaddr bp\n0xxx10001111001101111 0000001101001101 # setoutaddr sp\n0xxx10001111111111111 0000001101001110 # setreadburstmode\n0xxx10010000011111111 0000001101010000 # clearreadburstmode\n0xxx10010000111111111 0000001101010010 # setzerobufferpointer\n0xxx10010001011111111 0000001101010100 # incbufferpointer\n0xxx10010001111111111 0000001101010110 # setbuffersize opd\n0xxx10010001100001111 0000001101010111 # setbuffersize a\n0xxx10010001100011111 0000001101011000 # setbuffersize b\n0xxx10010001100101111 0000001101011001 # setbuffersize c\n0xxx10010001100111111 0000001101011010 # setbuffersize d\n0xxx10010001101001111 0000001101011011 # setbuffersize e\n0xxx10010001101011111 0000001101011100 # setbuffersize bp\n0xxx10010001101101111 0000001101011101 # setbuffersize sp\n0xxx10010010011111111 0000001101011110 # buffertomemval\n0xxx10010010111111111 0000001101011111 # setintdisableflag\n0xxx10010011011111111 0000001101100001 # clearintdisableflag\n0xxx10001110011111111 0000001101100011 # intret\n0xxx10010011111111111 0000001101101010 # syscall\n0xxx10010101011111111 0000001101110100 # sysret\n0xxx10010100011111111 0000001101111010 # usercall\n0xxx10010100111111111 0000001110000100 # userret\n1xxxxxxxxxxxxxxxxxxxx 0000001110001010 # Interrupt")) IMBD (
    .in({and_3_out[20], carry_flag, zero_flag, sign_flag, 1'b1, IR_opcode_q}), .out(IMBD_out));
  and and_3 (and_3_out[20], INT, State_To_Output_Decoder_out[0]);
  not not_1 (not_1_out, Instruction_permission_checker_out);
  and and_4 (output_status[1], not_1_out, or_5_out, exec_mode);
  Comparator #(.mode("unsigned")) comparator_7 (
    .a(State_Register_q[15:8]), .b({8{1'b1}}), .eq(comparator_7_eq));  // open: gt, lt
  ROM #(.addrWidth(16), .dataWidth(24)) Microcode_ROM (.addr(adder_6_out), .data(Microcode_ROM_data));
  Adder #(.width(16)) adder_6 (.a(IMBD_out), .b(MFCR_q), .out(adder_6_out));  // open: cin, cout
  and and_5 (output_status[3], comparator_7_eq, or_5_out);
  Multiplexer #(.width(22)) multiplexer_7 (
    .in0(22'h78), .in1(Microcode_ROM_data[21:0]), .out(multiplexer_7_out),
    .sel(State_To_Output_Decoder_out[2]));
  Register #(.width(16)) MOR (
    .D(multiplexer_7_out[15:0]), .en(Microcode_ROM_data[23]), .clk(CLK), .Q(MOR_q), .clr(RESET));
  Multiplexer #(.width(22)) multiplexer_8 (
    .in0(22'h78), .in1(multiplexer_7_out), .out({CPU_Control_BUS, multiplexer_8_out[0]}), .sel(not_2_out));
  not not_2 (not_2_out, Microcode_ROM_data[23]);
  or or_6 (HLT, output_status[2], and_1_out, output_status[4], output_status[3], output_status[1]);

  // Notes on the sheet:
  //   STOP_ADDRESS
  //   DEBUG_SW(1:ON_0:OFF)
  //   BIOS_SIZE
  //   contents of BIOS_ROM (hex, n*v repeats v):
  //   11ff 18 80f 0 f 1 123 0 fff 4 10f 1 23 0 830 0 8a6 0 8b9 0 6f 1 11bf 0 86f ffff 8af 0 8bf 58 8aa
  //   5002 11ff 19e 21ff 0 232f 0 25ff 0 1d0f 0 1e0f 0 85f 0 1fff 0 a1f 0 a2f 0 26ff 0 125f 1 1aff 36 20ff
  //   0 21ff 0 80f 0 24ff 0 8a3 0 8aa 0 3f 1 f 1 22ff 0 1202 0 1aff 40 8a6 0 8b9 0 6f 1 11bf 0 85f 1 1cff
  //   0 16f 1 8b2 0 8a6 0 8aa 0 16f 1 8b3 0 8a6 0 8aa 0 16f 1 8b4 0 8a6 0 8aa 0 821 0 8a2 0 839 0 843 0
  //   33f ff00 73f 8 123f 0 16ff 96 1e0f 0 a3f 0 34f ff 124f 0 16ff 96 1e0f 0 a4f 0 2f 1 11ff 76 8a6 0 849
  //   0 6f 1 8a6 0 839 0 6f 1 8a6 0 829 0 6f 1 8a6 0 8b9 0 6f 1 11bf 0 506f 7765 7265 6420 6279 204e 432d
  //   3136 2043 5055 202f 2043 7265 6174 6564 2062 7920 4d6f 6d6f 7465 7261 2e0a 0 4249 4f53 2073 7461
  //   7274 6564 2073 7563 6365 7373 6675 6c6c 792e a00 5365 6172 6368 696e 6720 666f 7220 6f70 6572 6174
  //   696e 6720 7379 7374 656d 2e2e 2e0a 0 4f70 6572 6174 696e 6720 7379 7374 656d 2066 6f75 6e64 2e0a 0
  //   5b45 5252 4f52 5d20 4e6f 2062 6f6f 7461 626c 6520 4f53 2066 6f75 6e64 2e0a 506c 6561 7365 206c 6f61
  //   6420 6120 626f 6f74 6162 6c65 204f 5320 696e 746f 204f 535f 524f 4d20 616e 6420 7072 6573 7320 7468
  //   6520 5245 5345 5420 6275 7474 6f6e 2e0a a4e 6f74 653a 2049 6620 7468 6973 206d 6573 7361 6765 2070
  //   6572 7369 7374 7320 6166 7465 7220 6c6f 6164 696e 672c 2076 6572 6966 7920 7468 6174 2074 6865 2066
  //   6972 7374 2034 2062 7974 6573 206f 6620 7468 6520 4f53 2061 7265 2030 7832 3432 3120 3078 3866 3261
  //   2e20 5573 6520 6f73 6173 7365 6d62 6c65 722e 7079 2074 6f20 6765 6e65 7261 7465 2061 2076 616c 6964
  //   204f 5320 6269 6e61 7279 2e0a 0 4f53 206c 6f61 6469 6e67 2063 6f6d 706c 6574 652e a00 5374 6172 7469
  //   6e67 206f 7065 7261 7469 6e67 2073 7973 7465 6d2e a00 4c6f 6164 696e 6720 6f70 6572 6174 696e 6720
  //   7379 7374 656d 2e2e 2e0a 4*0 80f 0 81f b0 15ff 0 bf a 16f 1 8a6 0 8aa 0 11ff 5c 81f c7 15ff 0 bf a
  //   16f 1 8a6 0 8aa 0 11ff 5c 81f d5 15ff 0 bf a 16f 1 8a6 0 8aa 0 11ff 5c 80f 2 81f 0 82f 3 83f 19b
  //   15ff 0 bf a 16f 1 8a6 0 8aa 0 11ff 22 81f 19b 8a1 0 809 0 120f ff21 17ff 244 8a1 0 809 1 120f 8f2a
  //   17ff 244 8a1 0 829 2 80f 0 81f e7 15ff 0 bf a 16f 1 8a6 0 8aa 0 11ff 5c 81f 18c 15ff 0 bf a 16f 1
  //   8a6 0 8aa 0 11ff 5c 80f 2 81f 3 83f 500 15ff 0 bf a 16f 1 8a6 0 8aa 0 11ff 22 80f 0 81f 173 15ff 0
  //   bf a 16f 1 8a6 0 8aa 0 11ff 5c 81f 17e 15ff 0 bf a 16f 1 8a6 0 8aa 0 11ff 5c 11ff 500 80f 0 81f f4
  //   15ff 0 bf a 16f 1 8a6 0 8aa 0 11ff 5c 13ff
  //   contents of Microcode_ROM (hex, n*v repeats v):
  //   78 38038 78 38038 78 38038 78 38038 78 38038 78 38038 78 38038 38038 78 38038 78 38038 78 38038
  //   38038 78 38038 78 38038 38038 78 100078 78 78 50050 204000 204800 205000 205800 206000 206800 207000
  //   20c008 20c808 20d008 20d808 20e008 20e808 20f008 214010 214810 215010 215810 216010 216810 217010
  //   21c018 21c818 21d018 21d818 21e018 21e818 21f018 224020 224820 225020 225820 226020 226820 227020
  //   22c028 22c828 22d028 22d828 22e028 22e828 22f028 234030 234830 235030 235830 236030 236830 237030
  //   204100 204900 205100 205900 206100 206900 207100 20c108 20c908 20d108 20d908 20e108 20e908 20f108
  //   214110 214910 215110 215910 216110 216910 217110 21c118 21c918 21d118 21d918 21e118 21e918 21f118
  //   224120 224920 225120 225920 226120 226920 227120 22c128 22c928 22d128 22d928 22e128 22e928 22f128
  //   234130 234930 235130 235930 236130 236930 237130 204200 204a00 205200 205a00 206200 206a00 207200
  //   20c208 20ca08 20d208 20da08 20e208 20ea08 20f208 214210 214a10 215210 215a10 216210 216a10 217210
  //   21c218 21ca18 21d218 21da18 21e218 21ea18 21f218 224220 224a20 225220 225a20 226220 226a20 227220
  //   22c228 22ca28 22d228 22da28 22e228 22ea28 22f228 234230 234a30 235230 235a30 236230 236a30 237230
  //   204300 204b00 205300 205b00 206300 206b00 207300 20c308 20cb08 20d308 20db08 20e308 20eb08 20f308
  //   214310 214b10 215310 215b10 216310 216b10 217310 21c318 21cb18 21d318 21db18 21e318 21eb18 21f318
  //   224320 224b20 225320 225b20 226320 226b20 227320 22c328 22cb28 22d328 22db28 22e328 22eb28 22f328
  //   234330 234b30 235330 235b30 236330 236b30 237330 204400 204c00 205400 205c00 206400 206c00 207400
  //   20c408 20cc08 20d408 20dc08 20e408 20ec08 20f408 214410 214c10 215410 215c10 216410 216c10 217410
  //   21c418 21cc18 21d418 21dc18 21e418 21ec18 21f418 224420 224c20 225420 225c20 226420 226c20 227420
  //   22c428 22cc28 22d428 22dc28 22e428 22ec28 22f428 234430 234c30 235430 235c30 236430 236c30 237430
  //   204600 204e00 205600 205e00 206600 206e00 207600 20c608 20ce08 20d608 20de08 20e608 20ee08 20f608
  //   214610 214e10 215610 215e10 216610 216e10 217610 21c618 21ce18 21d618 21de18 21e618 21ee18 21f618
  //   224620 224e20 225620 225e20 226620 226e20 227620 22c628 22ce28 22d628 22de28 22e628 22ee28 22f628
  //   234630 234e30 235630 235e30 236630 236e30 237630 204700 204f00 205700 205f00 206700 206f00 207700
  //   20c708 20cf08 20d708 20df08 20e708 20ef08 20f708 214710 214f10 215710 215f10 216710 216f10 217710
  //   21c718 21cf18 21d718 21df18 21e718 21ef18 21f718 224720 224f20 225720 225f20 226720 226f20 227720
  //   22c728 22cf28 22d728 22df28 22e728 22ef28 22f728 234730 234f30 235730 235f30 236730 236f30 237730
  //   207800 20f808 217810 21f818 227820 22f828 237830 207900 20f908 217910 21f918 227920 22f928 237930
  //   207a00 20fa08 217a10 21fa18 227a20 22fa28 237a30 207b00 20fb08 217b10 21fb18 227b20 22fb28 237b30
  //   207c00 20fc08 217c10 21fc18 227c20 22fc28 237c30 207e00 20fe08 217e10 21fe18 227e20 22fe28 237e30
  //   207f00 20ff08 217f10 21ff18 227f20 22ff28 237f30 24c002 24c80a 24d012 24d81a 24e022 24e82a 24f032
  //   24c102 24c90a 24d112 24d91a 24e122 24e92a 24f132 24c202 24ca0a 24d212 24da1a 24e222 24ea2a 24f232
  //   24c302 24cb0a 24d312 24db1a 24e322 24eb2a 24f332 24c402 24cc0a 24d412 24dc1a 24e422 24ec2a 24f432
  //   24c602 24ce0a 24d612 24de1a 24e622 24ee2a 24f632 24c702 24cf0a 24d712 24df1a 24e722 24ef2a 24f732
  //   25f850 204500 20c508 214510 21c518 224520 22c528 234530 0 8000 10000 18000 20000 28000 30000 8 8008
  //   10008 18008 20008 28008 30008 10 8010 10010 18010 20010 28010 30010 18 8018 10018 18018 20018 28018
  //   30018 20 8020 10020 18020 20020 28020 30020 28 8028 10028 18028 20028 28028 30028 30 8030 10030
  //   18030 20030 28030 30030 48002 4800a 48012 4801a 48022 4802a 48032 48052 48 8048 10048 18048 20048
  //   28048 30048 50 8050 10050 18050 20050 28050 30050 50000 50008 50010 50018 50020 50028 50030 7b 38048
  //   38050 38000 38008 38010 38018 38020 38028 38030 40000 40008 40010 40018 40020 40028 40030 40 8040
  //   10040 18040 20040 28040 30040 38040 204178 204978 205178 205978 206178 206978 207178 20c178 20c978
  //   20d178 20d978 20e178 20e978 20f178 214178 214978 215178 215978 216178 216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
endmodule

module registers (
  input  [15:0] reg_data_in,
  input  CLK,
  input  RESET,
  input  [31:0] write_reg_select,
  input  carry_flag,
  input  zero_flag,
  input  sign_flag,
  input  flag_write_sw,
  input  [15:0] INTNUM_input,
  input  INT,
  input  [15:0] Input_data,
  input  Input_st,
  input  OS_RESTART,
  output [15:0] memval_out,
  output [15:0] memaddr_out,
  output [15:0] a_out,
  output [15:0] b_out,
  output [15:0] c_out,
  output [15:0] d_out,
  output [15:0] e_out,
  output [15:0] bp_out,
  output [15:0] sp_out,
  output [15:0] output_out,
  output [15:0] flag_output,
  output [15:0] INTNUM_out,
  output out_st,
  output [15:0] inaddr_out,
  output [15:0] outaddr_out,
  output [15:0] Input_out,
  output [15:0] buffer_out,
  output [15:0] buffer_point_out,
  output [15:0] buffer_size_out,
  output buffer_full_int,
  output exec_mode,
  output out_35
);

  wire and_1_out, and_2_out, comparator_1_eq, comparator_1_gt, d_ff_1_q, d_ff_2_q, multiplexer_2_out,
       not_1_out, not_2_out, not_3_out, not_4_out, not_5_out, or_1_out, or_2_out, or_3_out, or_4_out,
       or_5_out, or_6_out;
  wire [6:0] controlled_buffer_1_out;
  wire [15:0] adder_1_out, multiplexer_3_out, multiplexer_4_out, multiplexer_5_out;

  Clock clock_1 ();  // open: out
  D_Flip_Flop d_ff_1 (.D(1'b0), .clk(CLK), .Q(d_ff_1_q), .preset(OS_RESTART), .reset(RESET));  // open: Qn
  Multiplexer multiplexer_1 (.in0(exec_mode), .in1(1'b0), .out(controlled_buffer_1_out[6]), .sel(d_ff_1_q));
  D_Flip_Flop d_ff_2 (.D(INT), .clk(CLK), .Q(d_ff_2_q), .reset(RESET));  // open: Qn, preset
  assign controlled_buffer_1_out[0] = flag_write_sw ? carry_flag : 1'bz;  // Controlled_Buffer controlled_buffer_1
  assign controlled_buffer_1_out[1] = flag_write_sw ? zero_flag : 1'bz;  // Controlled_Buffer controlled_buffer_2
  assign controlled_buffer_1_out[3] = and_1_out ? and_1_out : 1'bz;  // Controlled_Buffer controlled_buffer_3
  not not_1 (not_1_out, flag_write_sw);
  not not_2 (not_2_out, flag_output[4]);
  assign controlled_buffer_1_out[2] = flag_write_sw ? sign_flag : 1'bz;  // Controlled_Buffer controlled_buffer_4
  assign controlled_buffer_1_out[4] = and_1_out ? and_1_out : 1'bz;  // Controlled_Buffer controlled_buffer_5
  assign controlled_buffer_1_out[0] = not_1_out ? flag_output[0] : 1'bz;  // Controlled_Buffer controlled_buffer_6
  assign controlled_buffer_1_out[1] = not_1_out ? flag_output[1] : 1'bz;  // Controlled_Buffer controlled_buffer_7
  assign controlled_buffer_1_out[2] = not_1_out ? flag_output[2] : 1'bz;  // Controlled_Buffer controlled_buffer_8
  and and_1 (and_1_out, d_ff_2_q, not_2_out);
  not not_3 (not_3_out, and_1_out);
  not not_4 (not_4_out, and_1_out);
  assign controlled_buffer_1_out[3] = not_4_out ? flag_output[3] : 1'bz;  // Controlled_Buffer controlled_buffer_9
  assign controlled_buffer_1_out[4] = not_3_out ? flag_output[4] : 1'bz;  // Controlled_Buffer controlled_buffer_10
  or or_1 (or_1_out, write_reg_select[16], Input_st);
  Multiplexer multiplexer_2 (.in0(write_reg_select[17]), .in1(Input_st), .out(multiplexer_2_out), .sel(flag_output[5]));
  Multiplexer #(.width(16)) multiplexer_3 (
    .in0(reg_data_in), .in1(INTNUM_input), .out(multiplexer_3_out), .sel(and_1_out));
  and and_2 (and_2_out, write_reg_select[13], not_5_out);
  Register #(.width(16)) MEMVAL (.D(reg_data_in), .en(write_reg_select[10]), .clk(CLK), .Q(memval_out), .clr(RESET));
  Register #(.width(16)) MEMADDR (.D(reg_data_in), .en(write_reg_select[9]), .clk(CLK), .Q(memaddr_out), .clr(RESET));
  Register #(.width(16)) A (.D(reg_data_in), .en(write_reg_select[0]), .clk(CLK), .Q(a_out), .clr(RESET));
  Register #(.width(16)) B (.D(reg_data_in), .en(write_reg_select[1]), .clk(CLK), .Q(b_out), .clr(RESET));
  Register #(.width(16)) C (.D(reg_data_in), .en(write_reg_select[2]), .clk(CLK), .Q(c_out), .clr(RESET));
  Register #(.width(16)) D (.D(reg_data_in), .en(write_reg_select[3]), .clk(CLK), .Q(d_out), .clr(RESET));
  Register #(.width(16)) E (.D(reg_data_in), .en(write_reg_select[4]), .clk(CLK), .Q(e_out), .clr(RESET));
  Register #(.width(16)) BP (.D(reg_data_in), .en(write_reg_select[5]), .clk(CLK), .Q(bp_out), .clr(RESET));
  Register #(.width(16)) Output_port (
    .D(reg_data_in), .en(write_reg_select[8]), .clk(CLK), .Q(output_out), .clr(RESET));
  Register #(.width(16)) INTNUM (.D(multiplexer_3_out), .en(or_2_out), .clk(CLK), .Q(INTNUM_out), .clr(RESET));
  or or_2 (or_2_out, write_reg_select[12], and_1_out);
  Register #(.width(16)) inaddr (.D(reg_data_in), .en(and_2_out), .clk(CLK), .Q(inaddr_out), .clr(RESET));
  Register #(.width(16)) outaddr (.D(reg_data_in), .en(write_reg_select[14]), .clk(CLK), .Q(outaddr_out), .clr(RESET));
  Register #(.width(16)) Input_port (.D(Input_data), .en(Input_st), .clk(CLK), .Q(Input_out), .clr(RESET));
  RAM #(.addrWidth(16), .dataWidth(16), .enables("line")) buffer_reg (
    .addr(buffer_point_out), .we(or_1_out), .clk(CLK), .din(Input_data), .dout(buffer_out));
  Multiplexer #(.width(16)) multiplexer_4 (
    .in0(reg_data_in),
    .in1({flag_output[15:7], controlled_buffer_1_out[6], flag_output[5], controlled_buffer_1_out[4:0]}),
    .out(multiplexer_4_out), .sel(or_5_out));
  or or_3 (or_3_out, and_1_out, flag_write_sw);
  Register #(.width(16)) buffer_pointer (
    .D(multiplexer_5_out), .en(multiplexer_2_out), .clk(CLK), .Q(buffer_point_out), .clr(RESET));
  Multiplexer #(.width(16)) multiplexer_5 (
    .in0(reg_data_in), .in1(adder_1_out), .out(multiplexer_5_out), .sel(flag_output[5]));
  Register #(.width(16)) buffer_size (
    .D(reg_data_in), .en(write_reg_select[18]), .clk(CLK), .Q(buffer_size_out), .clr(RESET));
  Register #(.width(16)) FLAGS (
    .D(multiplexer_4_out), .en(or_4_out), .clk(CLK), .Q({flag_output[15:7], exec_mode, flag_output[5:0]}),
    .clr(RESET));
  or or_4 (or_4_out, write_reg_select[11], d_ff_1_q, or_3_out);
  or or_5 (or_5_out, or_3_out, d_ff_1_q);
  Adder #(.width(16)) adder_1 (.a(buffer_point_out), .b(16'h1), .out(adder_1_out));  // open: cin, cout
  Comparator #(.mode("unsigned"), .width(16)) comparator_1 (
    .a(buffer_point_out), .b(buffer_size_out), .gt(comparator_1_gt), .eq(comparator_1_eq));  // open: lt
  sixteen_register_sp sixteen_register_sp_1 (
    .RESET(RESET), .CLK(CLK), .D(reg_data_in), .WE(write_reg_select[6]), .Q(sp_out));
  not not_5 (not_5_out, flag_output[5]);
  or or_6 (or_6_out, comparator_1_eq, comparator_1_gt);
  and and_3 (buffer_full_int, or_6_out, flag_output[5]);

  assign flag_output[6] = exec_mode;
  assign out_st = write_reg_select[8];
endmodule

module ALU (
  input  [15:0] in1_data_in,
  input  [15:0] in2_data_in,
  input  [2:0] ALU_function_select,
  output [15:0] ALU_Out,
  output sign_flag,
  output zero_flag,
  output carry_flag
);

  wire adder_1_cout, not_2_out, not_3_out, not_4_out, not_5_out, not_6_out, not_7_out, not_8_out, not_9_out,
       not_10_out, not_11_out, not_12_out, not_13_out, not_14_out, not_15_out, not_16_out, not_17_out,
       right_shifter_1_carry_out;
  wire [15:0] adder_1_out, and_1_out, demultiplexer_1_out0, demultiplexer_1_out1, demultiplexer_1_out2,
       demultiplexer_1_out3, demultiplexer_1_out4, demultiplexer_1_out5, demultiplexer_1_out6,
       demultiplexer_1_out7, demultiplexer_2_out0, demultiplexer_2_out1, demultiplexer_2_out2,
       demultiplexer_2_out3, demultiplexer_2_out4, demultiplexer_2_out6, demultiplexer_2_out7,
       multiplier_1_cout, multiplier_1_out, not_1_out, or_1_out, right_shifter_1_output_bus_1,
       subtractor_1_out, xor_1_out;

  Demultiplexer #(.select(3), .width(16)) demultiplexer_1 (
    .out0(demultiplexer_1_out0), .out1(demultiplexer_1_out1), .out2(demultiplexer_1_out2),
    .out3(demultiplexer_1_out3), .out4(demultiplexer_1_out4), .out5(demultiplexer_1_out5),
    .out6(demultiplexer_1_out6), .out7(demultiplexer_1_out7), .in(in1_data_in), .sel(ALU_function_select));
  Demultiplexer #(.select(3), .width(16)) demultiplexer_2 (
    .out0(demultiplexer_2_out0), .out1(demultiplexer_2_out1), .out2(demultiplexer_2_out2),
    .out3(demultiplexer_2_out3), .out4(demultiplexer_2_out4), .out6(demultiplexer_2_out6),
    .out7(demultiplexer_2_out7), .in(in2_data_in), .sel(ALU_function_select));  // open: out5
  Adder #(.width(16)) adder_1 (
    .a(demultiplexer_1_out0), .b(demultiplexer_2_out0), .out(adder_1_out), .cin(1'b0), .cout(adder_1_cout));
  Subtractor #(.width(16)) subtractor_1 (
    .a(demultiplexer_1_out1), .b(demultiplexer_2_out1), .out(subtractor_1_out), .bin(1'b0), .bout(sign_flag));
  Multiplier #(.width(16)) multiplier_1 (
    .a(demultiplexer_1_out2), .b(demultiplexer_2_out2), .out(multiplier_1_out), .cin({16{1'b0}}),
    .cout(multiplier_1_cout));
  assign and_1_out = demultiplexer_1_out3 & demultiplexer_2_out3;  // AND_Gate and_1, 16 bits wide
  assign or_1_out = demultiplexer_1_out4 | demultiplexer_2_out4;  // OR_Gate or_1, 16 bits wide
  assign not_1_out = ~demultiplexer_1_out5;  // NOT_Gate not_1, 16 bits wide
  assign xor_1_out = demultiplexer_1_out6 ^ demultiplexer_2_out6;  // XOR_Gate xor_1, 16 bits wide
  right_shifter right_shifter_1 (
    .Input_bus_1(demultiplexer_2_out7), .Input_bus_2(demultiplexer_1_out7),
    .carry_out(right_shifter_1_carry_out), .Output_bus_1(right_shifter_1_output_bus_1));
  Multiplexer #(.select(3), .width(16)) multiplexer_1 (
    .in0(adder_1_out), .in1(subtractor_1_out), .in2(multiplier_1_out), .in3(and_1_out), .in4(or_1_out),
    .in5(not_1_out), .in6(xor_1_out), .in7(right_shifter_1_output_bus_1), .out(ALU_Out),
    .sel(ALU_function_select));
  or or_2 (carry_flag, adder_1_cout, multiplier_1_cout[7], multiplier_1_cout[0], multiplier_1_cout[1], multiplier_1_cout[2], multiplier_1_cout[3], multiplier_1_cout[4], multiplier_1_cout[5], multiplier_1_cout[6], multiplier_1_cout[8], multiplier_1_cout[9], multiplier_1_cout[10], multiplier_1_cout[11], multiplier_1_cout[12], multiplier_1_cout[13], multiplier_1_cout[14], multiplier_1_cout[15], right_shifter_1_carry_out);
  not not_2 (not_2_out, ALU_Out[0]);
  not not_3 (not_3_out, ALU_Out[1]);
  not not_4 (not_4_out, ALU_Out[2]);
  not not_5 (not_5_out, ALU_Out[3]);
  not not_6 (not_6_out, ALU_Out[4]);
  not not_7 (not_7_out, ALU_Out[5]);
  not not_8 (not_8_out, ALU_Out[6]);
  not not_9 (not_9_out, ALU_Out[7]);
  not not_10 (not_10_out, ALU_Out[8]);
  not not_11 (not_11_out, ALU_Out[9]);
  not not_12 (not_12_out, ALU_Out[10]);
  not not_13 (not_13_out, ALU_Out[11]);
  not not_14 (not_14_out, ALU_Out[12]);
  not not_15 (not_15_out, ALU_Out[13]);
  not not_16 (not_16_out, ALU_Out[14]);
  not not_17 (not_17_out, ALU_Out[15]);
  and and_2 (zero_flag, not_9_out, not_2_out, not_3_out, not_4_out, not_5_out, not_6_out, not_7_out, not_8_out, not_10_out, not_11_out, not_12_out, not_13_out, not_14_out, not_15_out, not_16_out, not_17_out);
endmodule

module sixteen_register (
  input  OS_RESTART,
  input  CLK,
  input  RESET,
  input  [15:0] D,
  input  WE,
  output [15:0] Q
);

  wire or_1_out, or_2_out, or_3_out, or_4_out, or_5_out, or_6_out, or_7_out, or_8_out, or_9_out, or_10_out,
       or_11_out, or_12_out, or_13_out, or_14_out;
  wire [15:0] multiplexer_1_out;

  Multiplexer #(.width(16)) multiplexer_1 (.in0(Q), .in1(D), .out(multiplexer_1_out), .sel(WE));
  D_Flip_Flop d_ff_1 (.D(multiplexer_1_out[0]), .clk(CLK), .Q(Q[0]), .reset(or_1_out));  // open: Qn, preset
  or or_1 (or_1_out, RESET, OS_RESTART);
  D_Flip_Flop d_ff_2 (.D(multiplexer_1_out[1]), .clk(CLK), .Q(Q[1]), .reset(or_2_out));  // open: Qn, preset
  or or_2 (or_2_out, RESET, OS_RESTART);
  D_Flip_Flop d_ff_3 (.D(multiplexer_1_out[2]), .clk(CLK), .Q(Q[2]), .reset(or_3_out));  // open: Qn, preset
  or or_3 (or_3_out, RESET, OS_RESTART);
  D_Flip_Flop d_ff_4 (.D(multiplexer_1_out[3]), .clk(CLK), .Q(Q[3]), .reset(or_4_out));  // open: Qn, preset
  or or_4 (or_4_out, RESET, OS_RESTART);
  D_Flip_Flop d_ff_5 (.D(multiplexer_1_out[4]), .clk(CLK), .Q(Q[4]), .reset(or_5_out));  // open: Qn, preset
  or or_5 (or_5_out, RESET, OS_RESTART);
  D_Flip_Flop d_ff_6 (.D(multiplexer_1_out[5]), .clk(CLK), .Q(Q[5]), .reset(or_6_out));  // open: Qn, preset
  or or_6 (or_6_out, RESET, OS_RESTART);
  D_Flip_Flop d_ff_7 (.D(multiplexer_1_out[6]), .clk(CLK), .Q(Q[6]), .reset(or_7_out));  // open: Qn, preset
  or or_7 (or_7_out, RESET, OS_RESTART);
  D_Flip_Flop d_ff_8 (.D(multiplexer_1_out[7]), .clk(CLK), .Q(Q[7]), .reset(or_8_out));  // open: Qn, preset
  or or_8 (or_8_out, RESET, OS_RESTART);
  D_Flip_Flop d_ff_9 (.D(multiplexer_1_out[8]), .clk(CLK), .Q(Q[8]), .preset(OS_RESTART), .reset(RESET));  // open: Qn
  D_Flip_Flop d_ff_10 (.D(multiplexer_1_out[9]), .clk(CLK), .Q(Q[9]), .reset(or_9_out));  // open: Qn, preset
  or or_9 (or_9_out, RESET, OS_RESTART);
  D_Flip_Flop d_ff_11 (
    .D(multiplexer_1_out[10]), .clk(CLK), .Q(Q[10]), .preset(OS_RESTART), .reset(RESET));  // open: Qn
  D_Flip_Flop d_ff_12 (.D(multiplexer_1_out[11]), .clk(CLK), .Q(Q[11]), .reset(or_10_out));  // open: Qn, preset
  or or_10 (or_10_out, RESET, OS_RESTART);
  D_Flip_Flop d_ff_13 (.D(multiplexer_1_out[12]), .clk(CLK), .Q(Q[12]), .reset(or_11_out));  // open: Qn, preset
  or or_11 (or_11_out, RESET, OS_RESTART);
  D_Flip_Flop d_ff_14 (.D(multiplexer_1_out[13]), .clk(CLK), .Q(Q[13]), .reset(or_12_out));  // open: Qn, preset
  or or_12 (or_12_out, RESET, OS_RESTART);
  D_Flip_Flop d_ff_15 (.D(multiplexer_1_out[14]), .clk(CLK), .Q(Q[14]), .reset(or_13_out));  // open: Qn, preset
  or or_13 (or_13_out, RESET, OS_RESTART);
  D_Flip_Flop d_ff_16 (.D(multiplexer_1_out[15]), .clk(CLK), .Q(Q[15]), .reset(or_14_out));  // open: Qn, preset
  or or_14 (or_14_out, RESET, OS_RESTART);
endmodule

module out_switcher (
  input  [15:0] data_in,
  input  strobe_in,
  input  [15:0] addr_in,
  output [15:0] data_out_0,
  output [15:0] out_5,
  output [15:0] out_6,
  output [15:0] out_7,
  output [15:0] out_8,
  output [15:0] out_9,
  output [15:0] out_10,
  output [15:0] out_11,
  output [15:0] out_12,
  output [15:0] out_13,
  output [15:0] out_14,
  output [15:0] out_15,
  output [15:0] out_16,
  output [15:0] out_17,
  output [15:0] out_18,
  output [15:0] out_19,
  output [15:0] out_20,
  output [15:0] out_21,
  output [15:0] out_22,
  output [15:0] out_23,
  output [15:0] out_24,
  output [15:0] out_25,
  output [15:0] out_26,
  output [15:0] out_27,
  output [15:0] out_28,
  output [15:0] out_29,
  output [15:0] out_30,
  output [15:0] out_31,
  output [15:0] out_32,
  output [15:0] out_33,
  output [15:0] out_34,
  output [15:0] data_out_31,
  output strobe_out_0,
  output out_37,
  output out_38,
  output out_39,
  output out_40,
  output out_41,
  output out_42,
  output out_43,
  output out_44,
  output out_45,
  output out_46,
  output out_47,
  output out_48,
  output out_49,
  output out_50,
  output out_51,
  output out_52,
  output out_53,
  output out_54,
  output out_55,
  output out_56,
  output out_57,
  output out_58,
  output out_59,
  output out_60,
  output out_61,
  output out_62,
  output out_63,
  output out_64,
  output out_65,
  output out_66,
  output strobe_out_31
);

  Demultiplexer #(.select(5), .width(16)) demultiplexer_1 (
    .out0(data_out_0), .out1(out_5), .out2(out_6), .out3(out_7), .out4(out_8), .out5(out_9), .out6(out_10),
    .out7(out_11), .out8(out_12), .out9(out_13), .out10(out_14), .out11(out_15), .out12(out_16),
    .out13(out_17), .out14(out_18), .out15(out_19), .out16(out_20), .out17(out_21), .out18(out_22),
    .out19(out_23), .out20(out_24), .out21(out_25), .out22(out_26), .out23(out_27), .out24(out_28),
    .out25(out_29), .out26(out_30), .out27(out_31), .out28(out_32), .out29(out_33), .out30(out_34),
    .out31(data_out_31), .in(data_in), .sel(addr_in[4:0]));
  Demultiplexer #(.select(5)) demultiplexer_2 (
    .out0(strobe_out_0), .out1(out_37), .out2(out_38), .out3(out_39), .out4(out_40), .out5(out_41),
    .out6(out_42), .out7(out_43), .out8(out_44), .out9(out_45), .out10(out_46), .out11(out_47),
    .out12(out_48), .out13(out_49), .out14(out_50), .out15(out_51), .out16(out_52), .out17(out_53),
    .out18(out_54), .out19(out_55), .out20(out_56), .out21(out_57), .out22(out_58), .out23(out_59),
    .out24(out_60), .out25(out_61), .out26(out_62), .out27(out_63), .out28(out_64), .out29(out_65),
    .out30(out_66), .out31(strobe_out_31), .in(strobe_in), .sel(addr_in[4:0]));
endmodule

module int_controller (
  input  int_0,
  input  in_2,
  input  in_3,
  input  in_4,
  input  in_5,
  input  in_6,
  input  in_7,
  input  in_8,
  input  in_9,
  input  in_10,
  input  in_11,
  input  in_12,
  input  in_13,
  input  in_14,
  input  in_15,
  input  in_16,
  input  in_17,
  input  in_18,
  input  in_19,
  input  in_20,
  input  in_21,
  input  in_22,
  input  in_23,
  input  in_24,
  input  in_25,
  input  in_26,
  input  in_27,
  input  in_28,
  input  in_29,
  input  in_30,
  input  in_31,
  input  int_31,
  input  CLOCK,
  input  RESET,
  output [4:0] out_intnum,
  output INT
);

  wire priority_encoder_1_en_out;
  wire [4:0] multiplexer_1_out, priority_encoder_1_out;

  Priority_Encoder #(.select(5)) priority_encoder_1 (
    .in0(int_0), .in1(in_2), .in2(in_3), .in3(in_4), .in4(in_5), .in5(in_6), .in6(in_7), .in7(in_8),
    .in8(in_9), .in9(in_10), .in10(in_11), .in11(in_12), .in12(in_13), .in13(in_14), .in14(in_15),
    .in15(in_16), .in16(in_17), .in17(in_18), .in18(in_19), .in19(in_20), .in20(in_21), .in21(in_22),
    .in22(in_23), .in23(in_24), .in24(in_25), .in25(in_26), .in26(in_27), .in27(in_28), .in28(in_29),
    .in29(in_30), .in30(in_31), .in31(int_31), .out(priority_encoder_1_out),
    .en_out(priority_encoder_1_en_out), .en_in(1'b1));  // open: gs
  or or_1 (INT, int_0, in_2, in_3, in_4, in_5, in_6, in_7, in_8, in_9, in_10, in_11, in_12, in_13, in_14, in_15, in_16, in_17, in_18, in_19, in_20, in_21, in_22, in_23, in_24, in_25, in_26, in_27, in_28, in_29, in_30, in_31, int_31);
  Multiplexer #(.width(5)) multiplexer_1 (
    .in0(priority_encoder_1_out), .in1({5{1'b0}}), .out(multiplexer_1_out), .sel(priority_encoder_1_en_out));
  Register #(.width(5)) register_1 (.D(multiplexer_1_out), .en(INT), .clk(CLOCK), .Q(out_intnum), .clr(RESET));
endmodule

module in_switcher (
  input  [15:0] in_0,
  input  [15:0] in_2,
  input  [15:0] in_3,
  input  [15:0] in_4,
  input  [15:0] in_5,
  input  [15:0] in_6,
  input  [15:0] in_7,
  input  [15:0] in_8,
  input  [15:0] in_9,
  input  [15:0] in_10,
  input  [15:0] in_11,
  input  [15:0] in_12,
  input  [15:0] in_13,
  input  [15:0] in_14,
  input  [15:0] in_15,
  input  [15:0] in_16,
  input  [15:0] in_17,
  input  [15:0] in_18,
  input  [15:0] in_19,
  input  [15:0] in_20,
  input  [15:0] in_21,
  input  [15:0] in_22,
  input  [15:0] in_23,
  input  [15:0] in_24,
  input  [15:0] in_25,
  input  [15:0] in_26,
  input  [15:0] in_27,
  input  [15:0] in_28,
  input  [15:0] in_29,
  input  [15:0] in_30,
  input  [15:0] in_31,
  input  [15:0] in_31_2,
  input  in_strobe_0,
  input  in_34,
  input  in_35,
  input  in_36,
  input  in_37,
  input  in_38,
  input  in_39,
  input  in_40,
  input  in_41,
  input  in_42,
  input  in_43,
  input  in_44,
  input  in_45,
  input  in_46,
  input  in_47,
  input  in_48,
  input  in_49,
  input  in_50,
  input  in_51,
  input  in_52,
  input  in_53,
  input  in_54,
  input  in_55,
  input  in_56,
  input  in_57,
  input  in_58,
  input  in_59,
  input  in_60,
  input  in_61,
  input  in_62,
  input  in_63,
  input  in_strobe_31,
  input  [15:0] addr_in,
  output [15:0] data_out,
  output strobe_out
);

  Multiplexer #(.select(5), .width(16)) multiplexer_1 (
    .in0(in_0), .in1(in_2), .in2(in_3), .in3(in_4), .in4(in_5), .in5(in_6), .in6(in_7), .in7(in_8),
    .in8(in_9), .in9(in_10), .in10(in_11), .in11(in_12), .in12(in_13), .in13(in_14), .in14(in_15),
    .in15(in_16), .in16(in_17), .in17(in_18), .in18(in_19), .in19(in_20), .in20(in_21), .in21(in_22),
    .in22(in_23), .in23(in_24), .in24(in_25), .in25(in_26), .in26(in_27), .in27(in_28), .in28(in_29),
    .in29(in_30), .in30(in_31), .in31(in_31_2), .out(data_out), .sel(addr_in[4:0]));
  Multiplexer #(.select(5)) multiplexer_2 (
    .in0(in_strobe_0), .in1(in_34), .in2(in_35), .in3(in_36), .in4(in_37), .in5(in_38), .in6(in_39),
    .in7(in_40), .in8(in_41), .in9(in_42), .in10(in_43), .in11(in_44), .in12(in_45), .in13(in_46),
    .in14(in_47), .in15(in_48), .in16(in_49), .in17(in_50), .in18(in_51), .in19(in_52), .in20(in_53),
    .in21(in_54), .in22(in_55), .in23(in_56), .in24(in_57), .in25(in_58), .in26(in_59), .in27(in_60),
    .in28(in_61), .in29(in_62), .in30(in_63), .in31(in_strobe_31), .out(strobe_out), .sel(addr_in[4:0]));
endmodule

module rom_controller (
  input  [15:0] data_in,
  input  input_strobe,
  input  RESET,
  input  CLK,
  output [15:0] output_memaddr,
  output write_probe
);

  wire comparator_1_eq, comparator_1_gt, or_1_out;
  wire [4:0] State_To_Output_Decoder_out;
  wire [7:0] Next_State_Decoder_out;
  wire [9:0] State_Register_q;
  wire [15:0] adder_1_out, base_addr_q, data_size_q, register_1_q, subtractor_1_out;

  or or_1 (or_1_out, RESET, State_To_Output_Decoder_out[4]);
  Register #(.width(16)) base_addr (
    .D(data_in), .en(State_To_Output_Decoder_out[0]), .clk(CLK), .Q(base_addr_q), .clr(or_1_out));
  PLA #(.in_width(10), .out_width(8), .\table ("x000000000 00000000 # base_addr_receive stay\nx100000000 00000001 # base_addr_receive -> data_size_receive\nx000000001 00000001 # data_size_receive stay\nx100000001 00000101 # data_size_receive -> data_send_initsend\nxx00000101 00000110 # data_send_initsend -> data_send_wait1\nxx00000110 00000010 # data_send_wait1 -> data_send_count\nxx00000010 00000100 # data_send_count -> data_send_send\n0x00000100 00000010 # data_send_send -> data_send_count\n1x00000100 00000011 # data_send_send -> rom_controller_reset\nxx00000011 00000000 # rom_controller_reset -> base_addr_receive")) Next_State_Decoder (
    .in({State_Register_q[9], input_strobe, State_Register_q[7:0]}), .out(Next_State_Decoder_out));
  Clock clock_1 ();  // open: out
  Register State_Register (.D(Next_State_Decoder_out), .en(1'b1), .clk(CLK), .Q(State_Register_q[7:0]), .clr(or_1_out));
  Register #(.width(16)) data_size (
    .D(subtractor_1_out), .en(State_To_Output_Decoder_out[1]), .clk(CLK), .Q(data_size_q), .clr(or_1_out));
  Subtractor #(.width(16)) subtractor_1 (.a(data_in), .b(16'h1), .out(subtractor_1_out));  // open: bin, bout
  PLA #(.in_width(8), .out_width(5), .\table ("00000000 00001 # base_addr_receive\n00000001 00010 # data_size_receive\n00000010 00100 # data_send_count\n00000011 10000 # rom_controller_reset\n00000100 01000 # data_send_send\n00000101 01000 # data_send_initsend\n00000110 00000 # data_send_wait1")) State_To_Output_Decoder (
    .in(State_Register_q[7:0]),
    .out({State_To_Output_Decoder_out[4], write_probe, State_To_Output_Decoder_out[2:0]}));
  Register #(.width(16)) register_1 (
    .D(adder_1_out), .en(State_To_Output_Decoder_out[2]), .clk(CLK), .Q(register_1_q), .clr(or_1_out));
  Adder #(.width(16)) adder_1 (.a(register_1_q), .b(16'h1), .out(adder_1_out));  // open: cin, cout
  Comparator #(.mode("unsigned"), .width(16)) comparator_1 (
    .a(register_1_q), .b(data_size_q), .gt(comparator_1_gt), .eq(comparator_1_eq));  // open: lt
  Adder #(.width(16)) adder_2 (.a(base_addr_q), .b(register_1_q), .out(output_memaddr));  // open: cin, cout
  or or_2 (State_Register_q[9], comparator_1_gt, comparator_1_eq);
endmodule

module startup_sound_generator (
  input  CLK,
  input  RESET,
  output out_a
);

  wire comparator_1_eq, comparator_1_gt, comparator_1_lt, d_ff_1_q, not_1_out;
  wire [15:0] adder_1_out, register_1_q;

  not not_1 (not_1_out, d_ff_1_q);
  Register #(.width(16)) register_1 (.D(adder_1_out), .en(not_1_out), .clk(CLK), .Q(register_1_q), .clr(RESET));
  Adder #(.width(16)) adder_1 (.a(register_1_q), .b(16'h1), .out(adder_1_out));  // open: cin, cout
  Comparator #(.width(16)) comparator_1 (
    .a(register_1_q), .b(16'hbb8), .gt(comparator_1_gt), .eq(comparator_1_eq), .lt(comparator_1_lt));
  or or_1 (out_a, comparator_1_eq, comparator_1_lt);
  D_Flip_Flop d_ff_1 (.D(comparator_1_gt), .clk(CLK), .Q(d_ff_1_q), .reset(RESET));  // open: Qn, preset
endmodule

module sixteen_register_sp (
  input  RESET,
  input  CLK,
  input  [15:0] D,
  input  WE,
  output [15:0] Q
);

  wire [15:0] multiplexer_1_out;

  Multiplexer #(.width(16)) multiplexer_1 (.in0(Q), .in1(D), .out(multiplexer_1_out), .sel(WE));
  D_Flip_Flop d_ff_1 (.D(multiplexer_1_out[0]), .clk(CLK), .Q(Q[0]), .preset(RESET));  // open: Qn, reset
  D_Flip_Flop d_ff_2 (.D(multiplexer_1_out[1]), .clk(CLK), .Q(Q[1]), .preset(RESET));  // open: Qn, reset
  D_Flip_Flop d_ff_3 (.D(multiplexer_1_out[2]), .clk(CLK), .Q(Q[2]), .preset(RESET));  // open: Qn, reset
  D_Flip_Flop d_ff_4 (.D(multiplexer_1_out[3]), .clk(CLK), .Q(Q[3]), .preset(RESET));  // open: Qn, reset
  D_Flip_Flop d_ff_5 (.D(multiplexer_1_out[4]), .clk(CLK), .Q(Q[4]), .preset(RESET));  // open: Qn, reset
  D_Flip_Flop d_ff_6 (.D(multiplexer_1_out[5]), .clk(CLK), .Q(Q[5]), .preset(RESET));  // open: Qn, reset
  D_Flip_Flop d_ff_7 (.D(multiplexer_1_out[6]), .clk(CLK), .Q(Q[6]), .preset(RESET));  // open: Qn, reset
  D_Flip_Flop d_ff_8 (.D(multiplexer_1_out[7]), .clk(CLK), .Q(Q[7]), .preset(RESET));  // open: Qn, reset
  D_Flip_Flop d_ff_9 (.D(multiplexer_1_out[8]), .clk(CLK), .Q(Q[8]), .preset(RESET));  // open: Qn, reset
  D_Flip_Flop d_ff_10 (.D(multiplexer_1_out[9]), .clk(CLK), .Q(Q[9]), .preset(RESET));  // open: Qn, reset
  D_Flip_Flop d_ff_11 (.D(multiplexer_1_out[10]), .clk(CLK), .Q(Q[10]), .preset(RESET));  // open: Qn, reset
  D_Flip_Flop d_ff_12 (.D(multiplexer_1_out[11]), .clk(CLK), .Q(Q[11]), .preset(RESET));  // open: Qn, reset
  D_Flip_Flop d_ff_13 (.D(multiplexer_1_out[12]), .clk(CLK), .Q(Q[12]), .preset(RESET));  // open: Qn, reset
  D_Flip_Flop d_ff_14 (.D(multiplexer_1_out[13]), .clk(CLK), .Q(Q[13]), .preset(RESET));  // open: Qn, reset
  D_Flip_Flop d_ff_15 (.D(multiplexer_1_out[14]), .clk(CLK), .Q(Q[14]), .preset(RESET));  // open: Qn, reset
  D_Flip_Flop d_ff_16 (.D(multiplexer_1_out[15]), .clk(CLK), .Q(Q[15]), .preset(RESET));  // open: Qn, reset
endmodule
